// Logisim project 64.circ as structural Verilog
module main (
  input  Pa0,
  input  D,
  input  A
);

  wire and_1_out, and_2_out, and_3_out, and_4_out, and_5_out, and_6_out, and_7_out, button_1_out,
       button_2_out, button_3_out, clock_1_out, gallina_1__2_2, gallina_1__3_2, gallina_1_total,
       n7_segmentos_1_a, n7_segmentos_1_b, n7_segmentos_1_c, n7_segmentos_1_d, n7_segmentos_1_e,
       n7_segmentos_1_f, n7_segmentos_1_g, n7_segmentos_decena_1_a, n7_segmentos_decena_1_b,
       n7_segmentos_decena_1_c, n7_segmentos_decena_1_d, n7_segmentos_decena_1_e, n7_segmentos_decena_1_f,
       n7_segmentos_decena_1_g, or_1_out, or_2_out, or_3_out, reg_des_1_out_3, reg_des_2_out_3,
       reg_des_3_out_3, reg_des_4_out_3, t_ff_1_q, t_ff_2_q, t_ff_2_qn, t_ff_3_q, t_ff_3_qn, t_ff_4_q,
       t_ff_4_qn;

  Button button_1 (.out(button_1_out));
  Button button_2 (.out(button_2_out));
  Button button_3 (.out(button_3_out));
  Clock clock_1 (.out(clock_1_out));
  gallina gallina_1 (
    ._1(button_1_out), ._2(button_2_out), ._3(button_3_out), .Ck(clock_1_out), ._2_2(gallina_1__2_2),
    ._3_2(gallina_1__3_2), .total(gallina_1_total));
  reg_des reg_des_1 (.in_1(and_1_out), .Ck(clock_1_out), .out_3(reg_des_1_out_3));
  and and_1 (and_1_out, ~gallina_1__2_2, ~gallina_1__3_2, gallina_1_total);  // AND_Gate
  reg_des reg_des_2 (.in_1(gallina_1__2_2), .Ck(clock_1_out), .out_3(reg_des_2_out_3));
  reg_des reg_des_3 (.in_1(gallina_1__3_2), .Ck(clock_1_out), .out_3(reg_des_3_out_3));
  reg_des reg_des_4 (.in_1(gallina_1_total), .Ck(clock_1_out), .out_3(reg_des_4_out_3));
  and and_2 (and_2_out, t_ff_2_q, t_ff_3_q, t_ff_4_q, A);
  or or_1 (or_1_out, and_2_out, and_3_out);
  and and_3 (and_3_out, D, t_ff_3_qn, t_ff_4_qn, t_ff_2_qn);
  LED led_1 (.in(reg_des_1_out_3));
  LED led_2 (.in(reg_des_2_out_3));
  LED led_3 (.in(reg_des_3_out_3));
  LED led_4 (.in(reg_des_4_out_3));
  T_Flip_Flop t_ff_1 (.clk(reg_des_3_out_3), .T(or_1_out), .Q(t_ff_1_q), .reset(Pa0));  // open: Qn, preset, en
  and and_4 (and_4_out, t_ff_4_q, t_ff_3_q, A);
  and and_5 (and_5_out, D, t_ff_3_qn, t_ff_4_qn);
  or or_2 (or_2_out, and_4_out, and_5_out);
  T_Flip_Flop t_ff_2 (
    .clk(reg_des_3_out_3), .T(or_2_out), .Q(t_ff_2_q), .Qn(t_ff_2_qn), .reset(Pa0));  // open: preset, en
  and and_6 (and_6_out, t_ff_4_q, A);
  and and_7 (and_7_out, D, t_ff_4_qn);
  _7_Segmentos_decena u_7_segmentos_decena_1 (
    .b0(t_ff_1_q), .b1(t_ff_2_q), .b2(t_ff_3_q), .b3(t_ff_4_q), .a(n7_segmentos_decena_1_a),
    .b(n7_segmentos_decena_1_b), .c(n7_segmentos_decena_1_c), .d(n7_segmentos_decena_1_d),
    .e(n7_segmentos_decena_1_e), .f(n7_segmentos_decena_1_f), .g(n7_segmentos_decena_1_g));
  _7_Segment_Display u_7_segment_display_1 (
    .g(n7_segmentos_1_a), .f(n7_segmentos_1_b), .a(n7_segmentos_1_c), .b(n7_segmentos_1_d),
    .e(n7_segmentos_1_g), .d(n7_segmentos_1_f), .c(n7_segmentos_1_e));  // open: dp
  _7_Segment_Display u_7_segment_display_2 (
    .g(n7_segmentos_decena_1_a), .f(n7_segmentos_decena_1_b), .a(n7_segmentos_decena_1_c),
    .b(n7_segmentos_decena_1_d), .e(n7_segmentos_decena_1_g), .d(n7_segmentos_decena_1_f),
    .c(n7_segmentos_decena_1_e));  // open: dp
  T_Flip_Flop t_ff_3 (
    .clk(reg_des_3_out_3), .T(or_3_out), .Q(t_ff_3_q), .Qn(t_ff_3_qn), .reset(Pa0));  // open: preset, en
  or or_3 (or_3_out, and_6_out, and_7_out);
  _7_Segmentos u_7_segmentos_1 (
    .b0(t_ff_1_q), .b1(t_ff_2_q), .b2(t_ff_3_q), .b3(t_ff_4_q), .a(n7_segmentos_1_a), .b(n7_segmentos_1_b),
    .c(n7_segmentos_1_c), .d(n7_segmentos_1_d), .e(n7_segmentos_1_e), .f(n7_segmentos_1_f),
    .g(n7_segmentos_1_g));
  T_Flip_Flop t_ff_4 (.clk(reg_des_3_out_3), .T(1'b1), .Q(t_ff_4_q), .Qn(t_ff_4_qn), .reset(Pa0));  // open: preset, en
endmodule

module reg_des (
  input  in_1,
  input  Ck,
  output out_3
);

  wire d_ff_1_q, d_ff_2_q, d_ff_3_q, d_ff_4_q, d_ff_5_q, d_ff_6_q, d_ff_7_q, d_ff_8_q, d_ff_9_q, d_ff_10_q,
       d_ff_11_q, d_ff_12_q, d_ff_13_q, d_ff_14_q, d_ff_15_q;

  D_Flip_Flop d_ff_1 (.clk(Ck), .D(in_1), .Q(d_ff_1_q));  // open: Qn, preset, en, reset
  D_Flip_Flop d_ff_2 (.clk(Ck), .D(d_ff_1_q), .Q(d_ff_2_q));  // open: Qn, preset, en, reset
  D_Flip_Flop d_ff_3 (.clk(Ck), .D(d_ff_2_q), .Q(d_ff_3_q));  // open: Qn, preset, en, reset
  D_Flip_Flop d_ff_4 (.clk(Ck), .D(d_ff_3_q), .Q(d_ff_4_q));  // open: Qn, preset, en, reset
  D_Flip_Flop d_ff_5 (.clk(Ck), .D(d_ff_4_q), .Q(d_ff_5_q));  // open: Qn, preset, en, reset
  D_Flip_Flop d_ff_6 (.clk(Ck), .D(d_ff_5_q), .Q(d_ff_6_q));  // open: Qn, preset, en, reset
  D_Flip_Flop d_ff_7 (.clk(Ck), .D(d_ff_6_q), .Q(d_ff_7_q));  // open: Qn, preset, en, reset
  D_Flip_Flop d_ff_8 (.clk(Ck), .D(d_ff_7_q), .Q(d_ff_8_q));  // open: Qn, preset, en, reset
  D_Flip_Flop d_ff_9 (.clk(Ck), .D(d_ff_8_q), .Q(d_ff_9_q));  // open: Qn, preset, en, reset
  D_Flip_Flop d_ff_10 (.clk(Ck), .D(d_ff_9_q), .Q(d_ff_10_q));  // open: Qn, preset, en, reset
  D_Flip_Flop d_ff_11 (.clk(Ck), .D(d_ff_10_q), .Q(d_ff_11_q));  // open: Qn, preset, en, reset
  D_Flip_Flop d_ff_12 (.clk(Ck), .D(d_ff_11_q), .Q(d_ff_12_q));  // open: Qn, preset, en, reset
  D_Flip_Flop d_ff_13 (.clk(Ck), .D(d_ff_12_q), .Q(d_ff_13_q));  // open: Qn, preset, en, reset
  D_Flip_Flop d_ff_14 (.clk(Ck), .D(d_ff_13_q), .Q(d_ff_14_q));  // open: Qn, preset, en, reset
  D_Flip_Flop d_ff_15 (.clk(Ck), .D(d_ff_14_q), .Q(d_ff_15_q));  // open: Qn, preset, en, reset
  D_Flip_Flop d_ff_16 (.clk(Ck), .D(d_ff_15_q), .Q(out_3));  // open: Qn, preset, en, reset
endmodule

module gallina (
  input  _1,
  input  _2,
  input  _3,
  input  Ck,
  output _2_2,
  output _3_2,
  output total
);

  wire and_1_out, and_2_out, and_3_out, s_r_ff_1_q, s_r_ff_2_q, s_r_ff_3_q;

  S_R_Flip_Flop s_r_ff_1 (.S(and_1_out), .clk(Ck), .R(s_r_ff_1_q), .Q(s_r_ff_1_q));  // open: Qn, preset, reset, en
  and and_1 (and_1_out, _1, ~_2, ~_3);  // AND_Gate
  and and_2 (and_2_out, ~_1, _2, ~_3);  // AND_Gate
  S_R_Flip_Flop s_r_ff_2 (.S(and_2_out), .clk(Ck), .R(s_r_ff_2_q), .Q(s_r_ff_2_q));  // open: Qn, preset, reset, en
  and and_3 (and_3_out, ~_1, ~_2, _3);  // AND_Gate
  S_R_Flip_Flop s_r_ff_3 (.S(and_3_out), .clk(Ck), .R(s_r_ff_3_q), .Q(s_r_ff_3_q));  // open: Qn, preset, reset, en
  and and_4 (_2_2, ~s_r_ff_1_q, s_r_ff_2_q, ~s_r_ff_3_q);  // AND_Gate
  and and_5 (_3_2, ~s_r_ff_1_q, ~s_r_ff_2_q, s_r_ff_3_q);  // AND_Gate
  or or_1 (total, s_r_ff_1_q, s_r_ff_2_q, s_r_ff_3_q);
endmodule
