// Logisim project Ejercicio 30 - Contador asc-desc.circ as structural Verilog: 3 circuits, main circuit main
module main (
  input  Pa0,
  input  D,
  input  A
);

  wire and_1_out, and_2_out, and_3_out, and_4_out, and_5_out, and_6_out, Ck_out, n7_segmentos_1_a,
       n7_segmentos_1_b, n7_segmentos_1_c, n7_segmentos_1_d, n7_segmentos_1_e, n7_segmentos_1_f,
       n7_segmentos_1_g, n7_segmentos_decena_1_a, n7_segmentos_decena_1_b, n7_segmentos_decena_1_c,
       n7_segmentos_decena_1_d, n7_segmentos_decena_1_e, n7_segmentos_decena_1_f, n7_segmentos_decena_1_g,
       or_1_out, or_2_out, or_3_out, t_ff_1_q, t_ff_2_q, t_ff_2_qn, t_ff_3_q, t_ff_3_qn, t_ff_4_q, t_ff_4_qn;

  Clock Ck (.out(Ck_out));
  and and_1 (and_1_out, t_ff_2_q, t_ff_3_q, t_ff_4_q, A);
  and and_2 (and_2_out, D, t_ff_3_qn, t_ff_4_qn, t_ff_2_qn);
  T_Flip_Flop t_ff_1 (.clk(Ck_out), .T(or_1_out), .Q(t_ff_1_q), .reset(Pa0));  // open: Qn, preset, en
  or or_1 (or_1_out, and_1_out, and_2_out);
  and and_3 (and_3_out, t_ff_4_q, t_ff_3_q, A);
  or or_2 (or_2_out, and_3_out, and_4_out);
  and and_4 (and_4_out, D, t_ff_3_qn, t_ff_4_qn);
  T_Flip_Flop t_ff_2 (.clk(Ck_out), .T(or_2_out), .Q(t_ff_2_q), .Qn(t_ff_2_qn), .reset(Pa0));  // open: preset, en
  and and_5 (and_5_out, t_ff_4_q, A);
  and and_6 (and_6_out, D, t_ff_4_qn);
  _7_Segmentos_decena u_7_segmentos_decena_1 (
    .b0(t_ff_1_q), .b1(t_ff_2_q), .b2(t_ff_3_q), .b3(t_ff_4_q), .a(n7_segmentos_decena_1_a),
    .b(n7_segmentos_decena_1_b), .c(n7_segmentos_decena_1_c), .d(n7_segmentos_decena_1_d),
    .e(n7_segmentos_decena_1_e), .f(n7_segmentos_decena_1_f), .g(n7_segmentos_decena_1_g));
  _7_Segment_Display u_7_segment_display_1 (
    .g(n7_segmentos_decena_1_a), .f(n7_segmentos_decena_1_b), .a(n7_segmentos_decena_1_c),
    .b(n7_segmentos_decena_1_d), .e(n7_segmentos_decena_1_g), .d(n7_segmentos_decena_1_f),
    .c(n7_segmentos_decena_1_e));  // open: dp
  or or_3 (or_3_out, and_5_out, and_6_out);
  _7_Segmentos u_7_segmentos_1 (
    .b0(t_ff_1_q), .b1(t_ff_2_q), .b2(t_ff_3_q), .b3(t_ff_4_q), .a(n7_segmentos_1_a), .b(n7_segmentos_1_b),
    .c(n7_segmentos_1_c), .d(n7_segmentos_1_d), .e(n7_segmentos_1_e), .f(n7_segmentos_1_f),
    .g(n7_segmentos_1_g));
  _7_Segment_Display u_7_segment_display_2 (
    .g(n7_segmentos_1_a), .f(n7_segmentos_1_b), .a(n7_segmentos_1_c), .b(n7_segmentos_1_d),
    .e(n7_segmentos_1_g), .d(n7_segmentos_1_f), .c(n7_segmentos_1_e));  // open: dp
  T_Flip_Flop t_ff_3 (.clk(Ck_out), .T(or_3_out), .Q(t_ff_3_q), .Qn(t_ff_3_qn), .reset(Pa0));  // open: preset, en
  T_Flip_Flop t_ff_4 (.clk(Ck_out), .T(1'b1), .Q(t_ff_4_q), .Qn(t_ff_4_qn), .reset(Pa0));  // open: preset, en
endmodule

module _7_Segmentos (
  input  b0,
  input  b1,
  input  b2,
  input  b3,
  output a,
  output b,
  output c,
  output d,
  output e,
  output f,
  output g
);

  wire and_1_out, and_2_out, and_3_out, and_4_out, and_5_out, and_6_out, and_7_out, and_8_out, and_9_out,
       and_10_out, and_11_out, and_12_out, and_13_out, and_14_out, and_15_out, and_16_out, and_17_out,
       and_18_out, and_19_out, and_20_out, and_21_out, and_22_out, and_23_out, and_24_out, and_25_out,
       and_26_out, and_27_out, and_28_out, and_29_out, and_30_out, and_31_out, not_1_out, not_2_out,
       not_3_out, not_4_out, not_5_out, not_6_out, not_7_out, not_8_out, not_9_out, not_10_out, not_11_out,
       not_12_out, not_13_out, not_14_out, not_15_out, not_16_out, not_17_out, not_18_out, not_19_out,
       not_20_out, not_21_out, not_22_out, not_23_out, not_24_out, not_25_out, not_26_out, not_27_out,
       not_28_out, not_29_out, not_30_out, not_31_out, not_32_out, not_33_out, not_34_out, not_35_out,
       not_36_out, not_37_out, not_38_out, not_39_out, not_40_out, not_41_out, not_42_out, not_43_out;

  not not_1 (not_1_out, b0);
  not not_2 (not_2_out, b1);
  and and_1 (and_1_out, not_1_out, not_2_out, b2);
  and and_2 (and_2_out, b1, not_3_out);
  not not_3 (not_3_out, b2);
  and and_3 (and_3_out, b1, not_4_out);
  not not_4 (not_4_out, b3);
  and and_4 (and_4_out, b0, not_5_out);
  not not_5 (not_5_out, b2);
  and and_5 (and_5_out, b0, b1);
  not not_6 (not_6_out, b0);
  not not_7 (not_7_out, b2);
  and and_6 (and_6_out, not_6_out, not_7_out, not_8_out);
  not not_8 (not_8_out, b3);
  not not_9 (not_9_out, b0);
  and and_7 (and_7_out, not_9_out, b1, not_10_out);
  not not_10 (not_10_out, b2);
  not not_11 (not_11_out, b0);
  and and_8 (and_8_out, not_11_out, b1, not_12_out);
  not not_12 (not_12_out, b3);
  and and_9 (and_9_out, b0, not_13_out, not_14_out);
  not not_13 (not_13_out, b1);
  not not_14 (not_14_out, b2);
  not not_15 (not_15_out, b1);
  and and_10 (and_10_out, b0, not_15_out, not_16_out);
  not not_16 (not_16_out, b3);
  and and_11 (and_11_out, b0, b1, b2);
  not not_17 (not_17_out, b1);
  and and_12 (and_12_out, not_17_out, not_18_out);
  not not_18 (not_18_out, b3);
  not not_19 (not_19_out, b0);
  and and_13 (and_13_out, not_19_out, b2);
  and and_14 (and_14_out, b1, b3);
  and and_15 (and_15_out, b0, not_20_out);
  not not_20 (not_20_out, b2);
  not not_21 (not_21_out, b1);
  not not_22 (not_22_out, b2);
  and and_16 (and_16_out, not_22_out, not_23_out);
  not not_23 (not_23_out, b3);
  not not_24 (not_24_out, b0);
  and and_17 (and_17_out, not_24_out, b2, b3);
  and and_18 (and_18_out, b0, not_25_out);
  not not_25 (not_25_out, b2);
  and and_19 (and_19_out, b0, not_26_out);
  not not_26 (not_26_out, b3);
  not not_27 (not_27_out, b0);
  and and_20 (and_20_out, not_27_out, not_28_out);
  not not_28 (not_28_out, b2);
  and and_21 (and_21_out, b1, b2);
  and and_22 (and_22_out, b0, not_29_out);
  not not_29 (not_29_out, b1);
  not not_30 (not_30_out, b1);
  and and_23 (and_23_out, not_30_out, not_31_out);
  not not_31 (not_31_out, b3);
  not not_32 (not_32_out, b0);
  and and_24 (and_24_out, not_32_out, not_33_out, b2);
  not not_33 (not_33_out, b1);
  not not_34 (not_34_out, b0);
  and and_25 (and_25_out, not_34_out, b2, not_35_out);
  not not_35 (not_35_out, b3);
  not not_36 (not_36_out, b2);
  and and_26 (and_26_out, b1, not_36_out, b3);
  and and_27 (and_27_out, b0, not_37_out);
  not not_37 (not_37_out, b2);
  and and_28 (and_28_out, b0, b1, b3);
  not not_38 (not_38_out, b1);
  and and_29 (and_29_out, not_38_out, not_39_out);
  not not_39 (not_39_out, b3);
  not not_40 (not_40_out, b0);
  and and_30 (and_30_out, not_40_out, b2, not_41_out);
  not not_41 (not_41_out, b3);
  not not_42 (not_42_out, b2);
  and and_31 (and_31_out, b0, not_42_out, not_43_out);
  not not_43 (not_43_out, b3);
  or or_1 (a, and_1_out, and_2_out, and_3_out, and_4_out, and_5_out);
  or or_2 (c, and_12_out, and_13_out, and_14_out, and_15_out);
  or or_3 (d, not_21_out, and_16_out, and_17_out, and_18_out, and_19_out);
  or or_4 (e, and_20_out, b3, and_21_out, and_22_out);
  or or_5 (g, and_29_out, and_30_out, and_31_out);
  or or_6 (b, and_6_out, and_7_out, and_8_out, and_9_out, and_10_out, and_11_out);
  or or_7 (f, and_23_out, and_24_out, and_25_out, and_26_out, and_27_out, and_28_out);
endmodule

module _7_Segmentos_decena (
  input  b0,
  input  b1,
  input  b2,
  input  b3,
  output a,
  output b,
  output c,
  output d,
  output e,
  output f,
  output g
);

  wire and_1_out, and_2_out, and_3_out, and_4_out, not_1_out, not_2_out, not_3_out, not_4_out, not_5_out,
       not_6_out, not_7_out, not_8_out, not_9_out, not_10_out, not_11_out, not_12_out;

  not not_1 (not_1_out, b0);
  not not_2 (not_2_out, b1);
  and and_1 (and_1_out, not_2_out, not_3_out);
  not not_3 (not_3_out, b2);
  not not_4 (not_4_out, b0);
  not not_5 (not_5_out, b1);
  and and_2 (and_2_out, not_5_out, not_6_out);
  not not_6 (not_6_out, b2);
  not not_7 (not_7_out, b0);
  not not_8 (not_8_out, b1);
  and and_3 (and_3_out, not_8_out, not_9_out);
  not not_9 (not_9_out, b2);
  not not_10 (not_10_out, b0);
  not not_11 (not_11_out, b1);
  and and_4 (and_4_out, not_11_out, not_12_out);
  not not_12 (not_12_out, b2);
  or or_1 (b, not_1_out, and_1_out);
  or or_2 (c, not_4_out, and_2_out);
  or or_3 (f, not_7_out, and_3_out);
  or or_4 (g, not_10_out, and_4_out);

  assign a = 1'b0;
  assign d = 1'b1;
  assign e = 1'b1;
endmodule
