// Logisim project Ejercicio 31 - Contador Grey.circ as structural Verilog
module main (
  input  in_1
);

  wire contador_grey_1_b0, contador_grey_1_b1, contador_grey_1_b2, contador_grey_1_b3, n7_segmentos_1_a,
       n7_segmentos_1_b, n7_segmentos_1_c, n7_segmentos_1_d, n7_segmentos_1_e, n7_segmentos_1_f,
       n7_segmentos_1_g;

  Contador_grey contador_grey_1 (
    .P0(in_1), .b3(contador_grey_1_b3), .b2(contador_grey_1_b2), .b1(contador_grey_1_b1),
    .b0(contador_grey_1_b0));
  _7_segmentos u_7_segmentos_1 (
    .b0(contador_grey_1_b3), .b1(contador_grey_1_b2), .b2(contador_grey_1_b1), .b3(contador_grey_1_b0),
    .a(n7_segmentos_1_a), .b(n7_segmentos_1_b), .c(n7_segmentos_1_c), .d(n7_segmentos_1_d),
    .e(n7_segmentos_1_e), .f(n7_segmentos_1_f), .g(n7_segmentos_1_g));
  _7_Segment_Display u_7_segment_display_1 ();  // open: g, f, a, b, e, d, c, dp
  _7_Segment_Display u_7_segment_display_2 (
    .g(n7_segmentos_1_g), .f(n7_segmentos_1_f), .a(n7_segmentos_1_a), .b(n7_segmentos_1_b),
    .e(n7_segmentos_1_e), .d(n7_segmentos_1_d), .c(n7_segmentos_1_c));  // open: dp
endmodule

module _7_segmentos (
  input  b0,
  input  b1,
  input  b2,
  input  b3,
  output a,
  output b,
  output c,
  output d,
  output e,
  output f,
  output g
);

  wire and_1_out, and_2_out, and_3_out, and_4_out, and_5_out, and_6_out, and_7_out, and_8_out, and_9_out,
       and_10_out, and_11_out, and_12_out, and_13_out, and_14_out, and_15_out, and_16_out, and_17_out,
       and_18_out, and_19_out, and_20_out, and_21_out, and_22_out, and_23_out, and_24_out, and_25_out,
       and_26_out, and_27_out, not_1_out, not_2_out, not_3_out, not_4_out, not_5_out, not_6_out, not_7_out,
       not_8_out, not_9_out, not_10_out, not_11_out, not_12_out, not_13_out, not_14_out, not_15_out,
       not_16_out, not_17_out, not_18_out, not_19_out, not_20_out, not_21_out, not_22_out, not_23_out,
       not_24_out, not_25_out, not_26_out, not_27_out, not_28_out, not_29_out, not_30_out, not_31_out,
       not_32_out, not_33_out, not_34_out, not_35_out, not_36_out;

  not not_1 (not_1_out, b1);
  and and_1 (and_1_out, not_1_out, not_2_out);
  not not_2 (not_2_out, b3);
  and and_2 (and_2_out, b2, b3);
  and and_3 (and_3_out, b1, not_3_out);
  not not_3 (not_3_out, b2);
  not not_4 (not_4_out, b0);
  and and_4 (and_4_out, not_4_out, not_5_out);
  not not_5 (not_5_out, b1);
  not not_6 (not_6_out, b1);
  and and_5 (and_5_out, not_6_out, b2);
  and and_6 (and_6_out, b1, not_7_out);
  not not_7 (not_7_out, b3);
  and and_7 (and_7_out, b0, b3);
  not not_8 (not_8_out, b0);
  and and_8 (and_8_out, not_8_out, not_9_out);
  not not_9 (not_9_out, b3);
  not not_10 (not_10_out, b2);
  and and_9 (and_9_out, b0, b3);
  not not_11 (not_11_out, b1);
  and and_10 (and_10_out, not_11_out, not_12_out);
  not not_12 (not_12_out, b3);
  not not_13 (not_13_out, b1);
  and and_11 (and_11_out, not_13_out, b2);
  and and_12 (and_12_out, b1, b3);
  and and_13 (and_13_out, b0, not_14_out, not_15_out);
  not not_14 (not_14_out, b2);
  not not_15 (not_15_out, b3);
  not not_16 (not_16_out, b0);
  not not_17 (not_17_out, b1);
  not not_18 (not_18_out, b2);
  not not_19 (not_19_out, b3);
  not not_20 (not_20_out, b0);
  not not_21 (not_21_out, b1);
  not not_22 (not_22_out, b0);
  not not_23 (not_23_out, b2);
  not not_24 (not_24_out, b1);
  not not_25 (not_25_out, b3);
  not not_26 (not_26_out, b2);
  not not_27 (not_27_out, b3);
  not not_28 (not_28_out, b1);
  and and_14 (and_14_out, not_28_out, not_29_out, not_30_out);
  not not_29 (not_29_out, b2);
  not not_30 (not_30_out, b3);
  and and_15 (and_15_out, b1, b3);
  not not_31 (not_31_out, b0);
  and and_16 (and_16_out, not_31_out, b1, b2);
  and and_17 (and_17_out, b0, not_32_out);
  not not_32 (not_32_out, b2);
  not not_33 (not_33_out, b0);
  and and_18 (and_18_out, not_33_out, b2);
  not not_34 (not_34_out, b0);
  and and_19 (and_19_out, not_34_out, b1, b3);
  and and_20 (and_20_out, b0, not_35_out);
  not not_35 (not_35_out, b1);
  and and_21 (and_21_out, b0, not_36_out);
  not not_36 (not_36_out, b2);
  or or_1 (a, and_1_out, and_2_out, and_3_out);
  or or_2 (b, and_4_out, and_5_out, and_6_out, and_7_out);
  or or_3 (c, and_8_out, not_10_out, b1, and_9_out);
  or or_4 (d, and_10_out, and_11_out, and_12_out, and_13_out);
  and and_22 (and_22_out, not_16_out, not_17_out, not_18_out, not_19_out);
  and and_23 (and_23_out, not_20_out, not_21_out, b2, b3);
  and and_24 (and_24_out, not_22_out, b1, not_23_out, b3);
  and and_25 (and_25_out, b0, not_24_out, b2, not_25_out);
  and and_26 (and_26_out, b0, b1, not_26_out, not_27_out);
  and and_27 (and_27_out, b0, b1, b2, b3);
  or or_5 (f, and_14_out, and_15_out, and_16_out, and_17_out);
  or or_6 (g, and_18_out, and_19_out, and_20_out, and_21_out);
  or or_7 (e, and_22_out, and_23_out, and_24_out, and_25_out, and_26_out, and_27_out);
endmodule

module Contador_grey (
  input  P0,
  output b3,
  output b2,
  output b1,
  output b0
);

  wire and_1_out, and_2_out, and_3_out, and_4_out, and_5_out, and_6_out, and_7_out, clock_1_out, not_1_out,
       not_2_out, t_ff_1_qn, t_ff_2_qn, t_ff_3_qn, t_ff_4_q, t_ff_5_qn, xor_1_out, xor_2_out, xor_3_out;

  Clock clock_1 (.out(clock_1_out));
  xor xor_1 (xor_1_out, b3, b2);
  not not_1 (not_1_out, b0);
  not not_2 (not_2_out, b1);
  and and_1 (and_1_out, not_1_out, not_2_out, xor_1_out);
  T_Flip_Flop t_ff_1 (.clk(clock_1_out), .T(and_1_out), .Q(b3), .Qn(t_ff_1_qn), .reset(P0));  // open: preset, en
  and and_2 (and_2_out, b0, t_ff_3_qn, t_ff_2_qn, t_ff_1_qn);
  and and_3 (and_3_out, b0, b1, b2, t_ff_1_qn);
  and and_4 (and_4_out, b0, t_ff_3_qn, b2, b3);
  and and_5 (and_5_out, b0, b1, t_ff_2_qn, b3);
  ExactlyOne xor_2 (.out(xor_2_out), .in0(and_2_out), .in1(and_3_out), .in2(and_4_out), .in3(and_5_out));
  T_Flip_Flop t_ff_2 (.clk(clock_1_out), .T(xor_3_out), .Q(b2), .Qn(t_ff_2_qn), .reset(P0));  // open: preset, en
  and and_6 (and_6_out, t_ff_5_qn, b1, t_ff_2_qn, t_ff_1_qn);
  and and_7 (and_7_out, t_ff_5_qn, b1, b2, b3);
  xor xor_3 (xor_3_out, and_6_out, and_7_out);
  T_Flip_Flop t_ff_3 (.clk(clock_1_out), .T(xor_2_out), .Q(b1), .Qn(t_ff_3_qn), .reset(P0));  // open: preset, en
  T_Flip_Flop t_ff_4 (.clk(clock_1_out), .T(1'b1), .Q(t_ff_4_q));  // open: Qn, preset, reset, en
  T_Flip_Flop t_ff_5 (.clk(clock_1_out), .T(t_ff_4_q), .Q(b0), .Qn(t_ff_5_qn), .reset(P0));  // open: preset, en
endmodule
