// Logisim project TP.circ as structural Verilog: 7 circuits, main circuit main
module main (
);

  wire _0_s0, _0_s1, _1_led, _1_s0, _2_p5, _2_p6, _3_p2, _3_p3, _3_p4, _4_p5, _4_p6, _5_p5, _5_p6, _7_p2,
       _7_p3, _7_p4, _8_p5, _8_p6, _9_p5, _9_p6, B_p2, B_p3, B_p4, C_p5, C_p6, clock_1_out,
       contador_0_3_1_out_2, contador_0_3_1_out_3, contador_0_3_2_out_2, contador_0_3_2_out_3, d_ff_1_q,
       D_p5, D_p6, decodificar_direcciones_1_s0, decodificar_direcciones_1_s1, decodificar_direcciones_1_s2,
       decodificar_direcciones_1_s3, decodificar_direcciones_2_s0, decodificar_direcciones_2_s1,
       decodificar_direcciones_2_s2, decodificar_direcciones_2_s3, F_p2, F_p3, F_p4, G_2_out, G_3_out,
       G_4_out, G_5_out, G_6_out, G_7_out, G_8_out, G_9_out, G_10_out, G_11_out, G_12_out, G_out, M_2_out,
       M_3_out, M_4_out, M_5_out, M_6_out, M_7_out, M_8_out, M_9_out, M_10_out, M_11_out, M_12_out, M_out,
       P_2_out, P_3_out, P_4_out, P_5_out, P_6_out, P_7_out, P_8_out, P_9_out, P_10_out, P_11_out, P_12_out,
       P_out, salida_de_celda_1_out_5, salida_de_celda_1_out_6, V_2_out, V_3_out, V_4_out, V_5_out, V_6_out,
       V_7_out, V_8_out, V_9_out, V_10_out, V_11_out, V_12_out, V_13_out, V_14_out, V_15_out, V_16_out, V_out;

  Clock clock_1 (.out(clock_1_out));
  Contador_0_3 contador_0_3_1 (.in_1(d_ff_1_q), .out_2(contador_0_3_1_out_2), .out_3(contador_0_3_1_out_3));
  D_Flip_Flop d_ff_1 (
    .clk(clock_1_out), .D(decodificar_direcciones_2_s3), .Q(d_ff_1_q));  // open: Qn, preset, en, reset
  Contador_0_3 contador_0_3_2 (.in_1(clock_1_out), .out_2(contador_0_3_2_out_2), .out_3(contador_0_3_2_out_3));
  Decodificar_direcciones decodificar_direcciones_1 (
    .b0(contador_0_3_1_out_2), .b1(contador_0_3_1_out_3), .s0(decodificar_direcciones_1_s0),
    .s1(decodificar_direcciones_1_s1), .s2(decodificar_direcciones_1_s2), .s3(decodificar_direcciones_1_s3));
  Decodificar_direcciones decodificar_direcciones_2 (
    .b0(contador_0_3_2_out_2), .b1(contador_0_3_2_out_3), .s0(decodificar_direcciones_2_s0),
    .s1(decodificar_direcciones_2_s1), .s2(decodificar_direcciones_2_s2), .s3(decodificar_direcciones_2_s3));
  Button V (.out(V_out));
  Button P (.out(P_out));
  Button M (.out(M_out));
  Button G (.out(G_out));
  LED led_1 ();  // open: in
  Button V_2 (.out(V_2_out));
  Button P_2 (.out(P_2_out));
  Button M_2 (.out(M_2_out));
  Button G_2 (.out(G_2_out));
  Button V_3 (.out(V_3_out));
  Button P_3 (.out(P_3_out));
  Button M_3 (.out(M_3_out));
  Button G_3 (.out(G_3_out));
  Button V_4 (.out(V_4_out));
  Button P_4 (.out(P_4_out));
  Button M_4 (.out(M_4_out));
  Button G_4 (.out(G_4_out));
  Salida_de_celda salida_de_celda_1 (
    .Fila(decodificar_direcciones_1_s0), .Col(decodificar_direcciones_2_s0), .b0(_0_s0), .b1(_0_s1),
    .out_5(salida_de_celda_1_out_5), .out_6(salida_de_celda_1_out_6));
  Celda_de_memoria _0 (.Pa0(V_out), .Pa1(P_out), .Pa2(M_out), .Pa3(G_out), .s0(_0_s0), .s1(_0_s1));  // open: LED
  Salida_de_celda salida_de_celda_2 (
    .Fila(decodificar_direcciones_1_s1), .Col(decodificar_direcciones_2_s0), .b0(_4_p5), .b1(_4_p6));  // open: out_5, out_6
  // Celda_de_memoria _4: pin names not known; wires that end beside it: V_2_out, P_2_out, M_2_out, G_2_out, _4_p5, _4_p6
  Salida_de_celda salida_de_celda_3 (
    .Fila(decodificar_direcciones_1_s2), .Col(decodificar_direcciones_2_s0), .b0(_8_p5), .b1(_8_p6));  // open: out_5, out_6
  // Celda_de_memoria _8: pin names not known; wires that end beside it: V_3_out, P_3_out, M_3_out, G_3_out, _8_p5, _8_p6
  Salida_de_celda salida_de_celda_4 (
    .Fila(decodificar_direcciones_1_s3), .Col(decodificar_direcciones_2_s0), .b0(C_p5), .b1(C_p6));  // open: out_5, out_6
  // Celda_de_memoria C: pin names not known; wires that end beside it: V_4_out, P_4_out, M_4_out, G_4_out, C_p5, C_p6
  Button V_5 (.out(V_5_out));
  Button P_5 (.out(P_5_out));
  Button M_5 (.out(M_5_out));
  Button G_5 (.out(G_5_out));
  Button V_6 (.out(V_6_out));
  Button P_6 (.out(P_6_out));
  Button M_6 (.out(M_6_out));
  Button G_6 (.out(G_6_out));
  Button V_7 (.out(V_7_out));
  Button P_7 (.out(P_7_out));
  Button M_7 (.out(M_7_out));
  Button G_7 (.out(G_7_out));
  Button V_8 (.out(V_8_out));
  Button P_8 (.out(P_8_out));
  Button M_8 (.out(M_8_out));
  Button G_8 (.out(G_8_out));
  Celda_de_memoria _1 (
    .Pa0(V_5_out), .Pa1(P_5_out), .Pa2(M_5_out), .Pa3(G_5_out), .s0(_1_s0), .LED(_1_led));  // open: s1
  // Celda_de_memoria _5: pin names not known; wires that end beside it: V_6_out, P_6_out, M_6_out, G_6_out, _5_p5, _5_p6
  // Celda_de_memoria _9: pin names not known; wires that end beside it: V_7_out, P_7_out, M_7_out, G_7_out, _9_p5, _9_p6
  // Celda_de_memoria D: pin names not known; wires that end beside it: V_8_out, P_8_out, M_8_out, G_8_out, D_p5, D_p6
  Salida_de_celda salida_de_celda_5 (
    .Fila(decodificar_direcciones_1_s0), .Col(decodificar_direcciones_2_s1), .b0(_1_s0), .b1(_1_led));  // open: out_5, out_6
  Salida_de_celda salida_de_celda_6 (
    .Fila(decodificar_direcciones_1_s1), .Col(decodificar_direcciones_2_s1), .b0(_5_p5), .b1(_5_p6));  // open: out_5, out_6
  Salida_de_celda salida_de_celda_7 (
    .Fila(decodificar_direcciones_1_s2), .Col(decodificar_direcciones_2_s1), .b0(_9_p5), .b1(_9_p6));  // open: out_5, out_6
  Salida_de_celda salida_de_celda_8 (
    .Fila(decodificar_direcciones_1_s3), .Col(decodificar_direcciones_2_s1), .b0(D_p5), .b1(D_p6));  // open: out_5, out_6
  Button V_9 (.out(V_9_out));
  Button P_9 (.out(P_9_out));
  Button M_9 (.out(M_9_out));
  Button G_9 (.out(G_9_out));
  Button V_10 (.out(V_10_out));
  Button P_10 (.out(P_10_out));
  Button M_10 (.out(M_10_out));
  Button G_10 (.out(G_10_out));
  Button V_11 (.out(V_11_out));
  Button P_11 (.out(P_11_out));
  Button M_11 (.out(M_11_out));
  Button G_11 (.out(G_11_out));
  Button V_12 (.out(V_12_out));
  Button P_12 (.out(P_12_out));
  Button M_12 (.out(M_12_out));
  Button G_12 (.out(G_12_out));
  // Celda_de_memoria _2: pin names not known; wires that end beside it: V_9_out, P_9_out, M_9_out, G_9_out, _2_p5, _2_p6
  // Celda_de_memoria _6: pin names not known; wires that end beside it: V_10_out, P_10_out, M_10_out, G_10_out
  // Celda_de_memoria A: pin names not known; wires that end beside it: V_11_out, P_11_out, M_11_out, G_11_out
  // Celda_de_memoria E: pin names not known; wires that end beside it: V_12_out, P_12_out, M_12_out, G_12_out
  Salida_de_celda salida_de_celda_9 (
    .Fila(decodificar_direcciones_1_s0), .Col(decodificar_direcciones_2_s2), .b0(_2_p5), .b1(_2_p6));  // open: out_5, out_6
  // AND_Gate and_1 has open pins: in0=decodificar_direcciones_1_s1, in1=decodificar_direcciones_2_s2, out=open
  // AND_Gate and_2 has open pins: in0=decodificar_direcciones_1_s2, in1=decodificar_direcciones_2_s2, out=open
  // AND_Gate and_3 has open pins: in0=decodificar_direcciones_1_s3, in1=decodificar_direcciones_2_s2, out=open
  Button V_13 (.out(V_13_out));
  // Celda_de_memoria _3: pin names not known; wires that end beside it: V_13_out, _3_p2, _3_p3, _3_p4
  Button P_13 (.out(_3_p2));
  Button M_13 (.out(_3_p3));
  Button G_13 (.out(_3_p4));
  Button V_14 (.out(V_14_out));
  // Celda_de_memoria _7: pin names not known; wires that end beside it: V_14_out, _7_p2, _7_p3, _7_p4
  Button P_14 (.out(_7_p2));
  Button M_14 (.out(_7_p3));
  Button G_14 (.out(_7_p4));
  Button V_15 (.out(V_15_out));
  // Celda_de_memoria B: pin names not known; wires that end beside it: V_15_out, B_p2, B_p3, B_p4
  Button P_15 (.out(B_p2));
  Button M_15 (.out(B_p3));
  Button G_15 (.out(B_p4));
  Button V_16 (.out(V_16_out));
  // Celda_de_memoria F: pin names not known; wires that end beside it: V_16_out, F_p2, F_p3, F_p4
  Button P_16 (.out(F_p2));
  Button M_16 (.out(F_p3));
  Button G_16 (.out(F_p4));
  // AND_Gate and_4 has open pins: in0=decodificar_direcciones_1_s1, in1=decodificar_direcciones_2_s3, out=open
  // AND_Gate and_5 has open pins: in0=decodificar_direcciones_1_s2, in1=decodificar_direcciones_2_s3, out=open
  // AND_Gate and_6 has open pins: in0=decodificar_direcciones_1_s3, in1=decodificar_direcciones_2_s3, out=open
endmodule

// Deco
module Decodificar_direcciones (
  input  b0,
  input  b1,
  output s0,
  output s1,
  output s2,
  output s3
);

  and and_1 (s0, ~b0, ~b1);  // AND_Gate
  and and_2 (s1, b0, ~b1);  // AND_Gate
  and and_3 (s2, ~b0, b1);  // AND_Gate
  and and_4 (s3, b0, b1);
endmodule

// Cont
module Contador_0_3 (
  input  in_1,
  output out_2,
  output out_3
);

  T_Flip_Flop t_ff_1 (.clk(in_1), .T(out_2), .Q(out_3));  // open: Qn, preset, reset, en
  T_Flip_Flop t_ff_2 (.clk(in_1), .T(in_1), .Q(out_2));  // open: Qn, preset, reset, en
endmodule

module Contador_filas (
  input  in_1
);
endmodule

module Celda_de_memoria (
  input  Pa0,
  input  Pa1,
  input  Pa2,
  input  Pa3,
  output s0,
  output s1,
  output LED
);

  wire control_dig_simult_1_out_5, control_dig_simult_1_out_6, control_dig_simult_1_out_7,
       control_dig_simult_1_out_8, or_1_out, or_2_out, or_3_out, or_4_out;

  Control_dig__simult control_dig_simult_1 (
    .in_1(Pa0), .in_2(Pa1), .in_3(Pa2), .in_4(Pa3), .out_5(control_dig_simult_1_out_5),
    .out_6(control_dig_simult_1_out_6), .out_7(control_dig_simult_1_out_7), .out_8(control_dig_simult_1_out_8));
  D_Flip_Flop d_ff_1 (.Q(s1), .preset(or_2_out), .reset(or_1_out));  // open: clk, D, Qn, en
  or or_1 (or_1_out, control_dig_simult_1_out_5, control_dig_simult_1_out_6);
  or or_2 (or_2_out, control_dig_simult_1_out_7, control_dig_simult_1_out_8);
  or or_3 (or_3_out, control_dig_simult_1_out_6, control_dig_simult_1_out_8);
  D_Flip_Flop d_ff_2 (.Q(s0), .preset(or_3_out), .reset(or_4_out));  // open: clk, D, Qn, en
  or or_4 (or_4_out, control_dig_simult_1_out_5, control_dig_simult_1_out_7);
  or or_5 (LED, s1, s0);
endmodule

// Crl. dig.
module Control_dig__simult (
  input  in_1,
  input  in_2,
  input  in_3,
  input  in_4,
  output out_5,
  output out_6,
  output out_7,
  output out_8
);

  wire xor_1_out, xor_2_out, xor_3_out, xor_4_out;

  ExactlyOne xor_1 (.out(xor_1_out), .in0(in_1), .in1(in_2), .in2(in_3), .in3(in_4));
  ExactlyOne xor_2 (.out(xor_2_out), .in0(in_1), .in1(in_2), .in2(in_3), .in3(in_4));
  ExactlyOne xor_3 (.out(xor_3_out), .in0(in_1), .in1(in_2), .in2(in_3), .in3(in_4));
  ExactlyOne xor_4 (.out(xor_4_out), .in0(in_1), .in1(in_2), .in2(in_3), .in3(in_4));
  and and_1 (out_5, in_1, xor_1_out);
  and and_2 (out_6, in_2, xor_2_out);
  and and_3 (out_7, in_3, xor_3_out);
  and and_4 (out_8, in_4, xor_4_out);
endmodule

// Salida
module Salida_de_celda (
  input  Fila,
  input  Col,
  input  b0,
  input  b1,
  output out_5,
  output out_6
);

  wire and_1_out;

  and and_1 (and_1_out, Fila, Col);
  and and_2 (out_5, and_1_out, b0);
  and and_3 (out_6, and_1_out, b1);
endmodule
