// Logisim project Trabajo Práctico.circ as structural Verilog: 10 circuits, main circuit main
module main (
  input  On_Off
);

  wire _0_led, _0_s0, _0_s1, _1_2_b0, _1_2_b1, _1_2_b2, _1_2_b3, _1_2_b4, _1_led, _1_s0, _1_s1, _2_2_b0,
       _2_2_b1, _2_2_b2, _2_2_b3, _2_2_b4, _2_led, _2_s0, _2_s1, _3_2_b0, _3_2_b1, _3_2_b2, _3_2_b3, _3_2_b4,
       _3_led, _3_s0, _3_s1, _4_led, _4_s0, _4_s1, _5_led, _5_s0, _5_s1, _6_led, _6_s0, _6_s1, _7_led, _7_s0,
       _7_s1, _8_led, _8_s0, _8_s1, _9_led, _9_s0, _9_s1, A_led, A_s0, A_s1, and_1_out, and_2_out, and_3_out,
       and_4_out, and_5_out, B_led, B_s0, B_s1, C_led, C_s0, C_s1, cc_1__1, cc_1__2, cc_1__3, clock_1_out,
       contador_0_3_1_out_4, contador_0_3_1_out_5, contador_0_3_1_s0, contador_0_3_1_s3, d_ff_1_q, D_led,
       D_s0, D_s1, decodificar_direcciones_1_s0, decodificar_direcciones_1_s1, decodificar_direcciones_1_s2,
       decodificar_direcciones_1_s3, decodificar_direcciones_1_s4, decodificar_direcciones_1_s5,
       decodificar_direcciones_1_s6, decodificar_direcciones_1_s7, E_led, E_s0, E_s1, F_led, F_s0, F_s1,
       G_2_out, G_3_out, G_4_out, G_5_out, G_6_out, G_7_out, G_8_out, G_9_out, G_10_out, G_11_out, G_12_out,
       G_13_out, G_14_out, G_15_out, G_16_out, G_out, M_2_out, M_3_out, M_4_out, M_5_out, M_6_out, M_7_out,
       M_8_out, M_9_out, M_10_out, M_11_out, M_12_out, M_13_out, M_14_out, M_15_out, M_16_out, M_out,
       n7_segmentos_total_1_d0, n7_segmentos_total_1_out_8, n7_segmentos_total_1_out_9,
       n7_segmentos_total_1_out_10, n7_segmentos_total_1_out_11, n7_segmentos_total_1_out_12,
       n7_segmentos_total_1_out_13, n7_segmentos_total_1_out_15, n7_segmentos_total_1_out_16,
       n7_segmentos_total_1_out_17, n7_segmentos_total_1_out_18, n7_segmentos_total_1_out_19,
       n7_segmentos_total_1_out_20, n7_segmentos_total_1_u0, n7_segmentos_total_2_d0,
       n7_segmentos_total_2_out_8, n7_segmentos_total_2_out_9, n7_segmentos_total_2_out_10,
       n7_segmentos_total_2_out_11, n7_segmentos_total_2_out_12, n7_segmentos_total_2_out_13,
       n7_segmentos_total_2_out_15, n7_segmentos_total_2_out_16, n7_segmentos_total_2_out_17,
       n7_segmentos_total_2_out_18, n7_segmentos_total_2_out_19, n7_segmentos_total_2_out_20,
       n7_segmentos_total_2_u0, n7_segmentos_total_3_d0, n7_segmentos_total_3_out_8,
       n7_segmentos_total_3_out_9, n7_segmentos_total_3_out_10, n7_segmentos_total_3_out_11,
       n7_segmentos_total_3_out_12, n7_segmentos_total_3_out_13, n7_segmentos_total_3_out_15,
       n7_segmentos_total_3_out_16, n7_segmentos_total_3_out_17, n7_segmentos_total_3_out_18,
       n7_segmentos_total_3_out_19, n7_segmentos_total_3_out_20, n7_segmentos_total_3_u0, not_1_out,
       not_2_out, or_1_out, or_2_out, or_3_out, or_4_out, or_5_out, or_6_out, or_7_out, or_8_out, or_9_out,
       or_10_out, or_11_out, or_12_out, or_13_out, or_14_out, or_15_out, or_16_out, or_17_out, or_18_out,
       or_19_out, or_20_out, or_21_out, or_22_out, or_23_out, or_24_out, or_25_out, or_26_out, or_27_out,
       or_28_out, or_29_out, or_30_out, P_2_out, P_3_out, P_4_out, P_5_out, P_6_out, P_7_out, P_8_out,
       P_9_out, P_10_out, P_11_out, P_12_out, P_13_out, P_14_out, P_15_out, P_16_out, P_out, V_2_out,
       V_3_out, V_4_out, V_5_out, V_6_out, V_7_out, V_8_out, V_9_out, V_10_out, V_11_out, V_12_out, V_13_out,
       V_14_out, V_15_out, V_16_out, V_out;

  not not_1 (not_1_out, On_Off);
  Clock clock_1 (.out(clock_1_out));
  and and_1 (and_1_out, clock_1_out, d_ff_1_q);
  not not_2 (not_2_out, On_Off);
  D_Flip_Flop d_ff_1 (.clk(clock_1_out), .D(On_Off), .Q(d_ff_1_q));  // open: Qn, preset, en, reset
  Contador_0_3 contador_0_3_1 (
    .in_1(and_1_out), .Pa0(not_2_out), .s0(contador_0_3_1_s0), .out_4(contador_0_3_1_out_4),
    .out_5(contador_0_3_1_out_5), .s3(contador_0_3_1_s3));
  Decodificar_direcciones decodificar_direcciones_1 (
    .b0(contador_0_3_1_s0), .b1(contador_0_3_1_out_4), .b2(contador_0_3_1_out_5), .b3(contador_0_3_1_s3),
    .s0(decodificar_direcciones_1_s0), .s1(decodificar_direcciones_1_s1), .s2(decodificar_direcciones_1_s2),
    .s3(decodificar_direcciones_1_s3), .s4(decodificar_direcciones_1_s4), .s5(decodificar_direcciones_1_s5),
    .s6(decodificar_direcciones_1_s6), .s7(decodificar_direcciones_1_s7));
  and and_2 (and_2_out, On_Off, decodificar_direcciones_1_s4);
  Button V (.out(V_out));
  Button P (.out(P_out));
  Button M (.out(M_out));
  Button G (.out(G_out));
  Button V_2 (.out(V_2_out));
  Button P_2 (.out(P_2_out));
  Button M_2 (.out(M_2_out));
  Button G_2 (.out(G_2_out));
  Button V_3 (.out(V_3_out));
  Button P_3 (.out(P_3_out));
  Button M_3 (.out(M_3_out));
  Button G_3 (.out(G_3_out));
  Button V_4 (.out(V_4_out));
  Button P_4 (.out(P_4_out));
  Button M_4 (.out(M_4_out));
  Button G_4 (.out(G_4_out));
  Celda_de_memoria _0 (
    .Fila(and_2_out), .Columna(decodificar_direcciones_1_s0), .Pa0(V_out), .Pa1(P_out), .Pa2(M_out),
    .Pa3(G_out), .s0(_0_s0), .s1(_0_s1), .LED(_0_led));
  LED led_1 (.in(_0_led));
  Celda_de_memoria _4 (
    .Fila(decodificar_direcciones_1_s6), .Columna(decodificar_direcciones_1_s0), .Pa0(V_2_out),
    .Pa1(P_2_out), .Pa2(M_2_out), .Pa3(G_2_out), .s0(_4_s0), .s1(_4_s1), .LED(_4_led));
  LED led_2 (.in(_4_led));
  Celda_de_memoria _8 (
    .Fila(decodificar_direcciones_1_s5), .Columna(decodificar_direcciones_1_s0), .Pa0(V_3_out),
    .Pa1(P_3_out), .Pa2(M_3_out), .Pa3(G_3_out), .s0(_8_s0), .s1(_8_s1), .LED(_8_led));
  LED led_3 (.in(_8_led));
  Celda_de_memoria C (
    .Fila(decodificar_direcciones_1_s7), .Columna(decodificar_direcciones_1_s0), .Pa0(V_4_out),
    .Pa1(P_4_out), .Pa2(M_4_out), .Pa3(G_4_out), .s0(C_s0), .s1(C_s1), .LED(C_led));
  LED led_4 (.in(C_led));
  Button V_5 (.out(V_5_out));
  Button P_5 (.out(P_5_out));
  Button M_5 (.out(M_5_out));
  Button G_5 (.out(G_5_out));
  Button V_6 (.out(V_6_out));
  Button P_6 (.out(P_6_out));
  Button M_6 (.out(M_6_out));
  Button G_6 (.out(G_6_out));
  Button V_7 (.out(V_7_out));
  Button P_7 (.out(P_7_out));
  Button M_7 (.out(M_7_out));
  Button G_7 (.out(G_7_out));
  Button V_8 (.out(V_8_out));
  Button P_8 (.out(P_8_out));
  Button M_8 (.out(M_8_out));
  Button G_8 (.out(G_8_out));
  Celda_de_memoria _1 (
    .Fila(and_2_out), .Columna(decodificar_direcciones_1_s2), .Pa0(V_5_out), .Pa1(P_5_out), .Pa2(M_5_out),
    .Pa3(G_5_out), .s0(_1_s0), .s1(_1_s1), .LED(_1_led));
  LED led_5 (.in(_1_led));
  Celda_de_memoria _5 (
    .Fila(decodificar_direcciones_1_s6), .Columna(decodificar_direcciones_1_s2), .Pa0(V_6_out),
    .Pa1(P_6_out), .Pa2(M_6_out), .Pa3(G_6_out), .s0(_5_s0), .s1(_5_s1), .LED(_5_led));
  LED led_6 (.in(_5_led));
  Celda_de_memoria _9 (
    .Fila(decodificar_direcciones_1_s5), .Columna(decodificar_direcciones_1_s2), .Pa0(V_7_out),
    .Pa1(P_7_out), .Pa2(M_7_out), .Pa3(G_7_out), .s0(_9_s0), .s1(_9_s1), .LED(_9_led));
  LED led_7 (.in(_9_led));
  Celda_de_memoria D (
    .Fila(decodificar_direcciones_1_s7), .Columna(decodificar_direcciones_1_s2), .Pa0(V_8_out),
    .Pa1(P_8_out), .Pa2(M_8_out), .Pa3(G_8_out), .s0(D_s0), .s1(D_s1), .LED(D_led));
  LED led_8 (.in(D_led));
  or or_1 (or_1_out, _1_s0, _0_s0);
  or or_2 (or_2_out, _1_s1, _0_s1);
  or or_3 (or_3_out, _5_s0, _4_s0);
  or or_4 (or_4_out, _5_s1, _4_s1);
  or or_5 (or_5_out, _9_s0, _8_s0);
  or or_6 (or_6_out, _9_s1, _8_s1);
  or or_7 (or_7_out, D_s0, C_s0);
  or or_8 (or_8_out, D_s1, C_s1);
  Button V_9 (.out(V_9_out));
  Button P_9 (.out(P_9_out));
  Button M_9 (.out(M_9_out));
  Button G_9 (.out(G_9_out));
  Button V_10 (.out(V_10_out));
  Button P_10 (.out(P_10_out));
  Button M_10 (.out(M_10_out));
  Button G_10 (.out(G_10_out));
  Button V_11 (.out(V_11_out));
  Button P_11 (.out(P_11_out));
  Button M_11 (.out(M_11_out));
  Button G_11 (.out(G_11_out));
  Button V_12 (.out(V_12_out));
  Button P_12 (.out(P_12_out));
  Button M_12 (.out(M_12_out));
  Button G_12 (.out(G_12_out));
  Celda_de_memoria _2 (
    .Fila(and_2_out), .Columna(decodificar_direcciones_1_s1), .Pa0(V_9_out), .Pa1(P_9_out), .Pa2(M_9_out),
    .Pa3(G_9_out), .s0(_2_s0), .s1(_2_s1), .LED(_2_led));
  LED led_9 (.in(_2_led));
  Celda_de_memoria _6 (
    .Fila(decodificar_direcciones_1_s6), .Columna(decodificar_direcciones_1_s1), .Pa0(V_10_out),
    .Pa1(P_10_out), .Pa2(M_10_out), .Pa3(G_10_out), .s0(_6_s0), .s1(_6_s1), .LED(_6_led));
  LED led_10 (.in(_6_led));
  Celda_de_memoria A (
    .Fila(decodificar_direcciones_1_s5), .Columna(decodificar_direcciones_1_s1), .Pa0(V_11_out),
    .Pa1(P_11_out), .Pa2(M_11_out), .Pa3(G_11_out), .s0(A_s0), .s1(A_s1), .LED(A_led));
  LED led_11 (.in(A_led));
  Celda_de_memoria E (
    .Fila(decodificar_direcciones_1_s7), .Columna(decodificar_direcciones_1_s1), .Pa0(V_12_out),
    .Pa1(P_12_out), .Pa2(M_12_out), .Pa3(G_12_out), .s0(E_s0), .s1(E_s1), .LED(E_led));
  LED led_12 (.in(E_led));
  Button V_13 (.out(V_13_out));
  Button P_13 (.out(P_13_out));
  Button M_13 (.out(M_13_out));
  Button G_13 (.out(G_13_out));
  or or_9 (or_9_out, _2_s0, or_1_out);
  or or_10 (or_10_out, _2_s1, or_2_out);
  Button V_14 (.out(V_14_out));
  Button P_14 (.out(P_14_out));
  Button M_14 (.out(M_14_out));
  Button G_14 (.out(G_14_out));
  or or_11 (or_11_out, _6_s0, or_3_out);
  or or_12 (or_12_out, _6_s1, or_4_out);
  Button V_15 (.out(V_15_out));
  Button P_15 (.out(P_15_out));
  Button M_15 (.out(M_15_out));
  Button G_15 (.out(G_15_out));
  or or_13 (or_13_out, A_s0, or_5_out);
  or or_14 (or_14_out, A_s1, or_6_out);
  Button V_16 (.out(V_16_out));
  Button P_16 (.out(P_16_out));
  Button M_16 (.out(M_16_out));
  Button G_16 (.out(G_16_out));
  or or_15 (or_15_out, E_s0, or_7_out);
  or or_16 (or_16_out, E_s1, or_8_out);
  Celda_de_memoria _3 (
    .Fila(and_2_out), .Columna(decodificar_direcciones_1_s3), .Pa0(V_13_out), .Pa1(P_13_out), .Pa2(M_13_out),
    .Pa3(G_13_out), .s0(_3_s0), .s1(_3_s1), .LED(_3_led));
  LED led_13 (.in(_3_led));
  Celda_de_memoria _7 (
    .Fila(decodificar_direcciones_1_s6), .Columna(decodificar_direcciones_1_s3), .Pa0(V_14_out),
    .Pa1(P_14_out), .Pa2(M_14_out), .Pa3(G_14_out), .s0(_7_s0), .s1(_7_s1), .LED(_7_led));
  LED led_14 (.in(_7_led));
  Celda_de_memoria B (
    .Fila(decodificar_direcciones_1_s5), .Columna(decodificar_direcciones_1_s3), .Pa0(V_15_out),
    .Pa1(P_15_out), .Pa2(M_15_out), .Pa3(G_15_out), .s0(B_s0), .s1(B_s1), .LED(B_led));
  LED led_15 (.in(B_led));
  Celda_de_memoria F (
    .Fila(decodificar_direcciones_1_s7), .Columna(decodificar_direcciones_1_s3), .Pa0(V_16_out),
    .Pa1(P_16_out), .Pa2(M_16_out), .Pa3(G_16_out), .s0(F_s0), .s1(F_s1), .LED(F_led));
  LED led_16 (.in(F_led));
  or or_17 (or_17_out, _3_s0, or_9_out);
  or or_18 (or_18_out, _3_s1, or_10_out);
  or or_19 (or_19_out, _7_s0, or_11_out);
  or or_20 (or_20_out, _7_s1, or_12_out);
  or or_21 (or_21_out, B_s0, or_13_out);
  or or_22 (or_22_out, B_s1, or_14_out);
  or or_23 (or_23_out, F_s0, or_15_out);
  or or_24 (or_24_out, F_s1, or_16_out);
  or or_25 (or_25_out, or_20_out, or_18_out);
  or or_26 (or_26_out, or_22_out, or_25_out);
  or or_27 (or_27_out, or_23_out, or_30_out);
  or or_28 (or_28_out, or_24_out, or_26_out);
  or or_29 (or_29_out, or_19_out, or_17_out);
  or or_30 (or_30_out, or_21_out, or_29_out);
  CC cc_1 (.b0(or_27_out), .b1(or_28_out), ._1(cc_1__1), ._2(cc_1__2), ._3(cc_1__3));
  _7_Segment_Display u_7_segment_display_1 (
    .g(n7_segmentos_total_1_d0), .f(n7_segmentos_total_1_out_15), .a(n7_segmentos_total_1_out_16),
    .b(n7_segmentos_total_1_out_17), .e(n7_segmentos_total_1_out_20), .d(n7_segmentos_total_1_out_19),
    .c(n7_segmentos_total_1_out_18));  // open: dp
  _7_segmentos_total u_7_segmentos_total_1 (
    .b0(_1_2_b0), .b1(_1_2_b1), .b2(_1_2_b2), .b3(_1_2_b3), .b4(_1_2_b4), .b5(1'b0),
    .u0(n7_segmentos_total_1_u0), .out_8(n7_segmentos_total_1_out_8), .out_9(n7_segmentos_total_1_out_9),
    .out_10(n7_segmentos_total_1_out_10), .out_11(n7_segmentos_total_1_out_11),
    .out_12(n7_segmentos_total_1_out_12), .out_13(n7_segmentos_total_1_out_13), .d0(n7_segmentos_total_1_d0),
    .out_15(n7_segmentos_total_1_out_15), .out_16(n7_segmentos_total_1_out_16),
    .out_17(n7_segmentos_total_1_out_17), .out_18(n7_segmentos_total_1_out_18),
    .out_19(n7_segmentos_total_1_out_19), .out_20(n7_segmentos_total_1_out_20));
  Contador_0_16 _1_2 (
    .in_1(and_3_out), .Pa0(not_1_out), .b0(_1_2_b0), .b1(_1_2_b1), .b2(_1_2_b2), .b3(_1_2_b3), .b4(_1_2_b4));
  and and_3 (and_3_out, ~clock_1_out, cc_1__1);  // AND_Gate
  _7_Segment_Display u_7_segment_display_2 (
    .g(n7_segmentos_total_1_u0), .f(n7_segmentos_total_1_out_8), .a(n7_segmentos_total_1_out_9),
    .b(n7_segmentos_total_1_out_10), .e(n7_segmentos_total_1_out_13), .d(n7_segmentos_total_1_out_12),
    .c(n7_segmentos_total_1_out_11));  // open: dp
  _7_segmentos_total u_7_segmentos_total_2 (
    .b0(_2_2_b0), .b1(_2_2_b1), .b2(_2_2_b2), .b3(_2_2_b3), .b4(_2_2_b4), .b5(1'b0),
    .u0(n7_segmentos_total_2_u0), .out_8(n7_segmentos_total_2_out_8), .out_9(n7_segmentos_total_2_out_9),
    .out_10(n7_segmentos_total_2_out_10), .out_11(n7_segmentos_total_2_out_11),
    .out_12(n7_segmentos_total_2_out_12), .out_13(n7_segmentos_total_2_out_13), .d0(n7_segmentos_total_2_d0),
    .out_15(n7_segmentos_total_2_out_15), .out_16(n7_segmentos_total_2_out_16),
    .out_17(n7_segmentos_total_2_out_17), .out_18(n7_segmentos_total_2_out_18),
    .out_19(n7_segmentos_total_2_out_19), .out_20(n7_segmentos_total_2_out_20));
  and and_4 (and_4_out, ~clock_1_out, cc_1__2);  // AND_Gate
  _7_Segment_Display u_7_segment_display_3 (
    .g(n7_segmentos_total_2_u0), .f(n7_segmentos_total_2_out_8), .a(n7_segmentos_total_2_out_9),
    .b(n7_segmentos_total_2_out_10), .e(n7_segmentos_total_2_out_13), .d(n7_segmentos_total_2_out_12),
    .c(n7_segmentos_total_2_out_11));  // open: dp
  _7_Segment_Display u_7_segment_display_4 (
    .g(n7_segmentos_total_2_d0), .f(n7_segmentos_total_2_out_15), .a(n7_segmentos_total_2_out_16),
    .b(n7_segmentos_total_2_out_17), .e(n7_segmentos_total_2_out_20), .d(n7_segmentos_total_2_out_19),
    .c(n7_segmentos_total_2_out_18));  // open: dp
  Contador_0_16 _2_2 (
    .in_1(and_4_out), .Pa0(not_1_out), .b0(_2_2_b0), .b1(_2_2_b1), .b2(_2_2_b2), .b3(_2_2_b3), .b4(_2_2_b4));
  _7_Segment_Display u_7_segment_display_5 (
    .g(n7_segmentos_total_3_d0), .f(n7_segmentos_total_3_out_15), .a(n7_segmentos_total_3_out_16),
    .b(n7_segmentos_total_3_out_17), .e(n7_segmentos_total_3_out_20), .d(n7_segmentos_total_3_out_19),
    .c(n7_segmentos_total_3_out_18));  // open: dp
  _7_segmentos_total u_7_segmentos_total_3 (
    .b0(_3_2_b0), .b1(_3_2_b1), .b2(_3_2_b2), .b3(_3_2_b3), .b4(_3_2_b4), .b5(1'b0),
    .u0(n7_segmentos_total_3_u0), .out_8(n7_segmentos_total_3_out_8), .out_9(n7_segmentos_total_3_out_9),
    .out_10(n7_segmentos_total_3_out_10), .out_11(n7_segmentos_total_3_out_11),
    .out_12(n7_segmentos_total_3_out_12), .out_13(n7_segmentos_total_3_out_13), .d0(n7_segmentos_total_3_d0),
    .out_15(n7_segmentos_total_3_out_15), .out_16(n7_segmentos_total_3_out_16),
    .out_17(n7_segmentos_total_3_out_17), .out_18(n7_segmentos_total_3_out_18),
    .out_19(n7_segmentos_total_3_out_19), .out_20(n7_segmentos_total_3_out_20));
  Contador_0_16 _3_2 (
    .in_1(and_5_out), .Pa0(not_1_out), .b0(_3_2_b0), .b1(_3_2_b1), .b2(_3_2_b2), .b3(_3_2_b3), .b4(_3_2_b4));
  and and_5 (and_5_out, ~clock_1_out, cc_1__3);  // AND_Gate
  _7_Segment_Display u_7_segment_display_6 (
    .g(n7_segmentos_total_3_u0), .f(n7_segmentos_total_3_out_8), .a(n7_segmentos_total_3_out_9),
    .b(n7_segmentos_total_3_out_10), .e(n7_segmentos_total_3_out_13), .d(n7_segmentos_total_3_out_12),
    .c(n7_segmentos_total_3_out_11));  // open: dp

  // Notes on the sheet:
  //   Para inicializar la máquina contadora y clasificadora de huevos, presione la tecla "On/Off"  (primero deberá cargar los huevos)
  //   V = Vacío
  //   P = Pequeño
  //   M = Mediano
  //   G = Grande
  //   Pequeño
  //   Primero cargue los huevos en cada celda de la siguiente manera:
  //   Mediano
  //   Grande
endmodule

// Deco
module Decodificar_direcciones (
  input  b0,
  input  b1,
  input  b2,
  input  b3,
  output s0,
  output s1,
  output s2,
  output s3,
  output s4,
  output s5,
  output s6,
  output s7
);

  wire not_1_out, not_2_out, not_3_out, not_4_out, not_5_out, not_6_out, not_7_out, not_8_out;

  not not_1 (not_1_out, b0);
  and and_1 (s0, not_1_out, not_2_out);
  not not_2 (not_2_out, b1);
  not not_3 (not_3_out, b0);
  and and_2 (s1, not_3_out, b1);
  and and_3 (s2, b0, not_4_out);
  not not_4 (not_4_out, b1);
  and and_4 (s3, b0, b1);
  not not_5 (not_5_out, b2);
  and and_5 (s4, not_5_out, not_6_out);
  not not_6 (not_6_out, b3);
  not not_7 (not_7_out, b2);
  and and_6 (s5, not_7_out, b3);
  and and_7 (s6, b2, not_8_out);
  not not_8 (not_8_out, b3);
  and and_8 (s7, b2, b3);
endmodule

// Cont
module Contador_0_3 (
  input  in_1,
  input  Pa0,
  output s0,
  output out_4,
  output out_5,
  output s3
);

  wire and_1_out, and_2_out;

  T_Flip_Flop t_ff_1 (.clk(in_1), .T(and_1_out), .Q(s3), .reset(Pa0));  // open: Qn, preset, en
  and and_1 (and_1_out, s0, out_4, out_5);
  and and_2 (and_2_out, s0, out_4);
  T_Flip_Flop t_ff_2 (.clk(in_1), .T(and_2_out), .Q(out_5), .reset(Pa0));  // open: Qn, preset, en
  T_Flip_Flop t_ff_3 (.clk(in_1), .T(s0), .Q(out_4), .reset(Pa0));  // open: Qn, preset, en
  T_Flip_Flop t_ff_4 (.clk(in_1), .T(in_1), .Q(s0), .reset(Pa0));  // open: Qn, preset, en
endmodule

module Celda_de_memoria (
  input  Fila,
  input  Columna,
  input  Pa0,
  input  Pa1,
  input  Pa2,
  input  Pa3,
  output s0,
  output s1,
  output LED
);

  wire and_1_out, control_dig_simult_1_out_5, control_dig_simult_1_out_6, control_dig_simult_1_out_7,
       control_dig_simult_1_out_8, d_ff_1_q, d_ff_2_q, or_1_out, or_2_out, or_3_out, or_4_out;

  and and_1 (and_1_out, Fila, Columna);
  Control_dig__simult control_dig_simult_1 (
    .in_1(Pa0), .in_2(Pa1), .in_3(Pa2), .in_4(Pa3), .out_5(control_dig_simult_1_out_5),
    .out_6(control_dig_simult_1_out_6), .out_7(control_dig_simult_1_out_7), .out_8(control_dig_simult_1_out_8));
  D_Flip_Flop #(.trigger("falling")) d_ff_1 (
    .clk(and_1_out), .D(1'b0), .Q(d_ff_1_q), .preset(or_1_out), .reset(or_2_out));  // open: Qn, en
  or or_1 (or_1_out, control_dig_simult_1_out_7, control_dig_simult_1_out_8);
  or or_2 (or_2_out, control_dig_simult_1_out_5, control_dig_simult_1_out_6);
  or or_3 (or_3_out, control_dig_simult_1_out_6, control_dig_simult_1_out_8);
  D_Flip_Flop #(.trigger("falling")) d_ff_2 (
    .clk(and_1_out), .D(1'b0), .Q(d_ff_2_q), .preset(or_3_out), .reset(or_4_out));  // open: Qn, en
  or or_4 (or_4_out, control_dig_simult_1_out_5, control_dig_simult_1_out_7);
  and and_2 (s0, and_1_out, d_ff_2_q);
  and and_3 (s1, and_1_out, d_ff_1_q);
  or or_5 (LED, d_ff_1_q, d_ff_2_q);
endmodule

// Crl. dig.
module Control_dig__simult (
  input  in_1,
  input  in_2,
  input  in_3,
  input  in_4,
  output out_5,
  output out_6,
  output out_7,
  output out_8
);

  wire xor_1_out, xor_2_out, xor_3_out, xor_4_out;

  ExactlyOne xor_1 (.out(xor_1_out), .in0(in_1), .in1(in_2), .in2(in_3), .in3(in_4));
  ExactlyOne xor_2 (.out(xor_2_out), .in0(in_1), .in1(in_2), .in2(in_3), .in3(in_4));
  ExactlyOne xor_3 (.out(xor_3_out), .in0(in_1), .in1(in_2), .in2(in_3), .in3(in_4));
  ExactlyOne xor_4 (.out(xor_4_out), .in0(in_1), .in1(in_2), .in2(in_3), .in3(in_4));
  and and_1 (out_5, in_1, xor_1_out);
  and and_2 (out_6, in_2, xor_2_out);
  and and_3 (out_7, in_3, xor_3_out);
  and and_4 (out_8, in_4, xor_4_out);
endmodule

module Contador_0_16 (
  input  in_1,
  input  Pa0,
  output b0,
  output b1,
  output b2,
  output b3,
  output b4
);

  wire and_1_out, and_2_out, and_3_out;

  and and_1 (and_1_out, b0, b1, b2, b3);
  T_Flip_Flop t_ff_1 (.clk(in_1), .T(and_1_out), .Q(b4), .reset(Pa0));  // open: Qn, preset, en
  T_Flip_Flop t_ff_2 (.clk(in_1), .T(and_2_out), .Q(b3), .reset(Pa0));  // open: Qn, preset, en
  and and_2 (and_2_out, b0, b1, b2);
  T_Flip_Flop t_ff_3 (.clk(in_1), .T(and_3_out), .Q(b2), .reset(Pa0));  // open: Qn, preset, en
  and and_3 (and_3_out, b0, b1);
  T_Flip_Flop t_ff_4 (.clk(in_1), .T(b0), .Q(b1), .reset(Pa0));  // open: Qn, preset, en
  T_Flip_Flop t_ff_5 (.clk(in_1), .T(in_1), .Q(b0), .reset(Pa0));  // open: Qn, preset, en
endmodule

module CC (
  input  b0,
  input  b1,
  output _1,
  output _2,
  output _3
);

  and and_1 (_1, b0, ~b1);  // AND_Gate
  and and_2 (_2, ~b0, b1);  // AND_Gate
  and and_3 (_3, b0, b1);
endmodule

module _7_segmentos_unidad (
  input  b0,
  input  b1,
  input  b2,
  input  b3,
  input  b4,
  input  b5,
  output a,
  output b,
  output c,
  output d,
  output e,
  output f,
  output g
);

  wire and_1_out, and_2_out, and_3_out, and_4_out, and_5_out, and_6_out, and_7_out, and_8_out, and_9_out,
       and_10_out, and_11_out, and_12_out, and_13_out, and_14_out, and_15_out, and_16_out, and_17_out,
       and_18_out, and_19_out, and_20_out, and_21_out, and_22_out, and_23_out, and_24_out, and_25_out,
       and_26_out, and_27_out, and_28_out, and_29_out, and_30_out, and_31_out, and_32_out, and_33_out,
       and_34_out, and_35_out, and_36_out, and_37_out, and_38_out, and_39_out, and_40_out, and_41_out,
       and_42_out, and_43_out, and_44_out, and_45_out, and_46_out, and_47_out, and_48_out, and_49_out,
       and_50_out, and_51_out, and_52_out, and_53_out, and_54_out, and_55_out, and_56_out, and_57_out,
       and_58_out, and_59_out, and_60_out, and_61_out, and_62_out, and_63_out, and_64_out, and_65_out,
       and_66_out, and_67_out, and_68_out, and_69_out, and_70_out, and_71_out, and_72_out, and_73_out,
       and_74_out, and_75_out, and_76_out, and_77_out, and_78_out, and_79_out, and_80_out, and_81_out,
       and_82_out, and_83_out, and_84_out, and_85_out, and_86_out, and_87_out, and_88_out, and_89_out,
       and_90_out, and_91_out, and_92_out, and_93_out, and_94_out, and_95_out, and_96_out, and_97_out,
       and_98_out, and_99_out, and_100_out, and_101_out, and_102_out, and_103_out, not_1_out, not_2_out,
       not_3_out, not_4_out, not_5_out, not_6_out, not_7_out, not_8_out, not_9_out, not_10_out, not_11_out,
       not_12_out, not_13_out, not_14_out, not_15_out, not_16_out, not_17_out, not_18_out, not_19_out,
       not_20_out, not_21_out, not_22_out, not_23_out, not_24_out, not_25_out, not_26_out, not_27_out,
       not_28_out, not_29_out, not_30_out, not_31_out, not_32_out, not_33_out, not_34_out, not_35_out,
       not_36_out, not_37_out, not_38_out, not_39_out, not_40_out, not_41_out, not_42_out, not_43_out,
       not_44_out, not_45_out, not_46_out, not_47_out, not_48_out, not_49_out, not_50_out, not_51_out,
       not_52_out, not_53_out, not_54_out, not_55_out, not_56_out, not_57_out, not_58_out, not_59_out,
       not_60_out, not_61_out, not_62_out, not_63_out, not_64_out, not_65_out, not_66_out, not_67_out,
       not_68_out, not_69_out, not_70_out, not_71_out, not_72_out, not_73_out, not_74_out, not_75_out,
       not_76_out, not_77_out, not_78_out, not_79_out, not_80_out, not_81_out, not_82_out, not_83_out,
       not_84_out, not_85_out, not_86_out, not_87_out, not_88_out, not_89_out, not_90_out, not_91_out,
       not_92_out, not_93_out, not_94_out, not_95_out, not_96_out, not_97_out, not_98_out, not_99_out,
       not_100_out, not_101_out, not_102_out, not_103_out, not_104_out, not_105_out, not_106_out,
       not_107_out, not_108_out, not_109_out, not_110_out, not_111_out, not_112_out, not_113_out,
       not_114_out, not_115_out, not_116_out, not_117_out, not_118_out, not_119_out, not_120_out,
       not_121_out, not_122_out, not_123_out, not_124_out, not_125_out, not_126_out, not_127_out,
       not_128_out, not_129_out, not_130_out, not_131_out, not_132_out, not_133_out, not_134_out,
       not_135_out, not_136_out, not_137_out, not_138_out, not_139_out, not_140_out, not_141_out,
       not_142_out, not_143_out, not_144_out, not_145_out, not_146_out, not_147_out, not_148_out,
       not_149_out, not_150_out, not_151_out, not_152_out, not_153_out, not_154_out, not_155_out,
       not_156_out, not_157_out, not_158_out, not_159_out, not_160_out, not_161_out, not_162_out,
       not_163_out, not_164_out, not_165_out, not_166_out, not_167_out, not_168_out, not_169_out,
       not_170_out, not_171_out, not_172_out, not_173_out, not_174_out, not_175_out, not_176_out,
       not_177_out, not_178_out, not_179_out, not_180_out, not_181_out, not_182_out, not_183_out,
       not_184_out, not_185_out, not_186_out, not_187_out, not_188_out, not_189_out, not_190_out,
       not_191_out, not_192_out, not_193_out, not_194_out, not_195_out, not_196_out, not_197_out,
       not_198_out, not_199_out, not_200_out, not_201_out, not_202_out, not_203_out, not_204_out,
       not_205_out, not_206_out, not_207_out, not_208_out, not_209_out, not_210_out, not_211_out,
       not_212_out, not_213_out, not_214_out, not_215_out, not_216_out, not_217_out, not_218_out,
       not_219_out, not_220_out, not_221_out, not_222_out;

  not not_1 (not_1_out, b0);
  not not_2 (not_2_out, b2);
  not not_3 (not_3_out, b3);
  not not_4 (not_4_out, b0);
  not not_5 (not_5_out, b1);
  not not_6 (not_6_out, b4);
  not not_7 (not_7_out, b1);
  not not_8 (not_8_out, b5);
  not not_9 (not_9_out, b0);
  not not_10 (not_10_out, b4);
  not not_11 (not_11_out, b0);
  not not_12 (not_12_out, b1);
  not not_13 (not_13_out, b4);
  not not_14 (not_14_out, b0);
  not not_15 (not_15_out, b3);
  not not_16 (not_16_out, b5);
  not not_17 (not_17_out, b3);
  not not_18 (not_18_out, b4);
  not not_19 (not_19_out, b5);
  not not_20 (not_20_out, b2);
  not not_21 (not_21_out, b1);
  not not_22 (not_22_out, b2);
  not not_23 (not_23_out, b3);
  not not_24 (not_24_out, b1);
  not not_25 (not_25_out, b2);
  not not_26 (not_26_out, b3);
  not not_27 (not_27_out, b2);
  not not_28 (not_28_out, b4);
  not not_29 (not_29_out, b0);
  not not_30 (not_30_out, b2);
  not not_31 (not_31_out, b4);
  not not_32 (not_32_out, b5);
  not not_33 (not_33_out, b0);
  not not_34 (not_34_out, b1);
  not not_35 (not_35_out, b2);
  not not_36 (not_36_out, b4);
  not not_37 (not_37_out, b1);
  not not_38 (not_38_out, b2);
  not not_39 (not_39_out, b5);
  not not_40 (not_40_out, b0);
  not not_41 (not_41_out, b3);
  not not_42 (not_42_out, b4);
  not not_43 (not_43_out, b0);
  not not_44 (not_44_out, b3);
  not not_45 (not_45_out, b5);
  not not_46 (not_46_out, b3);
  not not_47 (not_47_out, b4);
  not not_48 (not_48_out, b5);
  not not_49 (not_49_out, b0);
  not not_50 (not_50_out, b1);
  not not_51 (not_51_out, b3);
  not not_52 (not_52_out, b5);
  not not_53 (not_53_out, b0);
  not not_54 (not_54_out, b2);
  not not_55 (not_55_out, b3);
  not not_56 (not_56_out, b0);
  not not_57 (not_57_out, b4);
  not not_58 (not_58_out, b5);
  not not_59 (not_59_out, b1);
  not not_60 (not_60_out, b2);
  not not_61 (not_61_out, b1);
  not not_62 (not_62_out, b5);
  not not_63 (not_63_out, b2);
  not not_64 (not_64_out, b4);
  not not_65 (not_65_out, b2);
  not not_66 (not_66_out, b3);
  not not_67 (not_67_out, b4);
  not not_68 (not_68_out, b1);
  not not_69 (not_69_out, b3);
  not not_70 (not_70_out, b4);
  not not_71 (not_71_out, b5);
  not not_72 (not_72_out, b0);
  not not_73 (not_73_out, b2);
  not not_74 (not_74_out, b0);
  not not_75 (not_75_out, b3);
  not not_76 (not_76_out, b5);
  not not_77 (not_77_out, b1);
  not not_78 (not_78_out, b0);
  not not_79 (not_79_out, b1);
  not not_80 (not_80_out, b4);
  not not_81 (not_81_out, b0);
  not not_82 (not_82_out, b4);
  not not_83 (not_83_out, b0);
  not not_84 (not_84_out, b2);
  not not_85 (not_85_out, b5);
  not not_86 (not_86_out, b2);
  not not_87 (not_87_out, b3);
  not not_88 (not_88_out, b5);
  not not_89 (not_89_out, b0);
  not not_90 (not_90_out, b3);
  not not_91 (not_91_out, b0);
  not not_92 (not_92_out, b5);
  not not_93 (not_93_out, b2);
  not not_94 (not_94_out, b4);
  not not_95 (not_95_out, b1);
  not not_96 (not_96_out, b2);
  not not_97 (not_97_out, b1);
  not not_98 (not_98_out, b2);
  not not_99 (not_99_out, b4);
  not not_100 (not_100_out, b0);
  not not_101 (not_101_out, b1);
  not not_102 (not_102_out, b3);
  not not_103 (not_103_out, b0);
  not not_104 (not_104_out, b1);
  not not_105 (not_105_out, b4);
  not not_106 (not_106_out, b5);
  not not_107 (not_107_out, b1);
  not not_108 (not_108_out, b3);
  not not_109 (not_109_out, b4);
  not not_110 (not_110_out, b0);
  not not_111 (not_111_out, b2);
  not not_112 (not_112_out, b3);
  not not_113 (not_113_out, b0);
  not not_114 (not_114_out, b2);
  not not_115 (not_115_out, b3);
  not not_116 (not_116_out, b0);
  not not_117 (not_117_out, b2);
  not not_118 (not_118_out, b0);
  not not_119 (not_119_out, b3);
  not not_120 (not_120_out, b0);
  not not_121 (not_121_out, b1);
  not not_122 (not_122_out, b4);
  not not_123 (not_123_out, b0);
  not not_124 (not_124_out, b1);
  not not_125 (not_125_out, b5);
  not not_126 (not_126_out, b0);
  not not_127 (not_127_out, b4);
  not not_128 (not_128_out, b5);
  not not_129 (not_129_out, b4);
  not not_130 (not_130_out, b5);
  not not_131 (not_131_out, b0);
  not not_132 (not_132_out, b3);
  not not_133 (not_133_out, b4);
  not not_134 (not_134_out, b2);
  not not_135 (not_135_out, b5);
  not not_136 (not_136_out, b1);
  not not_137 (not_137_out, b2);
  not not_138 (not_138_out, b3);
  not not_139 (not_139_out, b1);
  not not_140 (not_140_out, b2);
  not not_141 (not_141_out, b3);
  not not_142 (not_142_out, b2);
  not not_143 (not_143_out, b4);
  not not_144 (not_144_out, b0);
  not not_145 (not_145_out, b2);
  not not_146 (not_146_out, b4);
  not not_147 (not_147_out, b1);
  not not_148 (not_148_out, b2);
  not not_149 (not_149_out, b3);
  not not_150 (not_150_out, b4);
  not not_151 (not_151_out, b0);
  not not_152 (not_152_out, b3);
  not not_153 (not_153_out, b2);
  not not_154 (not_154_out, b1);
  not not_155 (not_155_out, b0);
  not not_156 (not_156_out, b1);
  not not_157 (not_157_out, b3);
  not not_158 (not_158_out, b5);
  not not_159 (not_159_out, b0);
  not not_160 (not_160_out, b2);
  not not_161 (not_161_out, b3);
  not not_162 (not_162_out, b0);
  not not_163 (not_163_out, b1);
  not not_164 (not_164_out, b4);
  not not_165 (not_165_out, b1);
  not not_166 (not_166_out, b2);
  not not_167 (not_167_out, b5);
  not not_168 (not_168_out, b0);
  not not_169 (not_169_out, b1);
  not not_170 (not_170_out, b4);
  not not_171 (not_171_out, b0);
  not not_172 (not_172_out, b4);
  not not_173 (not_173_out, b0);
  not not_174 (not_174_out, b1);
  not not_175 (not_175_out, b4);
  not not_176 (not_176_out, b0);
  not not_177 (not_177_out, b2);
  not not_178 (not_178_out, b5);
  not not_179 (not_179_out, b0);
  not not_180 (not_180_out, b2);
  not not_181 (not_181_out, b3);
  not not_182 (not_182_out, b5);
  not not_183 (not_183_out, b5);
  not not_184 (not_184_out, b2);
  not not_185 (not_185_out, b3);
  not not_186 (not_186_out, b4);
  not not_187 (not_187_out, b2);
  not not_188 (not_188_out, b4);
  not not_189 (not_189_out, b5);
  not not_190 (not_190_out, b1);
  not not_191 (not_191_out, b2);
  not not_192 (not_192_out, b3);
  not not_193 (not_193_out, b5);
  not not_194 (not_194_out, b3);
  not not_195 (not_195_out, b5);
  not not_196 (not_196_out, b0);
  not not_197 (not_197_out, b1);
  not not_198 (not_198_out, b3);
  not not_199 (not_199_out, b5);
  not not_200 (not_200_out, b1);
  not not_201 (not_201_out, b2);
  not not_202 (not_202_out, b5);
  not not_203 (not_203_out, b0);
  not not_204 (not_204_out, b1);
  not not_205 (not_205_out, b4);
  not not_206 (not_206_out, b5);
  not not_207 (not_207_out, b0);
  not not_208 (not_208_out, b2);
  not not_209 (not_209_out, b5);
  not not_210 (not_210_out, b3);
  not not_211 (not_211_out, b5);
  not not_212 (not_212_out, b0);
  not not_213 (not_213_out, b5);
  not not_214 (not_214_out, b2);
  not not_215 (not_215_out, b4);
  not not_216 (not_216_out, b5);
  not not_217 (not_217_out, b3);
  not not_218 (not_218_out, b5);
  not not_219 (not_219_out, b1);
  not not_220 (not_220_out, b5);
  not not_221 (not_221_out, b4);
  not not_222 (not_222_out, b5);
  and and_1 (and_1_out, not_1_out, not_2_out, not_3_out, b4);
  and and_2 (and_2_out, not_4_out, not_5_out, b3, not_6_out);
  and and_3 (and_3_out, not_7_out, b3, not_8_out);
  and and_4 (and_4_out, not_9_out, b2, not_10_out);
  and and_5 (and_5_out, not_11_out, not_12_out, b2, b3);
  and and_6 (and_6_out, b2, b3, not_13_out, b5);
  and and_7 (and_7_out, not_14_out, b1, not_15_out, not_16_out);
  and and_8 (and_8_out, b1, not_17_out, not_18_out, not_19_out);
  and and_9 (and_9_out, b1, not_20_out, b3, b4);
  and and_10 (and_10_out, b0, not_21_out, not_22_out, not_23_out);
  and and_11 (and_11_out, b0, not_24_out, not_25_out, b4);
  and and_12 (and_12_out, b0, b2, not_26_out, b4);
  and and_13 (and_13_out, b0, b1, not_27_out, not_28_out);
  and and_14 (and_14_out, b0, b1, b2, b4);
  and and_15 (and_15_out, not_29_out, not_30_out, not_31_out, not_32_out);
  and and_16 (and_16_out, not_33_out, not_34_out, not_35_out, b3, not_36_out);
  and and_17 (and_17_out, not_37_out, not_38_out, b3, not_39_out);
  and and_18 (and_18_out, not_40_out, b2, not_41_out, not_42_out);
  and and_19 (and_19_out, not_43_out, b2, not_44_out, not_45_out);
  and and_20 (and_20_out, b2, not_46_out, not_47_out, not_48_out);
  and and_21 (and_21_out, not_49_out, not_50_out, b2, b3, b4);
  and and_22 (and_22_out, b1, not_51_out, not_52_out);
  and and_23 (and_23_out, not_53_out, b1, not_54_out, not_55_out, b4);
  and and_24 (and_24_out, not_56_out, b1, b2, not_57_out);
  and and_25 (and_25_out, b1, b2, not_58_out);
  and and_26 (and_26_out, b0, not_59_out, not_60_out, b4);
  and and_27 (and_27_out, b0, not_61_out, b3, not_62_out);
  and and_28 (and_28_out, b0, not_63_out, b3, b4);
  and and_29 (and_29_out, b0, b2, b3, not_64_out);
  and and_30 (and_30_out, b0, b1, not_65_out, not_66_out, not_67_out);
  and and_31 (and_31_out, b0, b1, b2, b4);
  and and_32 (and_32_out, not_68_out, not_69_out, not_70_out, not_71_out);
  and and_33 (and_33_out, not_72_out, not_73_out, b4);
  and and_34 (and_34_out, not_74_out, not_75_out, b4, not_76_out);
  and and_35 (and_35_out, not_77_out, b3, b5);
  and and_36 (and_36_out, not_78_out, not_79_out, b2, not_80_out);
  and and_37 (and_37_out, not_81_out, b2, b3, not_82_out);
  and and_38 (and_38_out, not_83_out, b1, not_84_out, not_85_out);
  and and_39 (and_39_out, b1, not_86_out, not_87_out, not_88_out);
  and and_40 (and_40_out, not_89_out, b1, not_90_out, b5);
  and and_41 (and_41_out, not_91_out, b1, b3, not_92_out);
  and and_42 (and_42_out, b0, not_93_out, not_94_out);
  and and_43 (and_43_out, b0, not_95_out, not_96_out, b5);
  and and_44 (and_44_out, b0, not_97_out, not_98_out, b3);
  and and_45 (and_45_out, b0, b3, b5);
  and and_46 (and_46_out, b0, b2, b4);
  and and_47 (and_47_out, b0, b1, not_99_out);
  and and_48 (and_48_out, not_100_out, not_101_out, not_102_out);
  and and_49 (and_49_out, not_103_out, not_104_out, not_105_out, not_106_out);
  and and_50 (and_50_out, not_107_out, not_108_out, not_109_out);
  and and_51 (and_51_out, not_110_out, not_111_out, not_112_out, b5);
  and and_52 (and_52_out, not_113_out, not_114_out, not_115_out, b4);
  and and_53 (and_53_out, not_116_out, not_117_out, b4, b5);
  and and_54 (and_54_out, not_118_out, not_119_out, b4, b5);
  and and_55 (and_55_out, not_120_out, not_121_out, b2, not_122_out);
  and and_56 (and_56_out, not_123_out, not_124_out, b2, not_125_out);
  and and_57 (and_57_out, not_126_out, b2, not_127_out, not_128_out);
  and and_58 (and_58_out, b2, b3, not_129_out, not_130_out);
  and and_59 (and_59_out, not_131_out, b1, b3);
  and and_60 (and_60_out, b0, not_132_out, not_133_out, b5);
  and and_61 (and_61_out, b0, not_134_out, b4, not_135_out);
  and and_62 (and_62_out, b0, not_136_out, not_137_out, b3, b5);
  and and_63 (and_63_out, b0, b2, not_138_out, b4);
  and and_64 (and_64_out, b0, not_139_out, b2, b4, b5);
  and and_65 (and_65_out, b0, b1, not_140_out, not_141_out);
  and and_66 (and_66_out, b0, b1, not_142_out, not_143_out);
  and and_67 (and_67_out, not_144_out, not_145_out, not_146_out);
  and and_68 (and_68_out, not_147_out, not_148_out, b3);
  and and_69 (and_69_out, b2, not_149_out, not_150_out);
  and and_70 (and_70_out, not_151_out, b2, b4);
  and and_71 (and_71_out, b1, not_152_out);
  and and_72 (and_72_out, b1, b2);
  and and_73 (and_73_out, b0, not_153_out, b4);
  and and_74 (and_74_out, b0, not_154_out, b3);
  and and_75 (and_75_out, not_155_out, not_156_out, not_157_out, not_158_out);
  and and_76 (and_76_out, not_159_out, not_160_out, not_161_out, b4);
  and and_77 (and_77_out, not_162_out, not_163_out, b3, not_164_out, b5);
  and and_78 (and_78_out, not_165_out, not_166_out, b3, b4, not_167_out);
  and and_79 (and_79_out, not_168_out, not_169_out, b2, not_170_out);
  and and_80 (and_80_out, not_171_out, b2, not_172_out, b5);
  and and_81 (and_81_out, not_173_out, not_174_out, b2, b3, b5);
  and and_82 (and_82_out, b2, b3, not_175_out, b5);
  and and_83 (and_83_out, not_176_out, b1, not_177_out, not_178_out);
  and and_84 (and_84_out, not_179_out, b1, not_180_out, b4);
  and and_85 (and_85_out, b1, not_181_out, b4, not_182_out);
  and and_86 (and_86_out, b1, b2, b3, not_183_out);
  and and_87 (and_87_out, b0, not_184_out, not_185_out, not_186_out);
  and and_88 (and_88_out, b0, not_187_out, not_188_out, not_189_out);
  and and_89 (and_89_out, b0, not_190_out, not_191_out, b4, b5);
  and and_90 (and_90_out, b0, b2, not_192_out, not_193_out);
  and and_91 (and_91_out, b0, b2, not_194_out, b4);
  and and_92 (and_92_out, b0, b2, b4, not_195_out);
  and and_93 (and_93_out, b0, b1, b3, b5);
  and and_94 (and_94_out, not_196_out, not_197_out, not_198_out, not_199_out);
  and and_95 (and_95_out, not_200_out, not_201_out, b3, b4, not_202_out);
  and and_96 (and_96_out, not_203_out, not_204_out, b2, not_205_out, not_206_out);
  and and_97 (and_97_out, not_207_out, b1, not_208_out, not_209_out);
  and and_98 (and_98_out, b1, not_210_out, b4, not_211_out);
  and and_99 (and_99_out, not_212_out, b1, b3, not_213_out);
  and and_100 (and_100_out, b0, not_214_out, not_215_out, not_216_out);
  and and_101 (and_101_out, b0, b2, not_217_out, not_218_out);
  and and_102 (and_102_out, b0, not_219_out, b2, b4, not_220_out);
  and and_103 (and_103_out, b0, b1, not_221_out, not_222_out);
  or or_1 (e, and_67_out, b5, and_68_out, and_69_out, and_70_out, and_71_out, and_72_out, and_73_out, and_74_out);
  or or_2 (g, and_94_out, and_95_out, and_96_out, and_97_out, and_98_out, and_99_out, and_100_out, and_101_out, and_102_out, and_103_out);
  or or_3 (a, and_1_out, and_2_out, and_3_out, and_4_out, and_5_out, and_6_out, and_7_out, and_8_out, and_9_out, and_10_out, and_11_out, and_12_out, and_13_out, and_14_out);
  or or_4 (b, and_15_out, and_16_out, and_17_out, and_18_out, and_19_out, and_20_out, and_21_out, and_22_out, and_23_out, and_24_out, and_25_out, and_26_out, and_27_out, and_28_out, and_29_out, and_30_out, and_31_out);
  or or_5 (c, and_32_out, and_33_out, and_34_out, and_35_out, and_36_out, and_37_out, and_38_out, and_39_out, and_40_out, and_41_out, and_42_out, and_43_out, and_44_out, and_45_out, and_46_out, and_47_out);
  or or_6 (d, and_48_out, and_49_out, and_50_out, and_51_out, and_52_out, and_53_out, and_54_out, and_55_out, and_56_out, and_57_out, and_58_out, and_59_out, and_60_out, and_61_out, and_62_out, and_63_out, and_64_out, and_65_out, and_66_out);
  or or_7 (f, and_75_out, and_76_out, and_77_out, and_78_out, and_79_out, and_80_out, and_81_out, and_82_out, and_83_out, and_84_out, and_85_out, and_86_out, and_87_out, and_88_out, and_89_out, and_90_out, and_91_out, and_92_out, and_93_out);
endmodule

module _7_segmentos_decena (
  input  b0,
  input  b1,
  input  b2,
  input  b3,
  input  b4,
  input  b5,
  output s0,
  output s1,
  output s2,
  output s3,
  output s4,
  output s5,
  output s6
);

  wire and_1_out, and_2_out, and_3_out, and_4_out, and_5_out, and_6_out, and_7_out, and_8_out, and_9_out,
       and_10_out, and_11_out, and_12_out, and_13_out, and_14_out, and_15_out, and_16_out, and_17_out,
       and_18_out, and_19_out, and_20_out, and_21_out, not_1_out, not_2_out, not_3_out, not_4_out, not_5_out,
       not_6_out, not_7_out, not_8_out, not_9_out, not_10_out, not_11_out, not_12_out, not_13_out,
       not_14_out, not_15_out, not_16_out, not_17_out, not_18_out, not_19_out, not_20_out, not_21_out,
       not_22_out, not_23_out, not_24_out, not_25_out, not_26_out, not_27_out, not_28_out, not_29_out,
       not_30_out, not_31_out, not_32_out, not_33_out, not_34_out, not_35_out;

  and and_1 (and_1_out, b1, b3);
  and and_2 (and_2_out, b1, b2);
  not not_1 (not_1_out, b0);
  not not_2 (not_2_out, b1);
  not not_3 (not_3_out, b2);
  not not_4 (not_4_out, b0);
  not not_5 (not_5_out, b1);
  not not_6 (not_6_out, b3);
  not not_7 (not_7_out, b4);
  not not_8 (not_8_out, b0);
  not not_9 (not_9_out, b1);
  not not_10 (not_10_out, b3);
  not not_11 (not_11_out, b4);
  not not_12 (not_12_out, b1);
  not not_13 (not_13_out, b2);
  not not_14 (not_14_out, b2);
  not not_15 (not_15_out, b2);
  not not_16 (not_16_out, b3);
  not not_17 (not_17_out, b0);
  not not_18 (not_18_out, b1);
  not not_19 (not_19_out, b3);
  not not_20 (not_20_out, b4);
  not not_21 (not_21_out, b1);
  not not_22 (not_22_out, b2);
  not not_23 (not_23_out, b2);
  not not_24 (not_24_out, b0);
  not not_25 (not_25_out, b1);
  not not_26 (not_26_out, b2);
  not not_27 (not_27_out, b0);
  not not_28 (not_28_out, b1);
  not not_29 (not_29_out, b3);
  not not_30 (not_30_out, b4);
  not not_31 (not_31_out, b0);
  not not_32 (not_32_out, b2);
  not not_33 (not_33_out, b3);
  not not_34 (not_34_out, b4);
  or or_1 (s0, and_1_out, and_2_out, b0);
  and and_3 (and_3_out, not_1_out, not_2_out, not_3_out);
  and and_4 (and_4_out, not_4_out, not_5_out, not_6_out, not_7_out);
  and and_5 (and_5_out, b0, b2);
  and and_6 (and_6_out, b0, b1);
  and and_7 (and_7_out, not_8_out, not_9_out, not_10_out, not_11_out);
  and and_8 (and_8_out, not_12_out, not_13_out);
  and and_9 (and_9_out, not_14_out, b3);
  and and_10 (and_10_out, b1, b2);
  not not_35 (not_35_out, b1);
  and and_11 (and_11_out, not_15_out, not_16_out);
  and and_12 (and_12_out, b2, b3, b4);
  and and_13 (and_13_out, not_17_out, not_18_out, not_19_out, not_20_out);
  and and_14 (and_14_out, not_21_out, not_22_out);
  and and_15 (and_15_out, not_23_out, b3);
  and and_16 (and_16_out, b1, b2);
  and and_17 (and_17_out, not_24_out, not_25_out, not_26_out);
  and and_18 (and_18_out, not_27_out, not_28_out, not_29_out, not_30_out);
  and and_19 (and_19_out, not_31_out, not_32_out, b3);
  and and_20 (and_20_out, b1, b2, not_33_out);
  and and_21 (and_21_out, b1, b2, not_34_out);
  or or_2 (s1, and_3_out, and_4_out, and_5_out, and_6_out);
  or or_3 (s2, and_7_out, and_8_out, and_9_out, and_10_out);
  or or_4 (s4, not_35_out, and_11_out, and_12_out);
  or or_5 (s5, and_13_out, and_14_out, and_15_out, and_16_out);
  or or_6 (s6, and_17_out, and_18_out, and_19_out, and_20_out, and_21_out);

  assign s3 = 1'b1;
endmodule

// 7 segmentos
module _7_segmentos_total (
  input  b0,
  input  b1,
  input  b2,
  input  b3,
  input  b4,
  input  b5,
  output u0,
  output out_8,
  output out_9,
  output out_10,
  output out_11,
  output out_12,
  output out_13,
  output d0,
  output out_15,
  output out_16,
  output out_17,
  output out_18,
  output out_19,
  output out_20
);

  _7_segmentos_unidad u_7_segmentos_unidad_1 (
    .b0(b5), .b1(b4), .b2(b3), .b3(b2), .b4(b1), .b5(b0), .a(u0), .b(out_8), .c(out_9), .d(out_10),
    .e(out_11), .f(out_12), .g(out_13));
  _7_segmentos_decena u_7_segmentos_decena_1 (
    .b0(b5), .b1(b4), .b2(b3), .b3(b2), .b4(b1), .b5(b0), .s0(d0), .s1(out_15), .s2(out_16), .s3(out_17),
    .s4(out_18), .s5(out_19), .s6(out_20));
endmodule
