// Logisim project tp.circ as structural Verilog: 10 circuits, main circuit celdaMemoria
module main (
  input  [7:0] in_1,
  input  verImagenDeJuego
);

  wire aceptarNombre_out, avanzar_out, button_5_out, button_6_out, button_7_out, button_8_out,
       celdamemoria_1_out_5, celdamemoria_1_out_6, celdamemoria_1_out_7, clock_1_out, counter_1_carry,
       goma_out, hielo_out, ingresarPuntos_out, pozo_out, premio_out, reiniciarPantalla_out, retroceder_out,
       rgbled_1_p2, rgbled_1_p5, rgbled_1_p6, rgbled_1_p7, rgbled_1_p8, rgbled_1_p9, rgbled_1_p10,
       rgbled_1_p11, rgbled_1_p12, rgbled_1_p13, rgbled_1_p14, rgbled_1_p15, selectorturnos_1_out_2,
       selectorturnos_1_out_3, selectorturnos_1_out_4, selectorturnos_1_out_5, undriven;
  wire [3:0] button_3_out, memoriaPuntos_out_7, memoriaPuntos_out_7_2, memoriaPuntos_out_7_3,
       memoriaPuntos_out_8, memoriaPuntos_out_8_2, memoriaPuntos_out_8_3, memoriaPuntos_out_9,
       memoriaPuntos_out_9_2, memoriaPuntos_out_9_3, memoriaPuntos_out_10, memoriaPuntos_out_10_2,
       memoriaPuntos_out_10_3;
  wire [4:0] letras_1_out_3, letras_2_out_3, letras_3_out_3, memorianombres_1_nombrejugador1,
       memorianombres_1_nombrejugador1_2, memorianombres_1_nombrejugador1_3, memorianombres_1_nombrejugador2,
       memorianombres_1_nombrejugador2_2, memorianombres_1_nombrejugador2_3, memorianombres_1_nombrejugador3,
       memorianombres_1_nombrejugador3_2, memorianombres_1_nombrejugador3_3, memorianombres_1_nombrejugador4,
       memorianombres_1_nombrejugador4_2, memorianombres_1_nombrejugador4_3;
  wire [7:0] counter_1_q, counter_2_q;
  wire [8:0] alfabeto_1_s0, alfabeto_1_s1, alfabeto_1_s2, alfabeto_1_s3, alfabeto_1_s4, alfabeto_1_s5,
       alfabeto_2_s0, alfabeto_2_s1, alfabeto_2_s2, alfabeto_2_s3, alfabeto_2_s4, alfabeto_2_s5,
       alfabeto_3_s0, alfabeto_3_s1, alfabeto_3_s2, alfabeto_3_s3, alfabeto_3_s4, alfabeto_3_s5,
       alfabeto_4_s0, alfabeto_4_s1, alfabeto_4_s2, alfabeto_4_s3, alfabeto_4_s4, alfabeto_4_s5,
       alfabeto_5_s0, alfabeto_5_s1, alfabeto_5_s2, alfabeto_5_s3, alfabeto_5_s4, alfabeto_5_s5,
       alfabeto_6_s0, alfabeto_6_s1, alfabeto_6_s2, alfabeto_6_s3, alfabeto_6_s4, alfabeto_6_s5,
       alfabeto_7_s0, alfabeto_7_s1, alfabeto_7_s2, alfabeto_7_s3, alfabeto_7_s4, alfabeto_7_s5,
       alfabeto_8_s0, alfabeto_8_s1, alfabeto_8_s2, alfabeto_8_s3, alfabeto_8_s4, alfabeto_8_s5,
       alfabeto_9_s0, alfabeto_9_s1, alfabeto_9_s2, alfabeto_9_s3, alfabeto_9_s4, alfabeto_9_s5,
       alfabeto_10_s0, alfabeto_10_s1, alfabeto_10_s2, alfabeto_10_s3, alfabeto_10_s4, alfabeto_10_s5,
       alfabeto_11_s0, alfabeto_11_s1, alfabeto_11_s2, alfabeto_11_s3, alfabeto_11_s4, alfabeto_11_s5,
       alfabeto_12_s0, alfabeto_12_s1, alfabeto_12_s2, alfabeto_12_s3, alfabeto_12_s4, alfabeto_12_s5,
       alfabeto_13_s0, alfabeto_13_s1, alfabeto_13_s2, alfabeto_13_s3, alfabeto_13_s4, alfabeto_13_s5,
       alfabeto_14_s0, alfabeto_14_s1, alfabeto_14_s2, alfabeto_14_s3, alfabeto_14_s4, alfabeto_14_s5,
       alfabeto_15_s0, alfabeto_15_s1, alfabeto_15_s2, alfabeto_15_s3, alfabeto_15_s4, alfabeto_15_s5,
       numeros_10_s0, numeros_10_s1, numeros_10_s2, numeros_10_s3, numeros_10_s4, numeros_10_s5,
       numeros_11_s0, numeros_11_s1, numeros_11_s2, numeros_11_s3, numeros_11_s4, numeros_11_s5,
       numeros_12_s0, numeros_12_s1, numeros_12_s2, numeros_12_s3, numeros_12_s4, numeros_12_s5;
  wire [23:0] rgb_video_1_p4;
  wire [53:0] numeros_1_s5, numeros_2_s5, numeros_3_s5, numeros_4_s5, numeros_5_s5, numeros_6_s5,
       numeros_7_s5, numeros_8_s5, numeros_9_s5;

  Button reiniciarPantalla (.out(reiniciarPantalla_out));
  Clock clock_1 (.out(clock_1_out));
  Counter counter_1 (
    .clr(reiniciarPantalla_out), .count(verImagenDeJuego), .clk(clock_1_out), .carry(counter_1_carry),
    .Q(counter_1_q));  // open: load, up, D
  Counter counter_2 (
    .clr(reiniciarPantalla_out), .count(verImagenDeJuego), .clk(counter_1_carry), .Q(counter_2_q));  // open: load, up, D, carry
  Button pozo (.out(pozo_out));
  Button goma (.out(goma_out));
  Button premio (.out(premio_out));
  Button hielo (.out(hielo_out));
  Button button_1 (.out(button_3_out[3]));
  Button button_2 (.out(button_3_out[1]));
  Button button_3 (.out(button_3_out[0]));
  Button button_4 (.out(button_3_out[2]));
  // RGB_Video #(.cursor("No Cursor"), .height(256), .width(256)) rgb_video_1: pin names not known; wires that end beside it: reiniciarPantalla_out, clock_1_out, verImagenDeJuego, rgb_video_1_p4
  celdaMemoria celdamemoria_1 (
    .in_1(pozo_out), .in_2(goma_out), .in_3(premio_out), .in_4(hielo_out), .out_5(celdamemoria_1_out_5),
    .out_6(celdamemoria_1_out_6), .out_7(celdamemoria_1_out_7));
  // RGBLED rgbled_1: pin names not known; wires that end beside it: celdamemoria_1_out_7, rgbled_1_p2, celdamemoria_1_out_6, celdamemoria_1_out_5, rgbled_1_p5, rgbled_1_p6, rgbled_1_p7, rgbled_1_p8, rgbled_1_p9, rgbled_1_p10, rgbled_1_p11, rgbled_1_p12, rgbled_1_p13, rgbled_1_p14, rgbled_1_p15
  posicion posicion_1 (
    .newGame(aceptarNombre_out), .derecha(button_3_out[0]), .izquierda(button_3_out[1]),
    .abajo(button_3_out[2]), .arriba(button_3_out[3]), .h0(rgbled_1_p2), .out_7(rgbled_1_p5),
    .out_8(rgbled_1_p6), .out_9(rgbled_1_p7), .out_10(rgbled_1_p8), .out_11(rgbled_1_p9),
    .out_12(rgbled_1_p10), .out_13(rgbled_1_p11), .out_14(rgbled_1_p12), .out_15(rgbled_1_p13),
    .out_16(rgbled_1_p14), .out_17(rgbled_1_p15));
  Button ingresarPuntos (.out(ingresarPuntos_out));
  ROM #(.addrWidth(16), .dataWidth(24)) rom_1 (.addr({counter_1_q, counter_2_q}), .data(rgb_video_1_p4));
  Button avanzar (.out(avanzar_out));
  letras letras_1 (.adelante(avanzar_out), .atras(retroceder_out), .out_3(letras_1_out_3));
  Button retroceder (.out(retroceder_out));
  Button button_5 (.out(button_5_out));
  letras letras_2 (.adelante(button_5_out), .atras(button_6_out), .out_3(letras_2_out_3));
  Button button_6 (.out(button_6_out));
  Button button_7 (.out(button_7_out));
  letras letras_3 (.adelante(button_7_out), .atras(button_8_out), .out_3(letras_3_out_3));
  Button button_8 (.out(button_8_out));
  Button aceptarNombre (.out(aceptarNombre_out));
  selectorTurnos selectorturnos_1 (
    .in_1(undriven), .out_2(selectorturnos_1_out_2), .out_3(selectorturnos_1_out_3),
    .out_4(selectorturnos_1_out_4), .out_5(selectorturnos_1_out_5));
  DotMatrix #(.matrixcols(8), .matrixrows(9)) dotmatrix_1 (
    .col0({9{1'b0}}), .col1(alfabeto_1_s5), .col2(alfabeto_1_s4), .col3(alfabeto_1_s3), .col4(alfabeto_1_s2),
    .col5(alfabeto_1_s1), .col6(alfabeto_1_s0), .col7({9{1'b0}}));
  alfabeto alfabeto_1 (
    .e(letras_1_out_3), .s0(alfabeto_1_s0), .s1(alfabeto_1_s1), .s2(alfabeto_1_s2), .s3(alfabeto_1_s3),
    .s4(alfabeto_1_s4), .s5(alfabeto_1_s5));
  alfabeto alfabeto_2 (
    .e(letras_2_out_3), .s0(alfabeto_2_s0), .s1(alfabeto_2_s1), .s2(alfabeto_2_s2), .s3(alfabeto_2_s3),
    .s4(alfabeto_2_s4), .s5(alfabeto_2_s5));
  alfabeto alfabeto_3 (
    .e(letras_3_out_3), .s0(alfabeto_3_s0), .s1(alfabeto_3_s1), .s2(alfabeto_3_s2), .s3(alfabeto_3_s3),
    .s4(alfabeto_3_s4), .s5(alfabeto_3_s5));
  DotMatrix #(.matrixcols(8), .matrixrows(9)) dotmatrix_2 (
    .col0({9{1'b0}}), .col1(alfabeto_2_s5), .col2(alfabeto_2_s4), .col3(alfabeto_2_s3), .col4(alfabeto_2_s2),
    .col5(alfabeto_2_s1), .col6(alfabeto_2_s0), .col7({9{1'b0}}));
  DotMatrix #(.matrixcols(8), .matrixrows(9)) dotmatrix_3 (
    .col0({9{1'b0}}), .col1(alfabeto_3_s5), .col2(alfabeto_3_s4), .col3(alfabeto_3_s3), .col4(alfabeto_3_s2),
    .col5(alfabeto_3_s1), .col6(alfabeto_3_s0), .col7({9{1'b0}}));
  memoriaDePuntos memoriaPuntos (
    .in_1(in_1), .habilitacion(ingresarPuntos_out), .jug1(selectorturnos_1_out_2),
    .jug2(selectorturnos_1_out_3), .jug3(selectorturnos_1_out_4), .jug4(selectorturnos_1_out_5),
    .out_7({memoriaPuntos_out_7_3, memoriaPuntos_out_7_2, memoriaPuntos_out_7}),
    .out_8({memoriaPuntos_out_8_3, memoriaPuntos_out_8_2, memoriaPuntos_out_8}),
    .out_9({memoriaPuntos_out_9_3, memoriaPuntos_out_9_2, memoriaPuntos_out_9}),
    .out_10({memoriaPuntos_out_10_3, memoriaPuntos_out_10_2, memoriaPuntos_out_10}));
  memoriaNombres memorianombres_1 (
    .nombre({letras_3_out_3, letras_2_out_3, letras_1_out_3}), .habilitacionCargaNombre(aceptarNombre_out),
    .jug1(selectorturnos_1_out_2), .jug2(selectorturnos_1_out_3), .jug3(selectorturnos_1_out_4),
    .jug4(selectorturnos_1_out_5),
    .nombreJugador1({memorianombres_1_nombrejugador1_3, memorianombres_1_nombrejugador1_2, memorianombres_1_nombrejugador1}),
    .nombreJugador2({memorianombres_1_nombrejugador2_3, memorianombres_1_nombrejugador2_2, memorianombres_1_nombrejugador2}),
    .nombreJugador3({memorianombres_1_nombrejugador3_3, memorianombres_1_nombrejugador3_2, memorianombres_1_nombrejugador3}),
    .nombreJugador4({memorianombres_1_nombrejugador4_3, memorianombres_1_nombrejugador4_2, memorianombres_1_nombrejugador4}));
  alfabeto alfabeto_4 (
    .e(memorianombres_1_nombrejugador1), .s0(alfabeto_4_s0), .s1(alfabeto_4_s1), .s2(alfabeto_4_s2),
    .s3(alfabeto_4_s3), .s4(alfabeto_4_s4), .s5(alfabeto_4_s5));
  alfabeto alfabeto_5 (
    .e(memorianombres_1_nombrejugador1_2), .s0(alfabeto_5_s0), .s1(alfabeto_5_s1), .s2(alfabeto_5_s2),
    .s3(alfabeto_5_s3), .s4(alfabeto_5_s4), .s5(alfabeto_5_s5));
  alfabeto alfabeto_6 (
    .e(memorianombres_1_nombrejugador1_3), .s0(alfabeto_6_s0), .s1(alfabeto_6_s1), .s2(alfabeto_6_s2),
    .s3(alfabeto_6_s3), .s4(alfabeto_6_s4), .s5(alfabeto_6_s5));
  alfabeto alfabeto_7 (
    .e(memorianombres_1_nombrejugador2), .s0(alfabeto_7_s0), .s1(alfabeto_7_s1), .s2(alfabeto_7_s2),
    .s3(alfabeto_7_s3), .s4(alfabeto_7_s4), .s5(alfabeto_7_s5));
  alfabeto alfabeto_8 (
    .e(memorianombres_1_nombrejugador2_2), .s0(alfabeto_8_s0), .s1(alfabeto_8_s1), .s2(alfabeto_8_s2),
    .s3(alfabeto_8_s3), .s4(alfabeto_8_s4), .s5(alfabeto_8_s5));
  alfabeto alfabeto_9 (
    .e(memorianombres_1_nombrejugador2_3), .s0(alfabeto_9_s0), .s1(alfabeto_9_s1), .s2(alfabeto_9_s2),
    .s3(alfabeto_9_s3), .s4(alfabeto_9_s4), .s5(alfabeto_9_s5));
  alfabeto alfabeto_10 (
    .e(memorianombres_1_nombrejugador3), .s0(alfabeto_10_s0), .s1(alfabeto_10_s1), .s2(alfabeto_10_s2),
    .s3(alfabeto_10_s3), .s4(alfabeto_10_s4), .s5(alfabeto_10_s5));
  alfabeto alfabeto_11 (
    .e(memorianombres_1_nombrejugador3_2), .s0(alfabeto_11_s0), .s1(alfabeto_11_s1), .s2(alfabeto_11_s2),
    .s3(alfabeto_11_s3), .s4(alfabeto_11_s4), .s5(alfabeto_11_s5));
  alfabeto alfabeto_12 (
    .e(memorianombres_1_nombrejugador3_3), .s0(alfabeto_12_s0), .s1(alfabeto_12_s1), .s2(alfabeto_12_s2),
    .s3(alfabeto_12_s3), .s4(alfabeto_12_s4), .s5(alfabeto_12_s5));
  alfabeto alfabeto_13 (
    .e(memorianombres_1_nombrejugador4), .s0(alfabeto_13_s0), .s1(alfabeto_13_s1), .s2(alfabeto_13_s2),
    .s3(alfabeto_13_s3), .s4(alfabeto_13_s4), .s5(alfabeto_13_s5));
  alfabeto alfabeto_14 (
    .e(memorianombres_1_nombrejugador4_2), .s0(alfabeto_14_s0), .s1(alfabeto_14_s1), .s2(alfabeto_14_s2),
    .s3(alfabeto_14_s3), .s4(alfabeto_14_s4), .s5(alfabeto_14_s5));
  alfabeto alfabeto_15 (
    .e(memorianombres_1_nombrejugador4_3), .s0(alfabeto_15_s0), .s1(alfabeto_15_s1), .s2(alfabeto_15_s2),
    .s3(alfabeto_15_s3), .s4(alfabeto_15_s4), .s5(alfabeto_15_s5));
  numeros numeros_1 (
    .e(memoriaPuntos_out_7_3), .s0(numeros_1_s5[53:45]), .s1(numeros_1_s5[44:36]), .s2(numeros_1_s5[35:27]),
    .s3(numeros_1_s5[26:18]), .s4(numeros_1_s5[17:9]), .s5(numeros_1_s5[8:0]));
  DotMatrix #(.matrixcols(8), .matrixrows(9)) dotmatrix_4 (
    .col0({9{1'b0}}), .col1(alfabeto_4_s5), .col2(alfabeto_4_s4), .col3(alfabeto_4_s3), .col4(alfabeto_4_s2),
    .col5(alfabeto_4_s1), .col6(alfabeto_4_s0), .col7({9{1'b0}}));
  DotMatrix #(.matrixcols(8), .matrixrows(9)) dotmatrix_5 (
    .col0({9{1'b0}}), .col1(alfabeto_7_s5), .col2(alfabeto_7_s4), .col3(alfabeto_7_s3), .col4(alfabeto_7_s2),
    .col5(alfabeto_7_s1), .col6(alfabeto_7_s0), .col7({9{1'b0}}));
  DotMatrix #(.matrixcols(8), .matrixrows(9)) dotmatrix_6 (
    .col0({9{1'b0}}), .col1(alfabeto_10_s5), .col2(alfabeto_10_s4), .col3(alfabeto_10_s3),
    .col4(alfabeto_10_s2), .col5(alfabeto_10_s1), .col6(alfabeto_10_s0), .col7({9{1'b0}}));
  DotMatrix #(.matrixcols(8), .matrixrows(9)) dotmatrix_7 (
    .col0({9{1'b0}}), .col1(alfabeto_13_s5), .col2(alfabeto_13_s4), .col3(alfabeto_13_s3),
    .col4(alfabeto_13_s2), .col5(alfabeto_13_s1), .col6(alfabeto_13_s0), .col7({9{1'b0}}));
  numeros numeros_2 (
    .e(memoriaPuntos_out_9_3), .s0(numeros_2_s5[53:45]), .s1(numeros_2_s5[44:36]), .s2(numeros_2_s5[35:27]),
    .s3(numeros_2_s5[26:18]), .s4(numeros_2_s5[17:9]), .s5(numeros_2_s5[8:0]));
  numeros numeros_3 (
    .e(memoriaPuntos_out_8_3), .s0(numeros_3_s5[53:45]), .s1(numeros_3_s5[44:36]), .s2(numeros_3_s5[35:27]),
    .s3(numeros_3_s5[26:18]), .s4(numeros_3_s5[17:9]), .s5(numeros_3_s5[8:0]));
  numeros numeros_4 (
    .e(memoriaPuntos_out_7_2), .s0(numeros_4_s5[53:45]), .s1(numeros_4_s5[44:36]), .s2(numeros_4_s5[35:27]),
    .s3(numeros_4_s5[26:18]), .s4(numeros_4_s5[17:9]), .s5(numeros_4_s5[8:0]));
  DotMatrix #(.matrixcols(8), .matrixrows(9)) dotmatrix_8 (
    .col0({9{1'b0}}), .col1(alfabeto_5_s5), .col2(alfabeto_5_s4), .col3(alfabeto_5_s3), .col4(alfabeto_5_s2),
    .col5(alfabeto_5_s1), .col6(alfabeto_5_s0), .col7({9{1'b0}}));
  DotMatrix #(.matrixcols(8), .matrixrows(9)) dotmatrix_9 (
    .col0({9{1'b0}}), .col1(alfabeto_8_s5), .col2(alfabeto_8_s4), .col3(alfabeto_8_s3), .col4(alfabeto_8_s2),
    .col5(alfabeto_8_s1), .col6(alfabeto_8_s0), .col7({9{1'b0}}));
  DotMatrix #(.matrixcols(8), .matrixrows(9)) dotmatrix_10 (
    .col0({9{1'b0}}), .col1(alfabeto_11_s5), .col2(alfabeto_11_s4), .col3(alfabeto_11_s3),
    .col4(alfabeto_11_s2), .col5(alfabeto_11_s1), .col6(alfabeto_11_s0), .col7({9{1'b0}}));
  DotMatrix #(.matrixcols(8), .matrixrows(9)) dotmatrix_11 (
    .col0({9{1'b0}}), .col1(alfabeto_14_s5), .col2(alfabeto_14_s4), .col3(alfabeto_14_s3),
    .col4(alfabeto_14_s2), .col5(alfabeto_14_s1), .col6(alfabeto_14_s0), .col7({9{1'b0}}));
  numeros numeros_5 (
    .e(memoriaPuntos_out_9_2), .s0(numeros_5_s5[53:45]), .s1(numeros_5_s5[44:36]), .s2(numeros_5_s5[35:27]),
    .s3(numeros_5_s5[26:18]), .s4(numeros_5_s5[17:9]), .s5(numeros_5_s5[8:0]));
  numeros numeros_6 (
    .e(memoriaPuntos_out_8_2), .s0(numeros_6_s5[53:45]), .s1(numeros_6_s5[44:36]), .s2(numeros_6_s5[35:27]),
    .s3(numeros_6_s5[26:18]), .s4(numeros_6_s5[17:9]), .s5(numeros_6_s5[8:0]));
  numeros numeros_7 (
    .e(memoriaPuntos_out_7), .s0(numeros_7_s5[53:45]), .s1(numeros_7_s5[44:36]), .s2(numeros_7_s5[35:27]),
    .s3(numeros_7_s5[26:18]), .s4(numeros_7_s5[17:9]), .s5(numeros_7_s5[8:0]));
  DotMatrix #(.matrixcols(8), .matrixrows(9)) dotmatrix_12 (
    .col0({9{1'b0}}), .col1(alfabeto_6_s5), .col2(alfabeto_6_s4), .col3(alfabeto_6_s3), .col4(alfabeto_6_s2),
    .col5(alfabeto_6_s1), .col6(alfabeto_6_s0), .col7({9{1'b0}}));
  DotMatrix #(.matrixcols(8), .matrixrows(9)) dotmatrix_13 (
    .col0({9{1'b0}}), .col1(alfabeto_9_s5), .col2(alfabeto_9_s4), .col3(alfabeto_9_s3), .col4(alfabeto_9_s2),
    .col5(alfabeto_9_s1), .col6(alfabeto_9_s0), .col7({9{1'b0}}));
  DotMatrix #(.matrixcols(8), .matrixrows(9)) dotmatrix_14 (
    .col0({9{1'b0}}), .col1(alfabeto_12_s5), .col2(alfabeto_12_s4), .col3(alfabeto_12_s3),
    .col4(alfabeto_12_s2), .col5(alfabeto_12_s1), .col6(alfabeto_12_s0), .col7({9{1'b0}}));
  DotMatrix #(.matrixcols(8), .matrixrows(9)) dotmatrix_15 (
    .col0({9{1'b0}}), .col1(alfabeto_15_s5), .col2(alfabeto_15_s4), .col3(alfabeto_15_s3),
    .col4(alfabeto_15_s2), .col5(alfabeto_15_s1), .col6(alfabeto_15_s0), .col7({9{1'b0}}));
  numeros numeros_8 (
    .e(memoriaPuntos_out_9), .s0(numeros_8_s5[53:45]), .s1(numeros_8_s5[44:36]), .s2(numeros_8_s5[35:27]),
    .s3(numeros_8_s5[26:18]), .s4(numeros_8_s5[17:9]), .s5(numeros_8_s5[8:0]));
  numeros numeros_9 (
    .e(memoriaPuntos_out_8), .s0(numeros_9_s5[53:45]), .s1(numeros_9_s5[44:36]), .s2(numeros_9_s5[35:27]),
    .s3(numeros_9_s5[26:18]), .s4(numeros_9_s5[17:9]), .s5(numeros_9_s5[8:0]));
  DotMatrix #(.matrixcols(8), .matrixrows(9)) dotmatrix_16 (
    .col0({9{1'b0}}), .col1(numeros_1_s5[53:45]), .col2(numeros_1_s5[44:36]), .col3(numeros_1_s5[35:27]),
    .col4(numeros_1_s5[26:18]), .col5(numeros_1_s5[17:9]), .col6(numeros_1_s5[8:0]), .col7({9{1'b0}}));
  DotMatrix #(.matrixcols(8), .matrixrows(9)) dotmatrix_17 (
    .col0({9{1'b0}}), .col1(numeros_3_s5[53:45]), .col2(numeros_3_s5[44:36]), .col3(numeros_3_s5[35:27]),
    .col4(numeros_3_s5[26:18]), .col5(numeros_3_s5[17:9]), .col6(numeros_3_s5[8:0]), .col7({9{1'b0}}));
  DotMatrix #(.matrixcols(8), .matrixrows(9)) dotmatrix_18 (
    .col0({9{1'b0}}), .col1(numeros_2_s5[53:45]), .col2(numeros_2_s5[44:36]), .col3(numeros_2_s5[35:27]),
    .col4(numeros_2_s5[26:18]), .col5(numeros_2_s5[17:9]), .col6(numeros_2_s5[8:0]), .col7({9{1'b0}}));
  DotMatrix #(.matrixcols(8), .matrixrows(9)) dotmatrix_19 (
    .col0({9{1'b0}}), .col1(numeros_10_s0), .col2(numeros_10_s1), .col3(numeros_10_s2), .col4(numeros_10_s3),
    .col5(numeros_10_s4), .col6(numeros_10_s5), .col7({9{1'b0}}));
  numeros numeros_10 (
    .e(memoriaPuntos_out_10_3), .s0(numeros_10_s0), .s1(numeros_10_s1), .s2(numeros_10_s2),
    .s3(numeros_10_s3), .s4(numeros_10_s4), .s5(numeros_10_s5));
  DotMatrix #(.matrixcols(8), .matrixrows(9)) dotmatrix_20 (
    .col0({9{1'b0}}), .col1(numeros_4_s5[53:45]), .col2(numeros_4_s5[44:36]), .col3(numeros_4_s5[35:27]),
    .col4(numeros_4_s5[26:18]), .col5(numeros_4_s5[17:9]), .col6(numeros_4_s5[8:0]), .col7({9{1'b0}}));
  DotMatrix #(.matrixcols(8), .matrixrows(9)) dotmatrix_21 (
    .col0({9{1'b0}}), .col1(numeros_6_s5[53:45]), .col2(numeros_6_s5[44:36]), .col3(numeros_6_s5[35:27]),
    .col4(numeros_6_s5[26:18]), .col5(numeros_6_s5[17:9]), .col6(numeros_6_s5[8:0]), .col7({9{1'b0}}));
  DotMatrix #(.matrixcols(8), .matrixrows(9)) dotmatrix_22 (
    .col0({9{1'b0}}), .col1(numeros_5_s5[53:45]), .col2(numeros_5_s5[44:36]), .col3(numeros_5_s5[35:27]),
    .col4(numeros_5_s5[26:18]), .col5(numeros_5_s5[17:9]), .col6(numeros_5_s5[8:0]), .col7({9{1'b0}}));
  DotMatrix #(.matrixcols(8), .matrixrows(9)) dotmatrix_23 (
    .col0({9{1'b0}}), .col1(numeros_11_s0), .col2(numeros_11_s1), .col3(numeros_11_s2), .col4(numeros_11_s3),
    .col5(numeros_11_s4), .col6(numeros_11_s5), .col7({9{1'b0}}));
  numeros numeros_11 (
    .e(memoriaPuntos_out_10_2), .s0(numeros_11_s0), .s1(numeros_11_s1), .s2(numeros_11_s2),
    .s3(numeros_11_s3), .s4(numeros_11_s4), .s5(numeros_11_s5));
  DotMatrix #(.matrixcols(8), .matrixrows(9)) dotmatrix_24 (
    .col0({9{1'b0}}), .col1(numeros_7_s5[53:45]), .col2(numeros_7_s5[44:36]), .col3(numeros_7_s5[35:27]),
    .col4(numeros_7_s5[26:18]), .col5(numeros_7_s5[17:9]), .col6(numeros_7_s5[8:0]), .col7({9{1'b0}}));
  DotMatrix #(.matrixcols(8), .matrixrows(9)) dotmatrix_25 (
    .col0({9{1'b0}}), .col1(numeros_9_s5[53:45]), .col2(numeros_9_s5[44:36]), .col3(numeros_9_s5[35:27]),
    .col4(numeros_9_s5[26:18]), .col5(numeros_9_s5[17:9]), .col6(numeros_9_s5[8:0]), .col7({9{1'b0}}));
  DotMatrix #(.matrixcols(8), .matrixrows(9)) dotmatrix_26 (
    .col0({9{1'b0}}), .col1(numeros_8_s5[53:45]), .col2(numeros_8_s5[44:36]), .col3(numeros_8_s5[35:27]),
    .col4(numeros_8_s5[26:18]), .col5(numeros_8_s5[17:9]), .col6(numeros_8_s5[8:0]), .col7({9{1'b0}}));
  DotMatrix #(.matrixcols(8), .matrixrows(9)) dotmatrix_27 (
    .col0({9{1'b0}}), .col1(numeros_12_s0), .col2(numeros_12_s1), .col3(numeros_12_s2), .col4(numeros_12_s3),
    .col5(numeros_12_s4), .col6(numeros_12_s5), .col7({9{1'b0}}));
  numeros numeros_12 (
    .e(memoriaPuntos_out_10), .s0(numeros_12_s0), .s1(numeros_12_s1), .s2(numeros_12_s2), .s3(numeros_12_s3),
    .s4(numeros_12_s4), .s5(numeros_12_s5));
  DotMatrix #(.matrixcols(47), .matrixrows(9)) dotmatrix_28 (
    .col0({9{1'b0}}), .col1(9'hfe), .col2(9'hfe), .col3(9'h92), .col4(9'h90), .col5(9'hf0), .col6(9'h60),
    .col7({9{1'b0}}), .col8({9{1'b0}}), .col9(9'hfe), .col10(9'hfe), .col11(9'h2), .col12(9'h2),
    .col13(9'hfe), .col14(9'hfe), .col15({9{1'b0}}), .col16({9{1'b0}}), .col17(9'hfe), .col18(9'hfe),
    .col19(9'h60), .col20(9'h30), .col21(9'h18), .col22(9'hfe), .col23({9{1'b0}}), .col24({9{1'b0}}),
    .col25(9'hc0), .col26(9'h82), .col27(9'hfe), .col28(9'hfe), .col29(9'h82), .col30(9'hc0),
    .col31({9{1'b0}}), .col32({9{1'b0}}), .col33(9'h7c), .col34(9'hc6), .col35(9'h82), .col36(9'hc6),
    .col37(9'h7c), .col38({9{1'b0}}), .col39({9{1'b0}}), .col40(9'h64), .col41(9'hf6), .col42(9'hb2),
    .col43(9'h9a), .col44(9'hce), .col45(9'h4c), .col46({9{1'b0}}));
  DotMatrix #(.matrixcols(47), .matrixrows(9)) dotmatrix_29 (
    .col0({9{1'b0}}), .col1(9'hfe), .col2(9'hfe), .col3(9'h92), .col4(9'h90), .col5(9'hf0), .col6(9'h60),
    .col7({9{1'b0}}), .col8({9{1'b0}}), .col9(9'hfe), .col10(9'hfe), .col11(9'h2), .col12(9'h2),
    .col13(9'hfe), .col14(9'hfe), .col15({9{1'b0}}), .col16({9{1'b0}}), .col17(9'hfe), .col18(9'hfe),
    .col19(9'h60), .col20(9'h30), .col21(9'h18), .col22(9'hfe), .col23({9{1'b0}}), .col24({9{1'b0}}),
    .col25(9'hc0), .col26(9'h82), .col27(9'hfe), .col28(9'hfe), .col29(9'h82), .col30(9'hc0),
    .col31({9{1'b0}}), .col32({9{1'b0}}), .col33(9'h7c), .col34(9'hc6), .col35(9'h82), .col36(9'hc6),
    .col37(9'h7c), .col38({9{1'b0}}), .col39({9{1'b0}}), .col40(9'h64), .col41(9'hf6), .col42(9'hb2),
    .col43(9'h9a), .col44(9'hce), .col45(9'h4c), .col46({9{1'b0}}));
  DotMatrix #(.matrixcols(47), .matrixrows(9)) dotmatrix_30 (
    .col0({9{1'b0}}), .col1(9'hfe), .col2(9'hfe), .col3(9'h92), .col4(9'h90), .col5(9'hf0), .col6(9'h60),
    .col7({9{1'b0}}), .col8({9{1'b0}}), .col9(9'hfe), .col10(9'hfe), .col11(9'h2), .col12(9'h2),
    .col13(9'hfe), .col14(9'hfe), .col15({9{1'b0}}), .col16({9{1'b0}}), .col17(9'hfe), .col18(9'hfe),
    .col19(9'h60), .col20(9'h30), .col21(9'h18), .col22(9'hfe), .col23({9{1'b0}}), .col24({9{1'b0}}),
    .col25(9'hc0), .col26(9'h82), .col27(9'hfe), .col28(9'hfe), .col29(9'h82), .col30(9'hc0),
    .col31({9{1'b0}}), .col32({9{1'b0}}), .col33(9'h7c), .col34(9'hc6), .col35(9'h82), .col36(9'hc6),
    .col37(9'h7c), .col38({9{1'b0}}), .col39({9{1'b0}}), .col40(9'h64), .col41(9'hf6), .col42(9'hb2),
    .col43(9'h9a), .col44(9'hce), .col45(9'h4c), .col46({9{1'b0}}));
  DotMatrix #(.matrixcols(47), .matrixrows(9)) dotmatrix_31 (
    .col0({9{1'b0}}), .col1(9'hfe), .col2(9'hfe), .col3(9'h92), .col4(9'h90), .col5(9'hf0), .col6(9'h60),
    .col7({9{1'b0}}), .col8({9{1'b0}}), .col9(9'hfe), .col10(9'hfe), .col11(9'h2), .col12(9'h2),
    .col13(9'hfe), .col14(9'hfe), .col15({9{1'b0}}), .col16({9{1'b0}}), .col17(9'hfe), .col18(9'hfe),
    .col19(9'h60), .col20(9'h30), .col21(9'h18), .col22(9'hfe), .col23({9{1'b0}}), .col24({9{1'b0}}),
    .col25(9'hc0), .col26(9'h82), .col27(9'hfe), .col28(9'hfe), .col29(9'h82), .col30(9'hc0),
    .col31({9{1'b0}}), .col32({9{1'b0}}), .col33(9'h7c), .col34(9'hc6), .col35(9'h82), .col36(9'hc6),
    .col37(9'h7c), .col38({9{1'b0}}), .col39({9{1'b0}}), .col40(9'h64), .col41(9'hf6), .col42(9'hb2),
    .col43(9'h9a), .col44(9'hce), .col45(9'h4c), .col46({9{1'b0}}));

  // Notes on the sheet:
  //   contents of rom_1 (hex, n*v repeats v):
  //   fffbf8 fffbf8 fffbf8 fffbfa fffbfa fffbfa fdfcfa fdfdfb fdfdfb fdfdfb 7*fefefe 7*ffffff fcfefd
  //   fcfefd fcfefd fefefe 4*ffffff fffdfe fffdfe fefeff fffdff fdfbfc fdfbfc 5*fefdfb 9*fffefc 9*fffdfe
  //   fefcfd fefcfd fefcfd fffdfe fffdfe fefefe fefefe fefefe 4*ffffff fffdff fffdfe fffdfe fffcfb fdf9f6
  //   fdf8f4 fcf7f3 fef4f3 fff6f5 fff8f6 fffaf7 fffbf8 fefdf9 fffbf8 4*fffaf7 fef9f6 fff7f5 fff7f5 fef4f3
  //   fdf3f2 fdf5f2 fcf4f1 fcf2f0 faf0ee f8f0ed faf2ef f7f2ee f5f0ec f6f1ed f5f2ed f5f2ed f4efeb f3ebe9
  //   f4eaeb f4eaeb f4eaeb f4eae9 f4eae9 f3eaeb f0e7e8 f0e7e8 eee5e8 ede4e5 eee5e6 efe6e7 f0e7e8 ece6e8
  //   eae5e9 ebe6ea eae5eb e8e6eb e4e3e9 e4e1e8 e3e4e9 e1e1e9 dedee8 dadce8 d8dae7 d6d8e7 d2d5e4 cfd5e5
  //   cdd4e4 ccd5e6 c9d4e6 c9d4ea c3cfe7 becde4 bccce5 b9cae4 b6c7e3 b3c4e2 adc0e0 acc1e0 aabedf a7bee0
  //   a4bcde a2badc 9fb7dd 9bb4dd 96b1dc 95b0db 96aeda 94add6 8eaad2 8aaad3 8dacd8 8eaddb 8aabd8 8aadd7
  //   87acd6 84a9d3 84a6d3 80a5cf 80a6d3 80a6d5 84a9d6 87a9d6 85a7d4 84a6d4 83a5d3 82a4d2 82a4d2 82a4d4
  //   81a3d3 81a3d3 81a3d3 7fa3d3 7fa3d3 81a5d5 81a3d3 81a2d5 83a5d5 86a8d8 88aad8 88aad8 87a9d7 87a9d7
  //   86a8d6 85a7d5 86a6d5 87a7d6 89a9d8 8babda 89abd9 89abdb 8baddb 8baddb 8aacda 89abd9 88aad8 88aad8
  //   89abd9 8aacd9 8aacd9 88add9 87aed9 84add9 86aada 87a8db 6*86a7da 87a9d9 88aada 88aad8 86abd8 88aad7
  //   88aad7 8aacd9 8aafd9 8db0d8 8fb1d7 90b0d6 95b3d7 96b4d8 9bb8da a0badd a4bddc a9bedb afc1d9 b5c5dc
  //   c1cee1 c5d2e5 c4cfe1 c1ccde c0cbdd c2cbdc c2cbdc c2c9d9 bfc8d9 bfc8d9 c3cbde c6cee1 c6cee1 c5cedf
  //   c4ccdf c1cce2 fffbf8 fffcf7 fffbf8 fffbfa fffbfa fdfcf8 fefdf9 fdfdfb fdfdfb fdfdfb 7*fefefe
  //   7*ffffff fefefe ffffff fefefe fefefe fffdfe fffdfe fffdfe ffffff fffdfe fffdfe fefefe fefeff fefcfd
  //   fefcfd fefdfb fdfdfb fefdfb fefdfb fefdfb 9*fffefc 14*fffdfe fefefe fefefe fefefe 4*ffffff fefefe
  //   fffdfe fffdfe fefdfb fffbf8 fdf9f6 fdf9f6 fef4f2 fef4f2 fff5f3 fef9f5 fefbf6 fcfbf6 fefbf6 fefbf6
  //   fffaf7 fef9f6 fef9f6 fff8f5 fff7f4 fef6f3 fef4f2 fdf3f2 fbf1ef fbf1ef fbf1ef f9efed f9efed f9f1ee
  //   f8f0ed f7efec f7efec f8f0ed f7efec f5edeb f2eae8 5*f4eaeb f3e9ea f1e7e8 f0e7e8 efe6e7 eee5e6 efe6e7
  //   efe6e7 f0e7e8 ece6e8 ebe6ea ebe6ea ebe6ec e8e6eb e4e3e8 e4e1e8 e3e4e9 e0e0e8 dedee8 d9dbe7 d7d9e6
  //   d5d7e6 d2d5e4 cfd5e5 ccd3e3 c9d2e3 c5d0e4 c3cfe5 c0cce4 bbc9e3 b7c8e2 b3c7e2 b0c3e1 adc0e1 a8bcdd
  //   a5bcde a2b8dd a1b9df 9ebadf 9ab6de 97b2dd 93b0dc 8eadd9 8cabd7 8aa9d7 86a7d4 83a5d2 84a4d3 84a6d4
  //   86a8d8 83a5d5 7fa4d1 7fa4d1 7ea2d2 7ca0d2 78a0d1 78a0d3 7aa2d6 7ca1d5 7ca2d3 7da3d2 7ca2d3 7ca2d3
  //   7ca2d3 7ba0d4 7ba0d4 799ed3 799ed3 789dd2 789dd2 769ed2 799ed3 799cd2 7a9dd5 7c9fd5 7da0d6 7ea2d6
  //   7ea2d6 7da1d3 7ea2d4 7ea2d4 7fa3d5 7ea2d4 7ea2d4 7fa3d5 82a6d8 81a5d9 81a5d7 82a6d8 82a6d6 82a6d8
  //   81a5d7 80a4d4 80a4d4 81a6d3 82a6d6 82a6d6 82a6d6 81a7d6 7da6d4 7ea4d5 7fa3d7 7ea3d8 7da2d6 7da2d6
  //   7ea1d7 7ea1d7 7da2d6 7ea3d7 7ea4d5 7fa5d6 7fa5d4 81a5d5 81a5d5 82a7d4 84a9d5 86abd7 8aadd7 8babd4
  //   8facd4 94b2d8 96b2d7 99b6d8 9fb9da a2b9d8 aabbd7 b1c1da b7c6dd b9c8dd bac9de bcc9dc bbc8db bac7da
  //   bac5d7 bbc3d6 bcc4d7 bbc6d8 bec9dd c0cbdf c1cce0 c0cbdd bec9dd bcc8de fffbf8 fffcf7 fffbf8 fffbfa
  //   fffbfa fefdf9 fdfef9 fdfdfb fdfdfb fdfdfb 7*fefefe 10*ffffff fefefe fffdfe fffdfe fffdfe fefefe
  //   fffefc fffdfe fffeff fffeff fffdfe fffdfe fefefc fdfdfb fefdfb fefdfb fefdfb 9*fffefc 12*fffdfe
  //   fefcfd fffdfe fefefe fefefe fefefe 7*ffffff fffffd fffefc fffbf8 fffbf8 fff6f4 fff5f3 fff7f4 fef9f5
  //   fdfaf5 fcf9f4 fcf9f4 fef9f5 fff7f5 fff7f5 fff7f4 fff6f4 fff5f3 fff5f3 fdf3f1 fcf2f0 fcf1ef fbf1ef
  //   fbf1ef faf0ee faf0ee fcf1ef fcf1ef fbf0ee faefed faefed faefed f8ecec f6eceb f7edee f8eeef f8eeef
  //   f7edee f6eced f6eced f3e9ea f3e9ea f4eaeb f3e9ea f3e9e8 f3e9ea f2e9ea f1e8eb eee9ed ede8ee ede8ee
  //   ece7ed e8e6eb e6e3ea e4e5ea e2e2ea e0e0ea dcdeea dadce9 d8dae9 d4d7e6 cfd6e6 ccd3e3 c9d2e3 c5d0e4
  //   c2cee6 c0cce6 bbcbe5 b6c7e3 b1c6e1 aec3e0 acc0e1 a6bddf a3bbdd a1b9dd a0badf 9ebae1 9bb7de 97b4dc
  //   93b0da 90add7 8baad6 88a8d7 86a8d8 84a8da 83a7d7 83a7d7 83a7d9 82a6d8 80a4d6 7da1d5 7ca0d4 7da0d6
  //   7ca0d4 7ba0d5 7ca1d6 7da1d5 7da1d1 7ea2d2 7fa3d3 82a4d4 80a4d4 7ea2d2 7ea2d4 7c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
endmodule

module celdaMemoria (
  input  in_1,
  input  in_2,
  input  in_3,
  input  in_4,
  output out_5,
  output out_6,
  output out_7
);

  wire d_ff_1_q, d_ff_2_q, or_1_out, or_2_out, or_3_out;

  or or_1 (or_1_out, in_1, in_2, in_3, in_4);
  D_Flip_Flop d_ff_1 (.D(or_2_out), .clk(or_1_out), .Q(d_ff_1_q));  // open: Qn, preset, reset
  or or_2 (or_2_out, in_2, in_4);
  D_Flip_Flop d_ff_2 (.D(or_3_out), .clk(or_1_out), .Q(d_ff_2_q));  // open: Qn, preset, reset
  or or_3 (or_3_out, in_3, in_4);
  and and_1 (out_5, d_ff_1_q, d_ff_2_q);
  or or_4 (out_6, out_5, out_7, d_ff_2_q);
  and and_2 (out_7, d_ff_1_q, ~d_ff_2_q);  // AND_Gate
endmodule

module posicion (
  input  newGame,
  input  derecha,
  input  izquierda,
  input  abajo,
  input  arriba,
  output h0,
  output out_7,
  output out_8,
  output out_9,
  output out_10,
  output out_11,
  output out_12,
  output out_13,
  output out_14,
  output out_15,
  output out_16,
  output out_17
);

  wire and_1_out, and_2_out, and_3_out, and_4_out, and_5_out, and_6_out, and_7_out, and_8_out, and_9_out,
       and_10_out, and_11_out, and_12_out, nand_1_out, nand_2_out, nand_3_out, nand_4_out, or_1_out,
       or_2_out, or_3_out, or_4_out, or_5_out, or_6_out, or_7_out, or_8_out, or_9_out, or_10_out, t_ff_1_q,
       t_ff_2_q, t_ff_3_q, t_ff_4_q, t_ff_5_q, t_ff_6_q, t_ff_7_q, t_ff_8_q;

  and and_1 (and_1_out, derecha, nand_1_out);
  nand nand_1 (nand_1_out, t_ff_3_q, ~t_ff_5_q, t_ff_7_q);  // NAND_Gate
  and and_2 (and_2_out, izquierda, nand_2_out);
  nand nand_2 (nand_2_out, ~t_ff_3_q, ~t_ff_5_q, ~t_ff_7_q);  // NAND_Gate
  nand nand_3 (nand_3_out, t_ff_4_q, ~t_ff_6_q, t_ff_8_q);  // NAND_Gate
  nand nand_4 (nand_4_out, ~t_ff_4_q, ~t_ff_6_q, ~t_ff_8_q);  // NAND_Gate
  or or_1 (or_1_out, abajo, izquierda);
  T_Flip_Flop t_ff_1 (.Q(t_ff_1_q), .reset(or_2_out), .preset(or_1_out));  // open: T, clk, Qn
  or or_2 (or_2_out, derecha, arriba);
  and and_3 (and_3_out, t_ff_5_q, derecha, t_ff_7_q);
  or or_3 (or_3_out, and_1_out, and_2_out);
  and and_4 (and_4_out, abajo, nand_3_out);
  or or_4 (or_4_out, and_4_out, and_5_out);
  and and_5 (and_5_out, arriba, nand_4_out);
  T_Flip_Flop t_ff_2 (.Q(t_ff_2_q), .reset(or_8_out), .preset(or_7_out));  // open: T, clk, Qn
  T_Flip_Flop t_ff_3 (.T(or_5_out), .clk(or_3_out), .Q(t_ff_3_q), .reset(newGame));  // open: Qn, preset
  or or_5 (or_5_out, and_3_out, and_6_out);
  and and_6 (and_6_out, izquierda, ~t_ff_5_q, ~t_ff_7_q);  // AND_Gate
  T_Flip_Flop t_ff_4 (.T(or_6_out), .clk(or_4_out), .Q(t_ff_4_q), .reset(newGame));  // open: Qn, preset
  and and_7 (and_7_out, t_ff_6_q, abajo, t_ff_8_q);
  or or_6 (or_6_out, and_7_out, and_8_out);
  and and_8 (and_8_out, arriba, ~t_ff_6_q, ~t_ff_8_q);  // AND_Gate
  or or_7 (or_7_out, izquierda, derecha);
  or or_8 (or_8_out, arriba, abajo);
  and and_9 (and_9_out, t_ff_7_q, derecha);
  and and_10 (and_10_out, izquierda, ~t_ff_7_q);  // AND_Gate
  and and_11 (and_11_out, t_ff_8_q, abajo);
  and and_12 (and_12_out, arriba, ~t_ff_8_q);  // AND_Gate
  T_Flip_Flop t_ff_5 (.T(or_9_out), .clk(or_3_out), .Q(t_ff_5_q), .reset(newGame));  // open: Qn, preset
  or or_9 (or_9_out, and_9_out, and_10_out);
  T_Flip_Flop t_ff_6 (.T(or_10_out), .clk(or_4_out), .Q(t_ff_6_q), .reset(newGame));  // open: Qn, preset
  or or_10 (or_10_out, and_11_out, and_12_out);
  T_Flip_Flop t_ff_7 (.T(1'b1), .clk(or_3_out), .Q(t_ff_7_q), .reset(newGame));  // open: Qn, preset
  T_Flip_Flop t_ff_8 (.T(1'b1), .clk(or_4_out), .Q(t_ff_8_q), .reset(newGame));  // open: Qn, preset
  and and_13 (h0, ~t_ff_7_q, ~t_ff_5_q, ~t_ff_3_q);  // AND_Gate
  and and_14 (out_7, t_ff_7_q, ~t_ff_5_q, ~t_ff_3_q);  // AND_Gate
  and and_15 (out_8, ~t_ff_7_q, t_ff_5_q, ~t_ff_3_q);  // AND_Gate
  and and_16 (out_9, t_ff_7_q, t_ff_5_q, ~t_ff_3_q);  // AND_Gate
  and and_17 (out_10, ~t_ff_7_q, ~t_ff_5_q, t_ff_3_q);  // AND_Gate
  and and_18 (out_11, t_ff_7_q, ~t_ff_5_q, t_ff_3_q);  // AND_Gate
  and and_19 (out_12, ~t_ff_8_q, ~t_ff_6_q, ~t_ff_4_q);  // AND_Gate
  and and_20 (out_13, t_ff_8_q, ~t_ff_6_q, ~t_ff_4_q);  // AND_Gate
  and and_21 (out_14, ~t_ff_8_q, t_ff_6_q, ~t_ff_4_q);  // AND_Gate
  and and_22 (out_15, t_ff_8_q, t_ff_6_q, ~t_ff_4_q);  // AND_Gate
  and and_23 (out_16, ~t_ff_8_q, ~t_ff_6_q, t_ff_4_q);  // AND_Gate
  and and_24 (out_17, t_ff_8_q, ~t_ff_6_q, t_ff_4_q);  // AND_Gate
endmodule

module letras (
  input  adelante,
  input  atras,
  output [4:0] out_3
);

  wire and_1_out, and_2_out, and_3_out, and_4_out, and_5_out, and_6_out, and_7_out, and_8_out, and_9_out,
       and_10_out, nand_1_out, nand_2_out, or_1_out, or_2_out, or_3_out, or_4_out, or_5_out;

  nand nand_1 (nand_1_out, ~out_3[0], out_3[1], ~out_3[2], out_3[3], out_3[4]);  // NAND_Gate
  nand nand_2 (nand_2_out, ~out_3[4], ~out_3[3], ~out_3[2], ~out_3[1], ~out_3[0]);  // NAND_Gate
  and and_1 (and_1_out, adelante, nand_1_out);
  and and_2 (and_2_out, atras, nand_2_out);
  and and_3 (and_3_out, out_3[2], out_3[1], out_3[0], out_3[3], adelante);
  and and_4 (and_4_out, atras, ~out_3[3], ~out_3[0], ~out_3[1], ~out_3[2]);  // AND_Gate
  or or_1 (or_1_out, and_1_out, and_2_out);
  T_Flip_Flop t_ff_1 (.T(or_2_out), .clk(or_1_out), .Q(out_3[4]));  // open: Qn, reset, preset
  or or_2 (or_2_out, and_3_out, and_4_out);
  and and_5 (and_5_out, out_3[2], out_3[1], out_3[0], adelante);
  and and_6 (and_6_out, atras, ~out_3[0], ~out_3[1], ~out_3[2]);  // AND_Gate
  T_Flip_Flop t_ff_2 (.T(or_3_out), .clk(or_1_out), .Q(out_3[3]));  // open: Qn, reset, preset
  or or_3 (or_3_out, and_5_out, and_6_out);
  and and_7 (and_7_out, out_3[1], out_3[0], adelante);
  T_Flip_Flop t_ff_3 (.T(or_4_out), .clk(or_1_out), .Q(out_3[2]));  // open: Qn, reset, preset
  or or_4 (or_4_out, and_7_out, and_8_out);
  and and_8 (and_8_out, atras, ~out_3[0], ~out_3[1]);  // AND_Gate
  and and_9 (and_9_out, out_3[0], adelante);
  and and_10 (and_10_out, atras, ~out_3[0]);  // AND_Gate
  T_Flip_Flop t_ff_4 (.T(or_5_out), .clk(or_1_out), .Q(out_3[1]));  // open: Qn, reset, preset
  or or_5 (or_5_out, and_9_out, and_10_out);
  T_Flip_Flop t_ff_5 (.T(1'b1), .clk(or_1_out), .Q(out_3[0]));  // open: Qn, reset, preset
endmodule

module alfabeto (
  input  [4:0] e,
  output [8:0] s0,
  output [8:0] s1,
  output [8:0] s2,
  output [8:0] s3,
  output [8:0] s4,
  output [8:0] s5
);

  wire and_1_out, and_2_out, and_3_out, and_4_out, and_5_out, and_6_out, and_7_out, and_8_out, and_9_out,
       and_10_out, and_11_out, and_12_out, and_13_out, and_14_out, and_15_out, and_16_out, and_17_out,
       and_18_out, and_19_out, and_20_out, and_21_out, and_22_out, and_23_out, and_24_out, and_25_out,
       and_26_out, and_27_out, and_28_out, and_29_out, and_30_out, and_31_out, and_32_out, and_33_out,
       and_34_out, and_35_out, and_36_out, and_37_out, and_38_out, and_39_out, and_40_out, and_41_out,
       and_42_out, and_43_out, and_44_out, and_45_out, and_46_out, and_47_out, and_48_out, and_49_out,
       and_50_out, and_51_out, and_52_out, and_53_out, and_54_out, and_55_out, and_56_out, and_57_out,
       and_58_out, and_59_out, and_60_out, and_61_out, and_62_out, and_63_out, and_64_out, and_65_out,
       and_66_out, and_67_out, and_68_out, and_69_out, and_70_out, and_71_out, and_72_out, and_73_out,
       and_74_out, and_75_out, and_76_out, and_77_out, and_78_out, and_79_out, and_80_out, and_81_out,
       and_82_out, and_83_out, and_84_out, and_85_out, and_86_out, and_87_out, and_88_out, and_89_out,
       and_90_out, and_91_out, and_92_out, and_93_out, and_94_out, and_95_out, and_96_out, and_97_out,
       and_98_out, and_99_out, and_100_out, and_101_out, and_102_out, and_103_out, and_104_out, and_105_out,
       and_106_out, and_107_out, and_108_out, and_109_out, and_110_out, and_111_out, and_112_out,
       and_113_out, and_114_out, and_115_out, and_116_out, and_117_out, and_118_out, and_119_out,
       and_120_out, and_121_out, and_122_out, and_123_out, and_124_out, and_125_out, and_126_out,
       and_127_out, and_128_out, and_129_out, and_130_out, and_131_out, and_132_out, and_133_out,
       and_134_out, and_135_out, and_136_out, and_137_out, and_138_out, and_139_out, and_140_out,
       and_141_out, and_142_out, and_143_out, and_144_out, and_145_out, and_146_out, and_147_out,
       and_148_out, and_149_out, and_150_out, and_151_out, and_152_out, and_153_out, and_154_out,
       and_155_out, and_156_out, and_157_out, and_158_out, and_159_out, and_160_out, and_161_out,
       and_162_out, and_163_out, and_164_out, and_165_out, and_166_out, and_167_out, and_168_out,
       and_169_out, and_170_out, and_171_out, and_172_out, and_173_out, and_174_out, and_175_out,
       and_176_out, and_177_out, and_178_out, and_179_out, and_180_out, and_181_out, and_182_out,
       and_183_out, and_184_out, and_185_out, and_186_out, and_187_out, and_188_out, and_189_out,
       and_190_out, and_191_out, and_192_out, and_193_out, and_194_out, and_195_out, and_196_out,
       and_197_out, and_198_out, and_199_out, and_200_out, and_201_out, and_202_out, and_203_out,
       and_204_out, and_205_out, and_206_out, and_207_out, and_208_out, and_209_out, and_210_out,
       and_211_out, and_212_out, and_213_out, and_214_out, and_215_out, and_216_out, and_217_out,
       and_218_out, and_219_out, and_220_out, and_221_out, and_222_out, and_223_out, and_224_out,
       and_225_out, and_226_out, and_227_out, and_228_out, and_229_out, and_230_out, and_231_out,
       and_232_out, and_233_out, and_234_out, and_235_out, and_236_out, and_237_out, and_238_out,
       and_239_out, and_240_out, and_241_out, not_1_out, not_2_out, not_3_out, not_4_out, not_5_out;

  not not_1 (not_1_out, e[4]);
  not not_2 (not_2_out, e[3]);
  not not_3 (not_3_out, e[2]);
  not not_4 (not_4_out, e[1]);
  not not_5 (not_5_out, e[0]);
  and and_1 (and_1_out, e[2], not_4_out);
  and and_2 (and_2_out, not_2_out, e[2], e[0]);
  and and_3 (and_3_out, e[3], not_4_out, e[0]);
  and and_4 (and_4_out, e[3], not_3_out, e[1], not_5_out);
  and and_5 (and_5_out, e[4], e[1], e[0]);
  and and_6 (and_6_out, e[4], e[2]);
  and and_7 (and_7_out, e[4], e[3]);
  and and_8 (and_8_out, not_2_out, not_4_out, e[0]);
  and and_9 (and_9_out, e[1], not_5_out);
  and and_10 (and_10_out, not_2_out, not_3_out, not_4_out);
  and and_11 (and_11_out, not_1_out, not_2_out, e[1], e[0]);
  and and_12 (and_12_out, e[3], e[2]);
  and and_13 (and_13_out, e[4], not_4_out);
  and and_14 (and_14_out, e[4], e[2]);
  and and_15 (and_15_out, not_2_out, not_3_out, not_4_out, not_5_out);
  and and_16 (and_16_out, not_1_out, not_2_out, e[1], e[0]);
  and and_17 (and_17_out, e[3], e[2], not_4_out);
  and and_18 (and_18_out, e[3], e[2], not_5_out);
  and and_19 (and_19_out, e[4], e[2], not_4_out);
  and and_20 (and_20_out, e[4], e[2], not_5_out);
  and and_21 (and_21_out, not_1_out, not_2_out, not_3_out, not_4_out);
  and and_22 (and_22_out, not_1_out, not_3_out, e[1], e[0]);
  and and_23 (and_23_out, not_1_out, not_2_out, e[2], e[1]);
  and and_24 (and_24_out, e[3], e[2], not_4_out);
  and and_25 (and_25_out, e[3], e[2], not_5_out);
  and and_26 (and_26_out, e[4], not_2_out, not_5_out);
  and and_27 (and_27_out, e[4], e[2], not_4_out);
  and and_28 (and_28_out, not_1_out, not_2_out, not_3_out, not_4_out);
  and and_29 (and_29_out, e[1], not_5_out);
  and and_30 (and_30_out, e[2], not_5_out);
  and and_31 (and_31_out, not_2_out, e[2], e[1]);
  and and_32 (and_32_out, e[3], not_3_out, e[1]);
  and and_33 (and_33_out, e[3], e[2], not_4_out);
  and and_34 (and_34_out, e[4], not_3_out, not_4_out, e[0]);
  and and_35 (and_35_out, not_2_out, not_4_out, not_5_out);
  and and_36 (and_36_out, not_2_out, e[2], e[1]);
  and and_37 (and_37_out, e[3], not_3_out, e[1]);
  and and_38 (and_38_out, e[3], e[2], not_4_out);
  and and_39 (and_39_out, e[4], not_3_out, not_4_out, e[0]);
  and and_40 (and_40_out, not_2_out, not_4_out, e[0]);
  and and_41 (and_41_out, not_1_out, e[1], not_5_out);
  and and_42 (and_42_out, not_1_out, e[2], not_5_out);
  and and_43 (and_43_out, not_2_out, e[2], not_4_out);
  and and_44 (and_44_out, not_1_out, e[2], e[1]);
  and and_45 (and_45_out, e[3], not_3_out, not_4_out);
  and and_46 (and_46_out, e[4], not_3_out);
  and and_47 (and_47_out, not_1_out, not_2_out, not_3_out);
  and and_48 (and_48_out, not_2_out, not_3_out, not_5_out);
  and and_49 (and_49_out, not_1_out, not_3_out, not_4_out, e[0]);
  and and_50 (and_50_out, not_1_out, e[1], not_5_out);
  and and_51 (and_51_out, not_1_out, e[2], e[1]);
  and and_52 (and_52_out, e[3], e[2], not_5_out);
  and and_53 (and_53_out, e[4], not_2_out, not_4_out);
  and and_54 (and_54_out, e[4], not_3_out, not_5_out);
  and and_55 (and_55_out, not_2_out, not_3_out, not_4_out);
  and and_56 (and_56_out, not_1_out, not_2_out, not_3_out, e[0]);
  and and_57 (and_57_out, not_3_out, not_4_out, e[0]);
  and and_58 (and_58_out, e[2], e[1], e[0]);
  and and_59 (and_59_out, e[3], not_3_out, e[1], not_5_out);
  and and_60 (and_60_out, e[3], e[2], not_4_out, not_5_out);
  and and_61 (and_61_out, e[4], not_4_out);
  and and_62 (and_62_out, not_2_out, not_3_out, not_4_out);
  and and_63 (and_63_out, not_3_out, not_4_out, e[0]);
  and and_64 (and_64_out, not_1_out, not_2_out, e[1], e[0]);
  and and_65 (and_65_out, e[2], e[1], e[0]);
  and and_66 (and_66_out, e[3], e[2], not_4_out);
  and and_67 (and_67_out, e[4], not_4_out);
  and and_68 (and_68_out, not_2_out, not_3_out, not_4_out);
  and and_69 (and_69_out, not_1_out, not_2_out, not_3_out, e[0]);
  and and_70 (and_70_out, not_1_out, not_3_out, not_4_out, e[0]);
  and and_71 (and_71_out, not_2_out, e[2], e[1]);
  and and_72 (and_72_out, e[3], not_3_out, e[1], not_5_out);
  and and_73 (and_73_out, e[3], e[2], not_4_out);
  and and_74 (and_74_out, e[4], not_2_out, not_4_out);
  and and_75 (and_75_out, e[4], not_2_out, not_5_out);
  and and_76 (and_76_out, not_2_out, not_3_out, not_4_out);
  and and_77 (and_77_out, not_2_out, not_3_out, not_5_out);
  and and_78 (and_78_out, not_1_out, not_3_out, e[0]);
  and and_79 (and_79_out, not_1_out, not_2_out, e[1]);
  and and_80 (and_80_out, not_1_out, not_3_out, e[1]);
  and and_81 (and_81_out, e[3], e[2], not_5_out);
  and and_82 (and_82_out, e[4], e[2]);
  and and_83 (and_83_out, not_1_out, not_5_out);
  and and_84 (and_84_out, not_2_out, not_3_out, not_4_out);
  and and_85 (and_85_out, not_4_out, not_5_out);
  and and_86 (and_86_out, not_1_out, not_2_out, e[2], e[1]);
  and and_87 (and_87_out, e[3], not_3_out, e[1]);
  and and_88 (and_88_out, e[4], not_3_out);
  and and_89 (and_89_out, not_1_out, not_2_out, not_4_out);
  and and_90 (and_90_out, not_1_out, not_2_out, not_5_out);
  and and_91 (and_91_out, not_1_out, not_3_out, not_4_out);
  and and_92 (and_92_out, not_2_out, not_3_out);
  and and_93 (and_93_out, not_3_out, not_4_out, e[0]);
  and and_94 (and_94_out, e[3], e[2], e[1]);
  and and_95 (and_95_out, not_1_out, not_3_out, not_4_out, not_5_out);
  and and_96 (and_96_out, not_2_out, not_3_out, e[1], e[0]);
  and and_97 (and_97_out, not_1_out, e[3], not_3_out, not_4_out);
  and and_98 (and_98_out, not_1_out, e[3], not_4_out, not_5_out);
  and and_99 (and_99_out, not_1_out, e[2], not_4_out);
  and and_100 (and_100_out, not_1_out, e[3], not_3_out, not_5_out);
  and and_101 (and_101_out, not_1_out, e[3], not_4_out);
  and and_102 (and_102_out, e[4], not_3_out, e[1], e[0]);
  and and_103 (and_103_out, not_1_out, not_4_out, e[0]);
  and and_104 (and_104_out, not_3_out, not_4_out, e[0]);
  and and_105 (and_105_out, not_1_out, e[2], not_4_out);
  and and_106 (and_106_out, not_1_out, e[2], e[0]);
  and and_107 (and_107_out, e[3], not_3_out, not_5_out);
  and and_108 (and_108_out, e[4], e[1]);
  and and_109 (and_109_out, not_1_out, not_2_out, not_4_out, not_5_out);
  and and_110 (and_110_out, not_1_out, not_2_out, e[2], not_4_out);
  and and_111 (and_111_out, not_1_out, not_2_out, e[2], not_5_out);
  and and_112 (and_112_out, e[3], not_3_out, not_4_out);
  and and_113 (and_113_out, e[3], not_3_out, not_5_out);
  and and_114 (and_114_out, e[4], not_3_out);
  and and_115 (and_115_out, e[4], e[1]);
  and and_116 (and_116_out, not_2_out, not_3_out, e[1], e[0]);
  and and_117 (and_117_out, not_1_out, e[3], not_3_out, not_4_out);
  and and_118 (and_118_out, e[4], not_3_out, not_4_out, not_5_out);
  and and_119 (and_119_out, e[4], e[2], not_4_out, e[0]);
  and and_120 (and_120_out, not_1_out, not_3_out, e[0]);
  and and_121 (and_121_out, not_2_out, not_3_out, e[1]);
  and and_122 (and_122_out, not_2_out, e[2], not_4_out, not_5_out);
  and and_123 (and_123_out, not_1_out, e[2], e[1], not_5_out);
  and and_124 (and_124_out, e[3], not_3_out, not_4_out);
  and and_125 (and_125_out, e[4], not_3_out, not_5_out);
  and and_126 (and_126_out, e[4], e[2], not_4_out);
  and and_127 (and_127_out, not_1_out, not_2_out, not_4_out);
  and and_128 (and_128_out, not_1_out, not_3_out, not_4_out);
  and and_129 (and_129_out, not_2_out, not_3_out);
  and and_130 (and_130_out, not_3_out, e[0]);
  and and_131 (and_131_out, not_1_out, e[2], e[1], not_5_out);
  and and_132 (and_132_out, e[3], e[2], e[1]);
  and and_133 (and_133_out, not_1_out, not_3_out, not_4_out, not_5_out);
  and and_134 (and_134_out, e[3], e[2], not_4_out, e[0]);
  and and_135 (and_135_out, e[3], e[2], e[1], not_5_out);
  and and_136 (and_136_out, e[4], not_3_out, e[1], e[0]);
  and and_137 (and_137_out, not_1_out, e[3], not_4_out, not_5_out);
  and and_138 (and_138_out, e[3], e[2], not_4_out);
  and and_139 (and_139_out, e[4], not_3_out, e[1]);
  and and_140 (and_140_out, e[4], e[1], e[0]);
  and and_141 (and_141_out, not_2_out, not_3_out, not_4_out, e[0]);
  and and_142 (and_142_out, not_1_out, not_2_out, e[2], not_4_out);
  and and_143 (and_143_out, not_1_out, e[2], not_4_out, not_5_out);
  and and_144 (and_144_out, e[2], e[1], e[0]);
  and and_145 (and_145_out, e[3], not_3_out, not_5_out);
  and and_146 (and_146_out, e[4], not_3_out, e[1]);
  and and_147 (and_147_out, not_1_out, not_3_out, not_4_out, not_5_out);
  and and_148 (and_148_out, e[3], not_4_out, not_5_out);
  and and_149 (and_149_out, e[4], e[1], e[0]);
  and and_150 (and_150_out, e[4], e[2], e[1]);
  and and_151 (and_151_out, e[4], e[3]);
  and and_152 (and_152_out, e[3], not_3_out, not_4_out, not_5_out);
  and and_153 (and_153_out, e[3], e[2], e[1], not_5_out);
  and and_154 (and_154_out, e[4], not_3_out, not_4_out, not_5_out);
  and and_155 (and_155_out, e[4], e[1], e[0]);
  and and_156 (and_156_out, e[4], e[2], e[0]);
  and and_157 (and_157_out, e[4], e[2], e[1]);
  and and_158 (and_158_out, e[4], e[3]);
  and and_159 (and_159_out, not_1_out, not_3_out, e[0]);
  and and_160 (and_160_out, not_2_out, not_3_out, e[1]);
  and and_161 (and_161_out, not_2_out, e[2], not_4_out);
  and and_162 (and_162_out, not_1_out, e[2], e[1], not_5_out);
  and and_163 (and_163_out, e[3], not_3_out, not_4_out);
  and and_164 (and_164_out, e[3], e[2], e[1]);
  and and_165 (and_165_out, not_2_out, e[0]);
  and and_166 (and_166_out, not_3_out, e[1]);
  and and_167 (and_167_out, not_2_out, e[2]);
  and and_168 (and_168_out, e[2], e[0]);
  and and_169 (and_169_out, e[3], not_3_out, not_5_out);
  and and_170 (and_170_out, not_2_out, not_4_out);
  and and_171 (and_171_out, not_2_out, not_5_out);
  and and_172 (and_172_out, not_1_out, e[1]);
  and and_173 (and_173_out, e[4], not_4_out);
  and and_174 (and_174_out, not_2_out, not_4_out);
  and and_175 (and_175_out, not_1_out, not_2_out, e[0]);
  and and_176 (and_176_out, e[2], not_4_out);
  and and_177 (and_177_out, e[2], e[0]);
  and and_178 (and_178_out, e[3], e[1]);
  and and_179 (and_179_out, e[4], not_5_out);
  and and_180 (and_180_out, not_2_out, not_4_out);
  and and_181 (and_181_out, not_1_out, not_2_out, e[0]);
  and and_182 (and_182_out, e[2], not_4_out);
  and and_183 (and_183_out, e[3], e[1]);
  and and_184 (and_184_out, e[4], not_5_out);
  and and_185 (and_185_out, not_2_out, not_4_out);
  and and_186 (and_186_out, not_1_out, not_2_out, e[0]);
  and and_187 (and_187_out, not_1_out, e[2], e[0]);
  and and_188 (and_188_out, e[3], e[1]);
  and and_189 (and_189_out, e[4], e[2], not_5_out);
  and and_190 (and_190_out, not_2_out, not_4_out);
  and and_191 (and_191_out, not_2_out, not_5_out);
  and and_192 (and_192_out, not_1_out, e[1]);
  and and_193 (and_193_out, e[2], e[0]);
  and and_194 (and_194_out, e[4], not_4_out, e[0]);
  and and_195 (and_195_out, not_1_out, not_3_out);
  and and_196 (and_196_out, not_1_out, e[0]);
  and and_197 (and_197_out, not_3_out, e[0]);
  and and_198 (and_198_out, not_2_out, e[1]);
  and and_199 (and_199_out, not_2_out, e[2], not_5_out);
  and and_200 (and_200_out, e[3], not_3_out);
  and and_201 (and_201_out, not_2_out, e[0]);
  and and_202 (and_202_out, e[2], not_4_out);
  and and_203 (and_203_out, e[2], e[0]);
  and and_204 (and_204_out, e[3], not_3_out, e[1]);
  and and_205 (and_205_out, e[4], e[2]);
  and and_206 (and_206_out, e[4], e[3]);
  and and_207 (and_207_out, not_2_out, e[0]);
  and and_208 (and_208_out, not_3_out, e[1]);
  and and_209 (and_209_out, not_2_out, e[2]);
  and and_210 (and_210_out, e[2], not_4_out);
  and and_211 (and_211_out, e[2], e[0]);
  and and_212 (and_212_out, not_2_out, not_4_out);
  and and_213 (and_213_out, not_2_out, not_5_out);
  and and_214 (and_214_out, not_1_out, not_3_out, e[1]);
  and and_215 (and_215_out, e[2], not_4_out);
  and and_216 (and_216_out, not_1_out, e[2], e[0]);
  and and_217 (and_217_out, e[4], not_4_out);
  and and_218 (and_218_out, not_2_out, not_4_out);
  and and_219 (and_219_out, not_1_out, not_3_out, e[1]);
  and and_220 (and_220_out, not_2_out, e[2], not_5_out);
  and and_221 (and_221_out, e[2], not_4_out);
  and and_222 (and_222_out, not_1_out, e[2], e[0]);
  and and_223 (and_223_out, not_2_out, not_4_out);
  and and_224 (and_224_out, not_1_out, e[0]);
  and and_225 (and_225_out, not_1_out, not_3_out, e[1]);
  and and_226 (and_226_out, not_2_out, e[2], not_5_out);
  and and_227 (and_227_out, e[2], not_4_out);
  and and_228 (and_228_out, not_1_out, not_2_out);
  and and_229 (and_229_out, not_1_out, e[0]);
  and and_230 (and_230_out, not_2_out, not_3_out, not_4_out, e[0]);
  and and_231 (and_231_out, not_1_out, not_3_out, e[1]);
  and and_232 (and_232_out, not_2_out, e[1], not_5_out);
  and and_233 (and_233_out, not_1_out, e[2], not_4_out);
  and and_234 (and_234_out, not_2_out, e[2], not_5_out);
  and and_235 (and_235_out, not_1_out, not_2_out, not_4_out);
  and and_236 (and_236_out, not_1_out, e[0]);
  and and_237 (and_237_out, not_3_out, not_4_out, e[0]);
  and and_238 (and_238_out, not_1_out, e[2], not_4_out);
  and and_239 (and_239_out, e[3], not_3_out, e[1]);
  and and_240 (and_240_out, e[4], e[2], not_5_out);
  and and_241 (and_241_out, e[4], e[2], e[1]);
  and and_242 (s5[0], e[3], e[2], not_4_out, not_5_out);
  or or_1 (s0[7], and_1_out, and_2_out, and_3_out, and_4_out, and_5_out, and_6_out, and_7_out);
  or or_2 (s0[6], and_8_out, and_9_out, e[2], e[4]);
  or or_3 (s0[5], and_10_out, and_11_out, and_12_out, and_13_out, and_14_out);
  or or_4 (s0[4], and_15_out, and_16_out, and_17_out, and_18_out, and_19_out, and_20_out);
  or or_5 (s0[3], and_21_out, and_22_out, and_23_out, and_24_out, and_25_out, and_26_out, and_27_out);
  or or_6 (s0[2], and_28_out, and_29_out, and_30_out, and_31_out, and_32_out, and_33_out, and_34_out);
  or or_7 (s0[1], and_35_out, and_36_out, and_37_out, and_38_out, and_39_out);
  or or_8 (s1[7], and_40_out, and_41_out, and_42_out, and_43_out, and_44_out, and_45_out, and_46_out);
  or or_9 (s1[6], and_47_out, and_48_out, and_49_out, and_50_out, and_51_out, and_52_out, and_53_out, and_54_out);
  or or_10 (s1[5], and_55_out, and_56_out, and_57_out, and_58_out, and_59_out, and_60_out, and_61_out);
  or or_11 (s1[4], and_62_out, and_63_out, and_64_out, and_65_out, and_66_out, and_67_out);
  or or_12 (s1[3], and_68_out, and_69_out, and_70_out, and_71_out, and_72_out, and_73_out, and_74_out, and_75_out);
  or or_13 (s1[2], and_76_out, and_77_out, and_78_out, and_79_out, and_80_out, and_81_out, and_82_out);
  or or_14 (s1[1], and_83_out, and_84_out, and_85_out, and_86_out, and_87_out, and_88_out);
  or or_15 (s2[7], and_89_out, and_90_out, and_91_out, and_92_out, and_93_out, and_94_out);
  or or_16 (s2[6], and_95_out, and_96_out, and_97_out, and_98_out);
  or or_17 (s2[5], and_99_out, and_100_out, and_101_out, and_102_out);
  or or_18 (s2[4], and_103_out, and_104_out, and_105_out, and_106_out, and_107_out, and_108_out);
  or or_19 (s2[3], and_109_out, and_110_out, and_111_out, and_112_out, and_113_out, and_114_out, and_115_out);
  or or_20 (s2[2], and_116_out, and_117_out, and_118_out, and_119_out);
  or or_21 (s2[1], and_120_out, and_121_out, and_122_out, and_123_out, and_124_out, and_125_out, and_126_out);
  or or_22 (s3[7], and_127_out, and_128_out, and_129_out, and_130_out, and_131_out, and_132_out);
  or or_23 (s3[6], and_133_out, and_134_out, and_135_out, and_136_out);
  or or_24 (s3[5], and_137_out, and_138_out, and_139_out, and_140_out);
  or or_25 (s3[4], and_141_out, and_142_out, and_143_out, and_144_out, and_145_out, and_146_out);
  or or_26 (s3[3], and_147_out, and_148_out, and_149_out, and_150_out, and_151_out);
  or or_27 (s3[2], and_152_out, and_153_out, and_154_out, and_155_out, and_156_out, and_157_out, and_158_out);
  or or_28 (s3[1], and_159_out, and_160_out, and_161_out, and_162_out, and_163_out, and_164_out);
  or or_29 (s4[7], and_165_out, and_166_out, and_167_out, and_168_out, and_169_out, e[4]);
  or or_30 (s4[6], and_170_out, and_171_out, and_172_out, e[2], and_173_out);
  or or_31 (s4[5], and_174_out, and_175_out, and_176_out, and_177_out, and_178_out, and_179_out);
  or or_32 (s4[4], and_180_out, and_181_out, and_182_out, and_183_out, and_184_out);
  or or_33 (s4[3], and_185_out, and_186_out, and_187_out, and_188_out, and_189_out);
  or or_34 (s4[2], and_190_out, and_191_out, and_192_out, and_193_out, and_194_out);
  or or_35 (s4[1], and_195_out, and_196_out, and_197_out, and_198_out, and_199_out, and_200_out);
  or or_36 (s5[7], and_201_out, and_202_out, and_203_out, and_204_out, and_205_out, and_206_out);
  or or_37 (s5[6], and_207_out, and_208_out, and_209_out, and_210_out, and_211_out, e[4]);
  or or_38 (s5[5], and_212_out, and_213_out, and_214_out, and_215_out, and_216_out, and_217_out);
  or or_39 (s5[4], and_218_out, and_219_out, and_220_out, and_221_out, and_222_out);
  or or_40 (s5[3], and_223_out, and_224_out, and_225_out, and_226_out, and_227_out);
  or or_41 (s5[2], and_228_out, and_229_out, and_230_out, and_231_out, and_232_out, and_233_out, and_234_out);
  or or_42 (s5[1], and_235_out, and_236_out, and_237_out, and_238_out, and_239_out, and_240_out, and_241_out);

  assign {s0[8], s0[0]} = 2'b00;
  assign {s1[8], s1[0]} = 2'b00;
  assign {s2[8], s2[0]} = 2'b00;
  assign {s3[8], s3[0]} = 2'b00;
  assign {s4[8], s4[0]} = 2'b00;
  assign s5[8] = 1'b0;
endmodule

module memoriaNombres (
  input  [14:0] nombre,
  input  habilitacionCargaNombre,
  input  jug1,
  input  jug2,
  input  jug3,
  input  jug4,
  output [14:0] nombreJugador1,
  output [14:0] nombreJugador2,
  output [14:0] nombreJugador3,
  output [14:0] nombreJugador4
);

  wire and_1_out, and_2_out, and_3_out, and_4_out;

  and and_1 (and_1_out, habilitacionCargaNombre, jug1);
  and and_2 (and_2_out, jug2, habilitacionCargaNombre);
  and and_3 (and_3_out, jug3, habilitacionCargaNombre);
  and and_4 (and_4_out, jug4, habilitacionCargaNombre);
  D_Flip_Flop d_ff_1 (.D(nombre[14]), .clk(and_1_out), .Q(nombreJugador1[14]));  // open: Qn, preset, reset
  D_Flip_Flop d_ff_2 (.D(nombre[14]), .clk(and_2_out), .Q(nombreJugador2[14]));  // open: Qn, preset, reset
  D_Flip_Flop d_ff_3 (.D(nombre[14]), .clk(and_3_out), .Q(nombreJugador3[14]));  // open: Qn, preset, reset
  D_Flip_Flop d_ff_4 (.D(nombre[14]), .clk(and_4_out), .Q(nombreJugador4[14]));  // open: Qn, preset, reset
  D_Flip_Flop d_ff_5 (.D(nombre[13]), .clk(and_1_out), .Q(nombreJugador1[13]));  // open: Qn, preset, reset
  D_Flip_Flop d_ff_6 (.D(nombre[13]), .clk(and_2_out), .Q(nombreJugador2[13]));  // open: Qn, preset, reset
  D_Flip_Flop d_ff_7 (.D(nombre[13]), .clk(and_3_out), .Q(nombreJugador3[13]));  // open: Qn, preset, reset
  D_Flip_Flop d_ff_8 (.D(nombre[13]), .clk(and_4_out), .Q(nombreJugador4[13]));  // open: Qn, preset, reset
  D_Flip_Flop d_ff_9 (.D(nombre[12]), .clk(and_1_out), .Q(nombreJugador1[12]));  // open: Qn, preset, reset
  D_Flip_Flop d_ff_10 (.D(nombre[12]), .clk(and_2_out), .Q(nombreJugador2[12]));  // open: Qn, preset, reset
  D_Flip_Flop d_ff_11 (.D(nombre[12]), .clk(and_3_out), .Q(nombreJugador3[12]));  // open: Qn, preset, reset
  D_Flip_Flop d_ff_12 (.D(nombre[12]), .clk(and_4_out), .Q(nombreJugador4[12]));  // open: Qn, preset, reset
  D_Flip_Flop d_ff_13 (.D(nombre[11]), .clk(and_1_out), .Q(nombreJugador1[11]));  // open: Qn, preset, reset
  D_Flip_Flop d_ff_14 (.D(nombre[11]), .clk(and_2_out), .Q(nombreJugador2[11]));  // open: Qn, preset, reset
  D_Flip_Flop d_ff_15 (.D(nombre[11]), .clk(and_3_out), .Q(nombreJugador3[11]));  // open: Qn, preset, reset
  D_Flip_Flop d_ff_16 (.D(nombre[11]), .clk(and_4_out), .Q(nombreJugador4[11]));  // open: Qn, preset, reset
  D_Flip_Flop d_ff_17 (.D(nombre[10]), .clk(and_1_out), .Q(nombreJugador1[10]));  // open: Qn, preset, reset
  D_Flip_Flop d_ff_18 (.D(nombre[10]), .clk(and_2_out), .Q(nombreJugador2[10]));  // open: Qn, preset, reset
  D_Flip_Flop d_ff_19 (.D(nombre[10]), .clk(and_3_out), .Q(nombreJugador3[10]));  // open: Qn, preset, reset
  D_Flip_Flop d_ff_20 (.D(nombre[10]), .clk(and_4_out), .Q(nombreJugador4[10]));  // open: Qn, preset, reset
  D_Flip_Flop d_ff_21 (.D(nombre[9]), .clk(and_1_out), .Q(nombreJugador1[9]));  // open: Qn, preset, reset
  D_Flip_Flop d_ff_22 (.D(nombre[9]), .clk(and_2_out), .Q(nombreJugador2[9]));  // open: Qn, preset, reset
  D_Flip_Flop d_ff_23 (.D(nombre[9]), .clk(and_3_out), .Q(nombreJugador3[9]));  // open: Qn, preset, reset
  D_Flip_Flop d_ff_24 (.D(nombre[9]), .clk(and_4_out), .Q(nombreJugador4[9]));  // open: Qn, preset, reset
  D_Flip_Flop d_ff_25 (.D(nombre[8]), .clk(and_1_out), .Q(nombreJugador1[8]));  // open: Qn, preset, reset
  D_Flip_Flop d_ff_26 (.D(nombre[8]), .clk(and_2_out), .Q(nombreJugador2[8]));  // open: Qn, preset, reset
  D_Flip_Flop d_ff_27 (.D(nombre[8]), .clk(and_3_out), .Q(nombreJugador3[8]));  // open: Qn, preset, reset
  D_Flip_Flop d_ff_28 (.D(nombre[8]), .clk(and_4_out), .Q(nombreJugador4[8]));  // open: Qn, preset, reset
  D_Flip_Flop d_ff_29 (.D(nombre[7]), .clk(and_1_out), .Q(nombreJugador1[7]));  // open: Qn, preset, reset
  D_Flip_Flop d_ff_30 (.D(nombre[7]), .clk(and_2_out), .Q(nombreJugador2[7]));  // open: Qn, preset, reset
  D_Flip_Flop d_ff_31 (.D(nombre[7]), .clk(and_3_out), .Q(nombreJugador3[7]));  // open: Qn, preset, reset
  D_Flip_Flop d_ff_32 (.D(nombre[7]), .clk(and_4_out), .Q(nombreJugador4[7]));  // open: Qn, preset, reset
  D_Flip_Flop d_ff_33 (.D(nombre[6]), .clk(and_1_out), .Q(nombreJugador1[6]));  // open: Qn, preset, reset
  D_Flip_Flop d_ff_34 (.D(nombre[6]), .clk(and_2_out), .Q(nombreJugador2[6]));  // open: Qn, preset, reset
  D_Flip_Flop d_ff_35 (.D(nombre[6]), .clk(and_3_out), .Q(nombreJugador3[6]));  // open: Qn, preset, reset
  D_Flip_Flop d_ff_36 (.D(nombre[6]), .clk(and_4_out), .Q(nombreJugador4[6]));  // open: Qn, preset, reset
  D_Flip_Flop d_ff_37 (.D(nombre[5]), .clk(and_1_out), .Q(nombreJugador1[5]));  // open: Qn, preset, reset
  D_Flip_Flop d_ff_38 (.D(nombre[5]), .clk(and_2_out), .Q(nombreJugador2[5]));  // open: Qn, preset, reset
  D_Flip_Flop d_ff_39 (.D(nombre[5]), .clk(and_3_out), .Q(nombreJugador3[5]));  // open: Qn, preset, reset
  D_Flip_Flop d_ff_40 (.D(nombre[5]), .clk(and_4_out), .Q(nombreJugador4[5]));  // open: Qn, preset, reset
  D_Flip_Flop d_ff_41 (.D(nombre[4]), .clk(and_1_out), .Q(nombreJugador1[4]));  // open: Qn, preset, reset
  D_Flip_Flop d_ff_42 (.D(nombre[4]), .clk(and_2_out), .Q(nombreJugador2[4]));  // open: Qn, preset, reset
  D_Flip_Flop d_ff_43 (.D(nombre[4]), .clk(and_3_out), .Q(nombreJugador3[4]));  // open: Qn, preset, reset
  D_Flip_Flop d_ff_44 (.D(nombre[4]), .clk(and_4_out), .Q(nombreJugador4[4]));  // open: Qn, preset, reset
  D_Flip_Flop d_ff_45 (.D(nombre[3]), .clk(and_1_out), .Q(nombreJugador1[3]));  // open: Qn, preset, reset
  D_Flip_Flop d_ff_46 (.D(nombre[3]), .clk(and_2_out), .Q(nombreJugador2[3]));  // open: Qn, preset, reset
  D_Flip_Flop d_ff_47 (.D(nombre[3]), .clk(and_3_out), .Q(nombreJugador3[3]));  // open: Qn, preset, reset
  D_Flip_Flop d_ff_48 (.D(nombre[3]), .clk(and_4_out), .Q(nombreJugador4[3]));  // open: Qn, preset, reset
  D_Flip_Flop d_ff_49 (.D(nombre[2]), .clk(and_1_out), .Q(nombreJugador1[2]));  // open: Qn, preset, reset
  D_Flip_Flop d_ff_50 (.D(nombre[2]), .clk(and_2_out), .Q(nombreJugador2[2]));  // open: Qn, preset, reset
  D_Flip_Flop d_ff_51 (.D(nombre[2]), .clk(and_3_out), .Q(nombreJugador3[2]));  // open: Qn, preset, reset
  D_Flip_Flop d_ff_52 (.D(nombre[2]), .clk(and_4_out), .Q(nombreJugador4[2]));  // open: Qn, preset, reset
  D_Flip_Flop d_ff_53 (.D(nombre[1]), .clk(and_1_out), .Q(nombreJugador1[1]));  // open: Qn, preset, reset
  D_Flip_Flop d_ff_54 (.D(nombre[1]), .clk(and_2_out), .Q(nombreJugador2[1]));  // open: Qn, preset, reset
  D_Flip_Flop d_ff_55 (.D(nombre[1]), .clk(and_3_out), .Q(nombreJugador3[1]));  // open: Qn, preset, reset
  D_Flip_Flop d_ff_56 (.D(nombre[1]), .clk(and_4_out), .Q(nombreJugador4[1]));  // open: Qn, preset, reset
  D_Flip_Flop d_ff_57 (.D(nombre[0]), .clk(and_1_out), .Q(nombreJugador1[0]));  // open: Qn, preset, reset
  D_Flip_Flop d_ff_58 (.D(nombre[0]), .clk(and_2_out), .Q(nombreJugador2[0]));  // open: Qn, preset, reset
  D_Flip_Flop d_ff_59 (.D(nombre[0]), .clk(and_3_out), .Q(nombreJugador3[0]));  // open: Qn, preset, reset
  D_Flip_Flop d_ff_60 (.D(nombre[0]), .clk(and_4_out), .Q(nombreJugador4[0]));  // open: Qn, preset, reset
endmodule

// Turnos
module selectorTurnos (
  input  in_1,
  output out_2,
  output out_3,
  output out_4,
  output out_5
);

  wire t_ff_1_q, t_ff_2_q;

  T_Flip_Flop t_ff_1 (.T(t_ff_2_q), .clk(in_1), .Q(t_ff_1_q));  // open: Qn, reset, preset
  T_Flip_Flop t_ff_2 (.T(1'b1), .clk(in_1), .Q(t_ff_2_q));  // open: Qn, reset, preset
  and and_1 (out_2, ~t_ff_2_q, ~t_ff_1_q);  // AND_Gate
  and and_2 (out_3, t_ff_2_q, ~t_ff_1_q);  // AND_Gate
  and and_3 (out_4, ~t_ff_2_q, t_ff_1_q);  // AND_Gate
  and and_4 (out_5, t_ff_2_q, t_ff_1_q);
endmodule

module numeros (
  input  [3:0] e,
  output [8:0] s0,
  output [8:0] s1,
  output [8:0] s2,
  output [8:0] s3,
  output [8:0] s4,
  output [8:0] s5
);

  wire and_2_out, and_3_out, and_4_out, and_5_out, and_6_out, and_7_out, and_8_out, and_9_out, and_10_out,
       and_11_out, and_12_out, and_13_out, and_14_out, and_15_out, and_16_out, and_17_out, and_18_out,
       and_19_out, and_20_out, and_21_out, and_22_out, and_23_out, and_24_out, and_25_out, and_26_out,
       and_27_out, and_28_out, and_29_out, and_30_out, and_31_out, and_33_out, and_34_out, and_35_out,
       and_36_out, and_37_out, and_38_out, and_39_out, and_40_out, and_41_out, and_42_out, and_43_out,
       and_44_out, and_45_out, and_46_out, and_47_out, and_48_out, and_49_out, and_50_out, and_51_out,
       and_52_out, and_53_out, and_54_out, and_55_out, and_56_out, and_57_out, and_58_out, and_59_out,
       and_60_out, and_61_out, and_62_out, and_63_out, and_64_out, and_65_out, and_66_out, and_67_out,
       and_68_out, and_69_out, and_70_out, and_71_out, and_72_out, and_73_out, and_74_out, and_75_out,
       and_76_out, and_77_out, and_78_out, and_79_out, and_80_out, and_81_out, and_82_out, and_83_out,
       and_84_out, and_85_out, and_86_out, not_1_out, not_2_out, not_3_out;

  not not_1 (not_1_out, e[3]);
  not not_2 (not_2_out, e[2]);
  not not_3 (not_3_out, e[1]);
  not not_4 (s1[3], e[0]);
  and and_1 (s0[7], e[2], e[0]);
  and and_2 (and_2_out, not_2_out, s1[3]);
  and and_3 (and_3_out, e[2], e[0]);
  and and_4 (and_4_out, not_2_out, not_3_out, s1[3]);
  and and_5 (and_5_out, e[2], not_3_out, e[0]);
  and and_6 (and_6_out, e[2], e[1], s1[3]);
  and and_7 (and_7_out, not_1_out, not_3_out, s1[3]);
  or or_1 (s0[4], and_7_out, and_8_out);
  and and_8 (and_8_out, e[2], e[1], s1[3]);
  and and_9 (and_9_out, not_3_out, s1[3]);
  or or_2 (s0[3], and_9_out, and_10_out);
  and and_10 (and_10_out, e[2], s1[3]);
  and and_11 (and_11_out, not_2_out, s1[3]);
  and and_12 (and_12_out, not_2_out, e[1]);
  and and_13 (and_13_out, e[1], s1[3]);
  and and_14 (and_14_out, e[2], not_3_out, e[0]);
  and and_15 (and_15_out, not_1_out, not_2_out, not_3_out, e[0]);
  or or_3 (s0[1], and_15_out, and_16_out);
  and and_16 (and_16_out, not_2_out, e[1], s1[3]);
  and and_17 (and_17_out, not_2_out, s1[3]);
  and and_18 (and_18_out, e[2], e[0]);
  and and_19 (and_19_out, not_2_out, s1[3]);
  and and_20 (and_20_out, e[2], e[0]);
  or or_4 (s1[5], not_3_out, and_21_out);
  and and_21 (and_21_out, e[2], s1[3]);
  and and_22 (and_22_out, not_2_out, not_3_out, s1[3]);
  and and_23 (and_23_out, e[2], e[1], s1[3]);
  or or_5 (s1[4], and_22_out, and_23_out, e[3]);
  and and_24 (and_24_out, not_2_out, s1[3]);
  and and_25 (and_25_out, not_2_out, e[1]);
  and and_26 (and_26_out, e[1], s1[3]);
  and and_27 (and_27_out, e[2], not_3_out, e[0]);
  and and_28 (and_28_out, not_3_out, e[0]);
  or or_6 (s1[1], not_2_out, and_28_out, and_29_out);
  and and_29 (and_29_out, e[1], s1[3]);
  or or_7 (s2[7], not_2_out, e[0], e[1]);
  and and_30 (and_30_out, not_1_out, not_2_out, not_3_out, e[0]);
  or or_8 (s2[6], and_30_out, and_31_out);
  and and_31 (and_31_out, e[2], not_3_out, s1[3]);
  and and_32 (s2[5], not_1_out, not_3_out, e[0]);
  and and_33 (and_33_out, not_2_out, not_3_out);
  and and_34 (and_34_out, not_2_out, e[0]);
  and and_35 (and_35_out, e[2], e[1], s1[3]);
  and and_36 (and_36_out, not_1_out, not_2_out, not_3_out, e[0]);
  and and_37 (and_37_out, not_1_out, not_2_out, e[1], s1[3]);
  and and_38 (and_38_out, e[2], not_3_out, s1[3]);
  and and_39 (and_39_out, e[2], e[1], e[0]);
  and and_40 (and_40_out, not_1_out, not_2_out, not_3_out, e[0]);
  or or_9 (s2[2], and_40_out, and_41_out);
  and and_41 (and_41_out, e[2], e[1], e[0]);
  or or_10 (s2[1], not_2_out, e[0], e[1]);
  and and_42 (and_42_out, not_1_out, not_2_out, not_3_out, e[0]);
  or or_11 (s3[6], and_42_out, and_43_out);
  and and_43 (and_43_out, e[2], not_3_out, s1[3]);
  and and_44 (and_44_out, not_1_out, not_3_out);
  and and_45 (and_45_out, e[2], e[0]);
  or or_12 (s3[5], and_44_out, and_45_out, and_46_out);
  and and_46 (and_46_out, e[3], e[1]);
  and and_47 (and_47_out, not_2_out, e[0]);
  and and_48 (and_48_out, not_1_out, e[1]);
  and and_49 (and_49_out, e[2], s1[3]);
  and and_50 (and_50_out, e[3], not_3_out);
  and and_51 (and_51_out, not_1_out, not_2_out, not_3_out, e[0]);
  and and_52 (and_52_out, e[2], not_3_out, s1[3]);
  or or_13 (s3[3], and_51_out, and_52_out, and_53_out);
  and and_53 (and_53_out, e[2], e[1], e[0]);
  and and_54 (and_54_out, not_1_out, not_2_out, not_3_out, e[0]);
  and and_55 (and_55_out, e[2], not_3_out, s1[3]);
  or or_14 (s3[2], and_54_out, and_55_out, and_56_out);
  and and_56 (and_56_out, e[2], e[1], e[0]);
  or or_15 (s4[7], s1[3], e[1], e[2], e[3]);
  or or_16 (s4[6], s1[3], e[1], e[3]);
  and and_57 (and_57_out, not_2_out, s1[3]);
  and and_58 (and_58_out, e[1], e[0]);
  and and_59 (and_59_out, e[2], not_3_out);
  or or_17 (s4[4], s1[3], e[1], e[2], e[3]);
  and and_60 (and_60_out, not_3_out, s1[3]);
  and and_61 (and_61_out, not_2_out, e[1], e[0]);
  and and_62 (and_62_out, e[2], not_3_out);
  and and_63 (and_63_out, e[2], s1[3]);
  and and_64 (and_64_out, not_3_out, s1[3]);
  and and_65 (and_65_out, not_2_out, e[1], e[0]);
  and and_66 (and_66_out, e[2], not_3_out);
  and and_67 (and_67_out, e[2], s1[3]);
  or or_18 (s4[1], not_2_out, not_3_out, s1[3]);
  and and_68 (and_68_out, not_1_out, e[2], e[0]);
  or or_19 (s5[7], and_68_out, and_69_out);
  and and_69 (and_69_out, e[3], e[2], e[1]);
  and and_70 (and_70_out, not_2_out, s1[3]);
  or or_20 (s5[6], and_70_out, e[1], e[3]);
  and and_71 (and_71_out, not_2_out, s1[3]);
  and and_72 (and_72_out, not_2_out, e[1]);
  or or_21 (s5[5], and_71_out, and_72_out, e[3]);
  and and_73 (and_73_out, not_1_out, not_2_out, not_3_out, s1[3]);
  and and_74 (and_74_out, e[2], not_3_out, e[0]);
  and and_75 (and_75_out, e[3], e[0]);
  and and_76 (and_76_out, e[3], e[1]);
  and and_77 (and_77_out, not_3_out, s1[3]);
  and and_78 (and_78_out, not_2_out, e[1], e[0]);
  and and_79 (and_79_out, e[2], not_3_out);
  and and_80 (and_80_out, e[2], s1[3]);
  and and_81 (and_81_out, not_2_out, not_3_out, s1[3]);
  and and_82 (and_82_out, not_2_out, e[1], e[0]);
  and and_83 (and_83_out, e[2], not_3_out, e[0]);
  and and_84 (and_84_out, e[2], e[1], s1[3]);
  and and_85 (and_85_out, not_1_out, not_2_out, not_3_out, e[0]);
  or or_22 (s5[1], and_85_out, and_86_out);
  and and_86 (and_86_out, not_1_out, not_2_out, e[1], s1[3]);
  or or_23 (s0[6], and_2_out, e[1], and_3_out, e[3]);
  or or_24 (s0[5], and_4_out, and_5_out, and_6_out, e[3]);
  or or_25 (s0[2], and_11_out, and_12_out, and_13_out, and_14_out, e[3]);
  or or_26 (s1[7], and_17_out, e[1], and_18_out, e[3]);
  or or_27 (s1[6], and_19_out, e[1], and_20_out, e[3]);
  or or_28 (s1[2], and_24_out, and_25_out, and_26_out, and_27_out, e[3]);
  or or_29 (s2[4], and_33_out, and_34_out, and_35_out, e[3]);
  or or_30 (s2[3], and_36_out, and_37_out, and_38_out, and_39_out);
  or or_31 (s3[4], and_47_out, and_48_out, and_49_out, and_50_out);
  or or_32 (s4[5], and_57_out, and_58_out, and_59_out, e[3]);
  or or_33 (s4[3], and_60_out, and_61_out, and_62_out, and_63_out, e[3]);
  or or_34 (s4[2], and_64_out, and_65_out, and_66_out, and_67_out, e[3]);
  or or_35 (s5[4], and_73_out, and_74_out, and_75_out, and_76_out);
  or or_36 (s5[3], and_77_out, and_78_out, and_79_out, and_80_out, e[3]);
  or or_37 (s5[2], and_81_out, and_82_out, and_83_out, and_84_out, e[3]);

  assign {s0[8], s0[0]} = 2'b00;
  assign {s1[8], s1[0]} = 2'b00;
  assign {s2[8], s2[0]} = 2'b00;
  assign {s3[8:7], s3[1:0]} = 4'b0110;
  assign {s4[8], s4[0]} = 2'b00;
  assign {s5[8], s5[0]} = 2'b00;
endmodule

module puntos (
  input  resetear,
  input  in_2,
  output [3:0] out_3,
  output [3:0] out_4,
  output [3:0] out_5
);

  wire [4:0] counter_1_q, multiplier_1_cout, multiplier_1_out;

  Counter #(.max('h1f), .width(5)) counter_1 (
    .clr(resetear), .clk(in_2), .Q(counter_1_q));  // open: load, up, count, D, carry
  Multiplier #(.width(5)) multiplier_1 (
    .a(counter_1_q), .b(5'b00101), .out(multiplier_1_out), .cout(multiplier_1_cout));  // open: cin
  // Binary_to_BCD_converter #(.binvalue(10)) binary_to_bcd_converter_1: pin names not known; wires that end beside it: {multiplier_1_cout, multiplier_1_out}, out_3, out_4, out_5
endmodule

module memoriaDePuntos (
  input  [7:0] in_1,
  input  habilitacion,
  input  jug1,
  input  jug2,
  input  jug3,
  input  jug4,
  output [11:0] out_7,
  output [11:0] out_8,
  output [11:0] out_9,
  output [11:0] out_10
);

  wire and_1_out, and_2_out, and_3_out, and_4_out;
  wire [7:0] d_ff_29_q, d_ff_30_q, d_ff_31_q, d_ff_32_q;

  and and_1 (and_1_out, habilitacion, jug1);
  and and_2 (and_2_out, habilitacion, jug2);
  and and_3 (and_3_out, habilitacion, jug3);
  and and_4 (and_4_out, habilitacion, jug4);
  D_Flip_Flop d_ff_1 (.D(in_1[7]), .clk(and_1_out), .Q(d_ff_29_q[7]));  // open: Qn, preset, reset
  D_Flip_Flop d_ff_2 (.D(in_1[7]), .clk(and_2_out), .Q(d_ff_30_q[7]));  // open: Qn, preset, reset
  D_Flip_Flop d_ff_3 (.D(in_1[7]), .clk(and_3_out), .Q(d_ff_31_q[7]));  // open: Qn, preset, reset
  D_Flip_Flop d_ff_4 (.D(in_1[7]), .clk(and_4_out), .Q(d_ff_32_q[7]));  // open: Qn, preset, reset
  D_Flip_Flop d_ff_5 (.D(in_1[6]), .clk(and_1_out), .Q(d_ff_29_q[6]));  // open: Qn, preset, reset
  D_Flip_Flop d_ff_6 (.D(in_1[6]), .clk(and_2_out), .Q(d_ff_30_q[6]));  // open: Qn, preset, reset
  D_Flip_Flop d_ff_7 (.D(in_1[6]), .clk(and_3_out), .Q(d_ff_31_q[6]));  // open: Qn, preset, reset
  D_Flip_Flop d_ff_8 (.D(in_1[6]), .clk(and_4_out), .Q(d_ff_32_q[6]));  // open: Qn, preset, reset
  D_Flip_Flop d_ff_9 (.D(in_1[5]), .clk(and_1_out), .Q(d_ff_29_q[5]));  // open: Qn, preset, reset
  D_Flip_Flop d_ff_10 (.D(in_1[5]), .clk(and_2_out), .Q(d_ff_30_q[5]));  // open: Qn, preset, reset
  D_Flip_Flop d_ff_11 (.D(in_1[5]), .clk(and_3_out), .Q(d_ff_31_q[5]));  // open: Qn, preset, reset
  D_Flip_Flop d_ff_12 (.D(in_1[5]), .clk(and_4_out), .Q(d_ff_32_q[5]));  // open: Qn, preset, reset
  D_Flip_Flop d_ff_13 (.D(in_1[4]), .clk(and_1_out), .Q(d_ff_29_q[4]));  // open: Qn, preset, reset
  D_Flip_Flop d_ff_14 (.D(in_1[4]), .clk(and_2_out), .Q(d_ff_30_q[4]));  // open: Qn, preset, reset
  D_Flip_Flop d_ff_15 (.D(in_1[4]), .clk(and_3_out), .Q(d_ff_31_q[4]));  // open: Qn, preset, reset
  D_Flip_Flop d_ff_16 (.D(in_1[4]), .clk(and_4_out), .Q(d_ff_32_q[4]));  // open: Qn, preset, reset
  D_Flip_Flop d_ff_17 (.D(in_1[3]), .clk(and_1_out), .Q(d_ff_29_q[3]));  // open: Qn, preset, reset
  D_Flip_Flop d_ff_18 (.D(in_1[3]), .clk(and_2_out), .Q(d_ff_30_q[3]));  // open: Qn, preset, reset
  D_Flip_Flop d_ff_19 (.D(in_1[3]), .clk(and_3_out), .Q(d_ff_31_q[3]));  // open: Qn, preset, reset
  D_Flip_Flop d_ff_20 (.D(in_1[3]), .clk(and_4_out), .Q(d_ff_32_q[3]));  // open: Qn, preset, reset
  D_Flip_Flop d_ff_21 (.D(in_1[2]), .clk(and_1_out), .Q(d_ff_29_q[2]));  // open: Qn, preset, reset
  D_Flip_Flop d_ff_22 (.D(in_1[2]), .clk(and_2_out), .Q(d_ff_30_q[2]));  // open: Qn, preset, reset
  D_Flip_Flop d_ff_23 (.D(in_1[2]), .clk(and_3_out), .Q(d_ff_31_q[2]));  // open: Qn, preset, reset
  D_Flip_Flop d_ff_24 (.D(in_1[2]), .clk(and_4_out), .Q(d_ff_32_q[2]));  // open: Qn, preset, reset
  D_Flip_Flop d_ff_25 (.D(in_1[1]), .clk(and_1_out), .Q(d_ff_29_q[1]));  // open: Qn, preset, reset
  D_Flip_Flop d_ff_26 (.D(in_1[1]), .clk(and_2_out), .Q(d_ff_30_q[1]));  // open: Qn, preset, reset
  D_Flip_Flop d_ff_27 (.D(in_1[1]), .clk(and_3_out), .Q(d_ff_31_q[1]));  // open: Qn, preset, reset
  D_Flip_Flop d_ff_28 (.D(in_1[1]), .clk(and_4_out), .Q(d_ff_32_q[1]));  // open: Qn, preset, reset
  D_Flip_Flop d_ff_29 (.D(in_1[0]), .clk(and_1_out), .Q(d_ff_29_q[0]));  // open: Qn, preset, reset
  D_Flip_Flop d_ff_30 (.D(in_1[0]), .clk(and_2_out), .Q(d_ff_30_q[0]));  // open: Qn, preset, reset
  D_Flip_Flop d_ff_31 (.D(in_1[0]), .clk(and_3_out), .Q(d_ff_31_q[0]));  // open: Qn, preset, reset
  D_Flip_Flop d_ff_32 (.D(in_1[0]), .clk(and_4_out), .Q(d_ff_32_q[0]));  // open: Qn, preset, reset
  // Binary_to_BCD_converter #(.binvalue(8)) binary_to_bcd_converter_1: pin names not known; wires that end beside it: d_ff_29_q, out_7[3:0], out_7[7:4], out_7[11:8]
  // Binary_to_BCD_converter #(.binvalue(8)) binary_to_bcd_converter_2: pin names not known; wires that end beside it: d_ff_30_q, out_8[3:0], out_8[7:4], out_8[11:8]
  // Binary_to_BCD_converter #(.binvalue(8)) binary_to_bcd_converter_3: pin names not known; wires that end beside it: d_ff_31_q, out_9[3:0], out_9[7:4], out_9[11:8]
  // Binary_to_BCD_converter #(.binvalue(8)) binary_to_bcd_converter_4: pin names not known; wires that end beside it: d_ff_32_q, out_10[3:0], out_10[7:4], out_10[11:8]
endmodule
